// Logisim project ALU.circ as structural Verilog
module ALU (
  input  F0,
  input  F1,
  input  F2,
  input  F3,
  input  ENA,
  input  [15:0] A_Bus,
  input  ENB,
  input  [15:0] B_Bus,
  input  INC,
  output [15:0] C_Bus,
  output CARRY,
  output OVR,
  output POS,
  output ZERO,
  output NEG
);

  wire alu_base_1_carry, alu_shifter_1_carry, n74521_1__19__no__a_b, n74521_2__19__no__a_b, not_1_out;
  wire [14:0] alu_base_1_c_bus;

  ALU_Base alu_base_1 (
    .ENA(ENA), .A_Bus(A_Bus), .F0(F0), .F1(F1), .F2(F2), .INC(INC), .C_Bus({NEG, alu_base_1_c_bus}),
    .B_Bus(B_Bus), .ENB(ENB), .CARRY(alu_base_1_carry), .OVR(OVR));
  _74245 u_74245_1 (
    ._1__DIR(not_1_out), ._2__A1(alu_base_1_c_bus[0]), ._3__A2(alu_base_1_c_bus[1]),
    ._4__A3(alu_base_1_c_bus[2]), ._5__A4(alu_base_1_c_bus[3]), ._6__A5(alu_base_1_c_bus[4]),
    ._7__A6(alu_base_1_c_bus[5]), ._8__A7(alu_base_1_c_bus[6]), ._9__A8(alu_base_1_c_bus[7]), ._19__nG(1'b0),
    ._18___B1(C_Bus[0]), ._17__B2(C_Bus[1]), ._16__B3(C_Bus[2]), ._15__B4(C_Bus[3]), ._14__B5(C_Bus[4]),
    ._13__B6(C_Bus[5]), ._12__B7(C_Bus[6]), ._11__B8(C_Bus[7]));  // open: _10__GND, _20__Vcc
  not not_1 (not_1_out, F3);
  ALU_Shifter alu_shifter_1 (
    .A_Bus(A_Bus), .CARRY(alu_shifter_1_carry), .C_Bus(C_Bus), .F0(F0), .F1(F1), .F2(F2), .F3(F3));
  _74245 u_74245_2 (
    ._1__DIR(not_1_out), ._2__A1(alu_base_1_c_bus[8]), ._3__A2(alu_base_1_c_bus[9]),
    ._4__A3(alu_base_1_c_bus[10]), ._5__A4(alu_base_1_c_bus[11]), ._6__A5(alu_base_1_c_bus[12]),
    ._7__A6(alu_base_1_c_bus[13]), ._8__A7(alu_base_1_c_bus[14]), ._9__A8(NEG), ._19__nG(1'b0),
    ._18___B1(C_Bus[8]), ._17__B2(C_Bus[9]), ._16__B3(C_Bus[10]), ._15__B4(C_Bus[11]), ._14__B5(C_Bus[12]),
    ._13__B6(C_Bus[13]), ._12__B7(C_Bus[14]), ._11__B8(C_Bus[15]));  // open: _10__GND, _20__Vcc
  or or_1 (CARRY, alu_shifter_1_carry, alu_base_1_carry);
  _74521 u_74521_1 (
    ._2__A0(alu_base_1_c_bus[0]), ._3__B0(1'b0), ._4__A1(alu_base_1_c_bus[1]), ._5__B1(1'b0),
    ._6__A2(alu_base_1_c_bus[2]), ._7__B2(1'b0), ._8__A3(alu_base_1_c_bus[3]), ._9__B3(1'b0),
    ._11__A4(alu_base_1_c_bus[12]), ._12__B4(1'b0), ._13__A5(alu_base_1_c_bus[13]), ._14__B5(1'b0),
    ._15__A6(alu_base_1_c_bus[14]), ._16__B6(1'b0), ._17__A7(NEG), ._18__B7(1'b0), ._1__nI__A_B(1'b0),
    ._19__nO__A_B(n74521_1__19__no__a_b));  // open: _20__Vcc, _10__GND
  _74521 u_74521_2 (
    ._2__A0(alu_base_1_c_bus[4]), ._3__B0(1'b0), ._4__A1(alu_base_1_c_bus[5]), ._5__B1(1'b0),
    ._6__A2(alu_base_1_c_bus[6]), ._7__B2(1'b0), ._8__A3(alu_base_1_c_bus[7]), ._9__B3(1'b0),
    ._11__A4(alu_base_1_c_bus[8]), ._12__B4(1'b0), ._13__A5(alu_base_1_c_bus[9]), ._14__B5(1'b0),
    ._15__A6(alu_base_1_c_bus[10]), ._16__B6(1'b0), ._17__A7(alu_base_1_c_bus[11]), ._18__B7(1'b0),
    ._1__nI__A_B(1'b0), ._19__nO__A_B(n74521_2__19__no__a_b));  // open: _20__Vcc, _10__GND
  nor nor_1 (ZERO, n74521_1__19__no__a_b, n74521_2__19__no__a_b);
  nor nor_2 (POS, ZERO, NEG);
  ALU_Functions alu_functions_1 ();

  // Notes on the sheet:
  //   ALU || (shifter)
  //   Test Zero
endmodule

// ALU
module ALU_Base (
  input  ENA,
  input  ENB,
  input  [15:0] A_Bus,
  input  [15:0] B_Bus,
  input  F0,
  input  F1,
  input  F2,
  input  INC,
  output CARRY,
  output OVR,
  output [15:0] C_Bus
);

  wire n74182_1_cn_x, n74182_1_cn_y, n74182_1_cn_z, n74245_1__11__b8, n74245_1__12__b7, n74245_1__13__b6,
       n74245_1__14__b5, n74245_1__15__b4, n74245_1__16__b3, n74245_1__17__b2, n74245_1__18___b1,
       n74245_2__11__b8, n74245_2__12__b7, n74245_2__13__b6, n74245_2__14__b5, n74245_2__15__b4,
       n74245_2__16__b3, n74245_2__17__b2, n74245_2__18___b1, n74245_3__11__b8, n74245_3__12__b7,
       n74245_3__13__b6, n74245_3__14__b5, n74245_3__15__b4, n74245_3__16__b3, n74245_3__17__b2,
       n74245_3__18___b1, n74245_4__11__b8, n74245_4__12__b7, n74245_4__13__b6, n74245_4__14__b5,
       n74245_4__15__b4, n74245_4__16__b3, n74245_4__17__b2, n74245_4__18___b1, n74381_1_ng, n74381_1_np,
       n74381_2_ng, n74381_2_np, n74381_3_ng, n74381_3_np, not_1_out, not_2_out;

  not not_1 (not_1_out, ENA);
  not not_2 (not_2_out, ENB);
  _74245 u_74245_1 (
    ._1__DIR(1'b1), ._2__A1(A_Bus[0]), ._3__A2(A_Bus[1]), ._4__A3(A_Bus[2]), ._5__A4(A_Bus[3]),
    ._6__A5(A_Bus[4]), ._7__A6(A_Bus[5]), ._8__A7(A_Bus[6]), ._9__A8(A_Bus[7]), ._19__nG(not_1_out),
    ._18___B1(n74245_1__18___b1), ._17__B2(n74245_1__17__b2), ._16__B3(n74245_1__16__b3),
    ._15__B4(n74245_1__15__b4), ._14__B5(n74245_1__14__b5), ._13__B6(n74245_1__13__b6),
    ._12__B7(n74245_1__12__b7), ._11__B8(n74245_1__11__b8));  // open: _10__GND, _20__Vcc
  _74381 u_74381_1 (
    .Cin(INC), .B0(n74245_2__18___b1), .A0(n74245_1__18___b1), .B1(n74245_2__17__b2), .A1(n74245_1__17__b2),
    .B2(n74245_2__16__b3), .A2(n74245_1__16__b3), .B3(n74245_2__15__b4), .A3(n74245_1__15__b4), .F0(F0),
    .F1(F1), .F2(F2), .C0(C_Bus[0]), .C1(C_Bus[1]), .C2(C_Bus[2]), .C3(C_Bus[3]), .nP(n74381_1_np),
    .nG(n74381_1_ng));  // open: Vcc, GND
  _74245 u_74245_2 (
    ._1__DIR(1'b1), ._2__A1(B_Bus[0]), ._3__A2(B_Bus[1]), ._4__A3(B_Bus[2]), ._5__A4(B_Bus[3]),
    ._6__A5(B_Bus[4]), ._7__A6(B_Bus[5]), ._8__A7(B_Bus[6]), ._9__A8(B_Bus[7]), ._19__nG(not_2_out),
    ._18___B1(n74245_2__18___b1), ._17__B2(n74245_2__17__b2), ._16__B3(n74245_2__16__b3),
    ._15__B4(n74245_2__15__b4), ._14__B5(n74245_2__14__b5), ._13__B6(n74245_2__13__b6),
    ._12__B7(n74245_2__12__b7), ._11__B8(n74245_2__11__b8));  // open: _10__GND, _20__Vcc
  _74381 u_74381_2 (
    .Cin(n74182_1_cn_x), .B0(n74245_2__14__b5), .A0(n74245_1__14__b5), .B1(n74245_2__13__b6),
    .A1(n74245_1__13__b6), .B2(n74245_2__12__b7), .A2(n74245_1__12__b7), .B3(n74245_2__11__b8),
    .A3(n74245_1__11__b8), .F0(F0), .F1(F1), .F2(F2), .C0(C_Bus[4]), .C1(C_Bus[5]), .C2(C_Bus[6]),
    .C3(C_Bus[7]), .nP(n74381_2_np), .nG(n74381_2_ng));  // open: Vcc, GND
  _74182 u_74182_1 (
    .Cn_x(n74182_1_cn_x), .Cn_y(n74182_1_cn_y), .Cn_z(n74182_1_cn_z), .G0(n74381_1_ng), .P0(n74381_1_np),
    .Cn(INC), .G1(n74381_2_ng), .P1(n74381_2_np), .G2(n74381_3_ng), .P2(n74381_3_np));  // open: G, P, G3, P3, Vcc, GND
  _74245 u_74245_3 (
    ._1__DIR(1'b1), ._2__A1(A_Bus[8]), ._3__A2(A_Bus[9]), ._4__A3(A_Bus[10]), ._5__A4(A_Bus[11]),
    ._6__A5(A_Bus[12]), ._7__A6(A_Bus[13]), ._8__A7(A_Bus[14]), ._9__A8(A_Bus[15]), ._19__nG(not_1_out),
    ._18___B1(n74245_3__18___b1), ._17__B2(n74245_3__17__b2), ._16__B3(n74245_3__16__b3),
    ._15__B4(n74245_3__15__b4), ._14__B5(n74245_3__14__b5), ._13__B6(n74245_3__13__b6),
    ._12__B7(n74245_3__12__b7), ._11__B8(n74245_3__11__b8));  // open: _10__GND, _20__Vcc
  _74381 u_74381_3 (
    .Cin(n74182_1_cn_y), .B0(n74245_4__18___b1), .A0(n74245_3__18___b1), .B1(n74245_4__17__b2),
    .A1(n74245_3__17__b2), .B2(n74245_4__16__b3), .A2(n74245_3__16__b3), .B3(n74245_4__15__b4),
    .A3(n74245_3__15__b4), .F0(F0), .F1(F1), .F2(F2), .C0(C_Bus[8]), .C1(C_Bus[9]), .C2(C_Bus[10]),
    .C3(C_Bus[11]), .nP(n74381_3_np), .nG(n74381_3_ng));  // open: Vcc, GND
  _74245 u_74245_4 (
    ._1__DIR(1'b1), ._2__A1(B_Bus[8]), ._3__A2(B_Bus[9]), ._4__A3(B_Bus[10]), ._5__A4(B_Bus[11]),
    ._6__A5(B_Bus[12]), ._7__A6(B_Bus[13]), ._8__A7(B_Bus[14]), ._9__A8(B_Bus[15]), ._19__nG(not_2_out),
    ._18___B1(n74245_4__18___b1), ._17__B2(n74245_4__17__b2), ._16__B3(n74245_4__16__b3),
    ._15__B4(n74245_4__15__b4), ._14__B5(n74245_4__14__b5), ._13__B6(n74245_4__13__b6),
    ._12__B7(n74245_4__12__b7), ._11__B8(n74245_4__11__b8));  // open: _10__GND, _20__Vcc
  _74382 u_74382_1 (
    .Cin(n74182_1_cn_z), .A0(n74245_3__14__b5), .B0(n74245_4__14__b5), .A1(n74245_3__13__b6),
    .B1(n74245_4__13__b6), .A2(n74245_3__12__b7), .B2(n74245_4__12__b7), .A3(n74245_3__11__b8),
    .B3(n74245_4__11__b8), .F0(F0), .F1(F1), .F2(F2), .Cout(CARRY), .OVR(OVR), .C2(C_Bus[14]),
    .C3(C_Bus[15]), .C0(C_Bus[12]), .C1(C_Bus[13]));  // open: Vcc, GND
endmodule

// Shifter
module ALU_Shifter (
  input  F0,
  input  F1,
  input  F2,
  input  F3,
  input  [15:0] A_Bus,
  output CARRY,
  output [15:0] C_Bus
);

  wire and_1_out, and_2_out, and_3_out, and_4_out, and_5_out, or_1_out;

  _74245 u_74245_1 (
    ._1__DIR(F3), ._2__A1(A_Bus[7]), ._3__A2(A_Bus[8]), ._4__A3(A_Bus[9]), ._5__A4(A_Bus[10]),
    ._6__A5(A_Bus[11]), ._7__A6(A_Bus[12]), ._8__A7(A_Bus[13]), ._9__A8(A_Bus[14]), ._19__nG(and_3_out),
    ._18___B1(C_Bus[8]), ._17__B2(C_Bus[9]), ._16__B3(C_Bus[10]), ._15__B4(C_Bus[11]), ._14__B5(C_Bus[12]),
    ._13__B6(C_Bus[13]), ._12__B7(C_Bus[14]), ._11__B8(C_Bus[15]));  // open: _10__GND, _20__Vcc
  _74245 u_74245_2 (
    ._1__DIR(F3), ._2__A1(1'b0), ._3__A2(A_Bus[0]), ._4__A3(A_Bus[1]), ._5__A4(A_Bus[2]), ._6__A5(A_Bus[3]),
    ._7__A6(A_Bus[4]), ._8__A7(A_Bus[5]), ._9__A8(A_Bus[6]), ._19__nG(and_3_out), ._18___B1(C_Bus[0]),
    ._17__B2(C_Bus[1]), ._16__B3(C_Bus[2]), ._15__B4(C_Bus[3]), ._14__B5(C_Bus[4]), ._13__B6(C_Bus[5]),
    ._12__B7(C_Bus[6]), ._11__B8(C_Bus[7]));  // open: _10__GND, _20__Vcc
  and and_1 (and_1_out, F2, A_Bus[15]);
  _74245 u_74245_3 (
    ._1__DIR(F3), ._2__A1(A_Bus[9]), ._3__A2(A_Bus[10]), ._4__A3(A_Bus[11]), ._5__A4(A_Bus[12]),
    ._6__A5(A_Bus[13]), ._7__A6(A_Bus[14]), ._8__A7(A_Bus[15]), ._9__A8(and_1_out), ._19__nG(and_4_out),
    ._18___B1(C_Bus[8]), ._17__B2(C_Bus[9]), ._16__B3(C_Bus[10]), ._15__B4(C_Bus[11]), ._14__B5(C_Bus[12]),
    ._13__B6(C_Bus[13]), ._12__B7(C_Bus[14]), ._11__B8(C_Bus[15]));  // open: _10__GND, _20__Vcc
  and and_2 (and_2_out, A_Bus[0], F0);
  _74245 u_74245_4 (
    ._1__DIR(F3), ._2__A1(A_Bus[1]), ._3__A2(A_Bus[2]), ._4__A3(A_Bus[3]), ._5__A4(A_Bus[4]),
    ._6__A5(A_Bus[5]), ._7__A6(A_Bus[6]), ._8__A7(A_Bus[7]), ._9__A8(A_Bus[8]), ._19__nG(and_4_out),
    ._18___B1(C_Bus[0]), ._17__B2(C_Bus[1]), ._16__B3(C_Bus[2]), ._15__B4(C_Bus[3]), ._14__B5(C_Bus[4]),
    ._13__B6(C_Bus[5]), ._12__B7(C_Bus[6]), ._11__B8(C_Bus[7]));  // open: _10__GND, _20__Vcc
  and and_3 (and_3_out, F0, F3);
  and and_4 (and_4_out, F3, F1);
  and and_5 (and_5_out, F1, A_Bus[15]);
  or or_1 (or_1_out, and_2_out, and_5_out);
  and and_6 (CARRY, or_1_out, F3);

  // Notes on the sheet:
  //   Shift Left
  //   Shift Right
endmodule

module Test (
  input  [7:0] in_1,
  input  in_2,
  output [7:0] out_3
);

  wire not_1_out;

  _74245 u_74245_1 (
    ._1__DIR(1'b1), ._2__A1(1'b0), ._3__A2(in_1[0]), ._4__A3(in_1[1]), ._5__A4(in_1[2]), ._6__A5(in_1[3]),
    ._7__A6(in_1[4]), ._8__A7(in_1[5]), ._9__A8(in_1[6]), ._19__nG(not_1_out), ._18___B1(out_3[0]),
    ._17__B2(out_3[1]), ._16__B3(out_3[2]), ._15__B4(out_3[3]), ._14__B5(out_3[4]), ._13__B6(out_3[5]),
    ._12__B7(out_3[6]), ._11__B8(out_3[7]));  // open: _10__GND, _20__Vcc
  _74245 u_74245_2 (
    ._1__DIR(1'b1), ._2__A1(in_1[1]), ._3__A2(in_1[2]), ._4__A3(in_1[3]), ._5__A4(in_1[4]), ._6__A5(in_1[5]),
    ._7__A6(in_1[6]), ._8__A7(in_1[7]), ._9__A8(1'b0), ._19__nG(in_2), ._18___B1(out_3[0]),
    ._17__B2(out_3[1]), ._16__B3(out_3[2]), ._15__B4(out_3[3]), ._14__B5(out_3[4]), ._13__B6(out_3[5]),
    ._12__B7(out_3[6]), ._11__B8(out_3[7]));  // open: _10__GND, _20__Vcc
  not not_1 (not_1_out, in_2);
endmodule
