// Logisim project CPU.circ as structural Verilog: 1 circuit, main circuit main
module main (
  input  [7:0] in_1,
  input  R_0____W_1,
  input  B_Bus_Select_0,
  input  B_Bus_Select_1,
  output [15:0] A_Bus_Probe,
  output [15:0] B_Bus_Probe,
  output [15:0] C_Bus_Probe
);

  wire alu_1_carry, alu_1_neg, alu_1_ovr, alu_1_pos, alu_1_zero, CLK_out, Reset_out;
  wire [7:0] rom_1_data, rom_2_data, rom_3_data, transistor_1_out;

  ALU alu_1 (
    .A_Bus(A_Bus_Probe), .B_Bus(B_Bus_Probe), .C_Bus(C_Bus_Probe), .CARRY(alu_1_carry), .ZERO(alu_1_zero),
    .NEG(alu_1_neg), .POS(alu_1_pos), .OVR(alu_1_ovr));  // open: ENA, ENB, INC, F0, F1, F2, F3
  Clock CLK (.out(CLK_out));
  Button Reset (.out(Reset_out));
  // RAM ram_1: pin names not known
  Transistor #(.\type ("n"), .width(8)) transistor_1 (.in(in_1), .out(transistor_1_out), .gate(Reset_out));
  // Register16 IR: pin names not known
  // Registers registers_1: pin names not known
  ROM rom_1 (.addr(transistor_1_out), .data(rom_1_data));  // open: sel
  ROM rom_2 (.addr(transistor_1_out), .data(rom_2_data));  // open: sel
  ROM rom_3 (.addr(transistor_1_out), .data(rom_3_data));  // open: sel
  ROM rom_4 (.addr(transistor_1_out), .data(transistor_1_out));  // open: sel

  // Notes on the sheet:
  //   contents of rom_1 (hex, n*v repeats v):
  //   1 23 45 67 89 ab cd ef
  //   contents of rom_2 (hex, n*v repeats v):
  //   1 23 45 67 89 ab cd ef 248*11
  //   contents of rom_3 (hex, n*v repeats v):
  //   12 23 34 45
endmodule
