// Logisim project Console.circ as structural Verilog
module Console (
);

  wire n74240_1__3__2y4, n74240_1__5__2y3, n74240_1__7__2y2, n74240_1__9__2y1, n74240_1__12__1y4,
       n74240_1__14__1y3, n74240_1__16__1y2, n74240_1__18__1y1, n74240_2__3__2y4, n74240_2__5__2y3,
       n74240_2__7__2y2, n74240_2__9__2y1, n74240_2__12__1y4, n74240_2__14__1y3, n74240_2__16__1y2,
       n74240_2__18__1y1, n74240_3__3__2y4, n74240_3__5__2y3, n74240_3__7__2y2, n74240_3__9__2y1,
       n74240_3__12__1y4, n74240_3__14__1y3, n74240_3__16__1y2, n74240_3__18__1y1, n74240_4__3__2y4,
       n74240_4__5__2y3, n74240_4__7__2y2, n74240_4__9__2y1, n74240_4__12__1y4, n74240_4__14__1y3,
       n74240_4__16__1y2, n74240_4__18__1y1, n74240_5__3__2y4, n74240_5__5__2y3, n74240_5__7__2y2,
       n74240_5__9__2y1, n74240_5__12__1y4, n74240_5__14__1y3, n74240_5__16__1y2, n74240_5__18__1y1,
       n74240_6__3__2y4, n74240_6__5__2y3, n74240_6__7__2y2, n74240_6__9__2y1, n74240_6__12__1y4,
       n74240_6__14__1y3, n74240_6__16__1y2, n74240_6__18__1y1;
  wire [3:0] undriven, undriven_2, undriven_3, undriven_4, undriven_5, undriven_6, undriven_7, undriven_8,
       undriven_10;
  wire [15:0] undriven_9;

  LED led_1 (.in(n74240_1__9__2y1));
  LED led_2 (.in(n74240_1__18__1y1));
  LED led_3 (.in(n74240_1__5__2y3));
  LED led_4 (.in(n74240_1__3__2y4));
  LED led_5 (.in(n74240_1__7__2y2));
  _74240 u_74240_1 (
    ._2__1A1(undriven_2[0]), ._4__1A2(undriven_2[1]), ._6__1A3(undriven_2[2]), ._8__1A4(undriven_2[3]),
    ._13__2A2(undriven[3]), ._15__2A3(undriven[2]), ._17__2A4(undriven[1]), ._19__n2G(undriven[0]),
    ._18__1Y1(n74240_1__18__1y1), ._16__1Y2(n74240_1__16__1y2), ._14__1Y3(n74240_1__14__1y3),
    ._12__1Y4(n74240_1__12__1y4), ._9__2Y1(n74240_1__9__2y1), ._7__2Y2(n74240_1__7__2y2),
    ._5__2Y3(n74240_1__5__2y3), ._3__2Y4(n74240_1__3__2y4));  // open: _1__n1G, _11__2A1, _10__GND, _20__Vcc
  LED led_6 (.in(n74240_1__14__1y3));
  LED led_7 (.in(n74240_1__16__1y2));
  LED led_8 (.in(n74240_1__12__1y4));
  LED led_9 (.in(n74240_2__9__2y1));
  LED led_10 (.in(n74240_2__5__2y3));
  LED led_11 (.in(n74240_2__7__2y2));
  LED led_12 (.in(n74240_2__3__2y4));
  LED led_13 (.in(n74240_2__18__1y1));
  _74240 u_74240_2 (
    ._2__1A1(undriven_4[0]), ._4__1A2(undriven_4[1]), ._6__1A3(undriven_4[2]), ._8__1A4(undriven_4[3]),
    ._13__2A2(undriven_3[3]), ._15__2A3(undriven_3[2]), ._17__2A4(undriven_3[1]), ._19__n2G(undriven_3[0]),
    ._18__1Y1(n74240_2__18__1y1), ._16__1Y2(n74240_2__16__1y2), ._14__1Y3(n74240_2__14__1y3),
    ._12__1Y4(n74240_2__12__1y4), ._9__2Y1(n74240_2__9__2y1), ._7__2Y2(n74240_2__7__2y2),
    ._5__2Y3(n74240_2__5__2y3), ._3__2Y4(n74240_2__3__2y4));  // open: _1__n1G, _11__2A1, _10__GND, _20__Vcc
  LED led_14 (.in(n74240_3__5__2y3));
  LED led_15 (.in(n74240_3__7__2y2));
  LED led_16 (.in(n74240_3__9__2y1));
  LED led_17 (.in(n74240_2__16__1y2));
  LED led_18 (.in(n74240_2__12__1y4));
  LED led_19 (.in(n74240_2__14__1y3));
  LED led_20 (.in(n74240_3__18__1y1));
  LED led_21 (.in(n74240_3__16__1y2));
  LED led_22 (.in(n74240_3__3__2y4));
  _74240 u_74240_3 (
    ._2__1A1(undriven_6[0]), ._4__1A2(undriven_6[1]), ._6__1A3(undriven_6[2]), ._8__1A4(undriven_6[3]),
    ._13__2A2(undriven_5[3]), ._15__2A3(undriven_5[2]), ._17__2A4(undriven_5[1]), ._19__n2G(undriven_5[0]),
    ._18__1Y1(n74240_3__18__1y1), ._16__1Y2(n74240_3__16__1y2), ._14__1Y3(n74240_3__14__1y3),
    ._12__1Y4(n74240_3__12__1y4), ._9__2Y1(n74240_3__9__2y1), ._7__2Y2(n74240_3__7__2y2),
    ._5__2Y3(n74240_3__5__2y3), ._3__2Y4(n74240_3__3__2y4));  // open: _1__n1G, _11__2A1, _10__GND, _20__Vcc
  LED led_23 (.in(n74240_3__12__1y4));
  LED led_24 (.in(n74240_3__14__1y3));
  LED led_25 (.in(n74240_4__7__2y2));
  LED led_26 (.in(n74240_4__9__2y1));
  LED led_27 (.in(n74240_5__5__2y3));
  LED led_28 (.in(n74240_5__7__2y2));
  LED led_29 (.in(n74240_5__9__2y1));
  LED led_30 (.in(n74240_4__16__1y2));
  LED led_31 (.in(n74240_4__3__2y4));
  LED led_32 (.in(n74240_4__18__1y1));
  LED led_33 (.in(n74240_4__5__2y3));
  _74240 u_74240_4 (
    ._2__1A1(undriven_9[4]), ._4__1A2(undriven_9[5]), ._6__1A3(undriven_9[6]), ._8__1A4(undriven_9[7]),
    ._13__2A2(undriven_9[3]), ._15__2A3(undriven_9[2]), ._17__2A4(undriven_9[1]), ._19__n2G(undriven_9[0]),
    ._18__1Y1(n74240_4__18__1y1), ._16__1Y2(n74240_4__16__1y2), ._14__1Y3(n74240_4__14__1y3),
    ._12__1Y4(n74240_4__12__1y4), ._9__2Y1(n74240_4__9__2y1), ._7__2Y2(n74240_4__7__2y2),
    ._5__2Y3(n74240_4__5__2y3), ._3__2Y4(n74240_4__3__2y4));  // open: _1__n1G, _11__2A1, _10__GND, _20__Vcc
  LED led_34 (.in(n74240_5__18__1y1));
  LED led_35 (.in(n74240_5__3__2y4));
  LED led_36 (.in(n74240_5__16__1y2));
  _74240 u_74240_5 (
    ._2__1A1(undriven_8[0]), ._4__1A2(undriven_8[1]), ._6__1A3(undriven_8[2]), ._8__1A4(undriven_8[3]),
    ._13__2A2(undriven_7[3]), ._15__2A3(undriven_7[2]), ._17__2A4(undriven_7[1]), ._19__n2G(undriven_7[0]),
    ._18__1Y1(n74240_5__18__1y1), ._16__1Y2(n74240_5__16__1y2), ._14__1Y3(n74240_5__14__1y3),
    ._12__1Y4(n74240_5__12__1y4), ._9__2Y1(n74240_5__9__2y1), ._7__2Y2(n74240_5__7__2y2),
    ._5__2Y3(n74240_5__5__2y3), ._3__2Y4(n74240_5__3__2y4));  // open: _1__n1G, _11__2A1, _10__GND, _20__Vcc
  LED led_37 (.in(n74240_4__14__1y3));
  LED led_38 (.in(n74240_4__12__1y4));
  LED led_39 (.in(n74240_5__14__1y3));
  LED led_40 (.in(n74240_5__12__1y4));
  LED led_41 (.in(n74240_6__7__2y2));
  LED led_42 (.in(n74240_6__9__2y1));
  LED led_43 (.in(n74240_6__5__2y3));
  LED led_44 (.in(n74240_6__16__1y2));
  LED led_45 (.in(n74240_6__3__2y4));
  LED led_46 (.in(n74240_6__18__1y1));
  _74240 u_74240_6 (
    ._2__1A1(undriven_9[12]), ._4__1A2(undriven_9[13]), ._6__1A3(undriven_9[14]), ._8__1A4(undriven_9[15]),
    ._13__2A2(undriven_10[3]), ._15__2A3(undriven_10[2]), ._17__2A4(undriven_10[1]),
    ._19__n2G(undriven_10[0]), ._18__1Y1(n74240_6__18__1y1), ._16__1Y2(n74240_6__16__1y2),
    ._14__1Y3(n74240_6__14__1y3), ._12__1Y4(n74240_6__12__1y4), ._9__2Y1(n74240_6__9__2y1),
    ._7__2Y2(n74240_6__7__2y2), ._5__2Y3(n74240_6__5__2y3), ._3__2Y4(n74240_6__3__2y4));  // open: _1__n1G, _11__2A1, _10__GND, _20__Vcc
  LED led_47 (.in(n74240_6__14__1y3));
  LED led_48 (.in(n74240_6__12__1y4));
endmodule
