// Logisim project 7400-lib.circ as structural Verilog: 62 circuits, main circuit main
module main (
);

  _7414 u_7414_1 ();  // open: _1A_1, _2A_3, _3A_5, _4A_9, _5A_11, _6A_13, Vcc_14, Gnd_7, _1Y_2, _2Y_4, _3Y_6, _4Y_8, _5Y_10, _6Y_12
  _74382 u_74382_1 ();  // open: Cin, A0, B0, A1, B1, A2, B2, A3, B3, F0, F1, F2, Vcc, GND, Cout, OVR, C2, C3, C0, C1
  _7400 u_7400_1 ();  // open: _1__1A, _2__1B, _3__1Y, _4__2A, _5__2B, _6__2Y, _7__GND, _14__Vcc, _13__4B, _12__4A, _11__4Y, _10__3B, _9__3A, _8__3Y
  // _74xx28 74xx28_1: pin names not known
  _7451 u_7451_1 ();  // open: _1__1A, _2__2A, _3__2B, _4__2C, _5__2D, _6__2Y, _7__GND, _14__Vcc, _13__1B, _12__NC, _11__NC, _10__1D, _9__1C, _8__1Y
  _74116 u_74116_1 ();  // open: _1__nMRa, _2__nE0a, _3__nE1a, _4__D0a, _5__Q0a, _6__D1a, _7__Q1a, _8__D2a, _9__Q2a, _10__D3a, _11__Q3a, _12__GND, _24__Vcc, _23__Q3b, _22__D3b, _21__Q2b, _20__D2b, _19__Q1b, _18__D1b, _17__Q0b, _16__D0b, _15__nE1b, _14__nE0b, _13__nMRb
  _74153 u_74153_1 ();  // open: _1__nG1, _2__B, _3__1C3, _4__1C2, _5__1C1, _6__1C0, _7__Y1, _8__GND, _16__Vcc, _15__nG2, _14__A, _13__2C3, _12__2C2, _11__2C1, _10__2C0, _9__Y2
  _74174 u_74174_1 ();  // open: _1__MR_prime, _2__Q0, _3__D0, _4__D1, _5__Q1, _6__D2, _7__Q2, _8__GND, _16__Vcc, _15__Q5, _14__D5, _13__D4, _12__Q4, _11__D3, _10__Q3, _9__CP
  _74244 u_74244_1 ();  // open: _1__E1, _2__1A0, _4__1A1, _6__1A2, _8__1A3, _19__E2, _17__2A0, _15__2A1, _13__2A2, _11__2A3, _10__GND, _20__Vcc, _18__1Y0, _16__1Y1, _14__1Y2, _12__1Y3, _3__2Y0, _5__2Y1, _7__2Y2, _9__2Y3
  _744075 u_744075_1 ();  // open: _1__1A, _2__1B, _3__2A, _4__2B, _5__2C, _6__2Y, _7__GND, _14__Vcc, _13__1C, _12__1Y, _11__3C, _10__3B, _9__3A, _8__3Y
  _7418 u_7418_1 ();  // open: _1A_1, _1B_2, _1C_4, _1D_5, _2A_9, _2B_10, _2C_12, _2D_13, Vcc_14, Gnd_7, _1Y_6, _2Y_8
  // _74xx55 74xx55_1: pin names not known
  // _74181 74181_1: pin names not known
  // _74385 74385_1: pin names not known
  _7402 u_7402_1 ();  // open: _1__1Y, _2__1A, _3__1B, _4__2Y, _5__2A, _6__2B, _7__GND, _14__Vcc, _13__4Y, _12__4B, _11__4A, _10__3Y, _9__3B, _8__3A
  _7430 u_7430_1 ();  // open: _1__1A, _2__1B, _3__1C, _4__1D, _5__1E, _6__1F, _7__GND, _14__Vcc, _13__NC, _12__1H, _11__1G, _10__NC, _9__NC, _8__3Y
  _74133 u_74133_1 ();  // open: _1__A, _2__B, _3__C, _4__D, _5__E, _6__F, _7__G, _8__GND, _16__Vcc, _15__M, _14__L, _13__K, _12__J, _11__I, _10__H, _9__Y
  _74154 u_74154_1 ();  // open: _1__Y0, _2__Y1, _3__Y2, _4__Y3, _5__Y4, _6__Y5, _7__Y6, _8__Y7, _9__Y8, _10__Y9, _11__Y10, _12__GND, _24__Vcc, _23__A, _22__B, _21__C, _20__D, _19__G2, _18__G1, _17__Y15, _16__Y14, _15__Y13, _14__Y12, _13__Y11
  _74245 u_74245_1 ();  // open: _1__DIR, _2__A1, _3__A2, _4__A3, _5__A4, _6__A5, _7__A6, _8__A7, _9__A8, _10__GND, _20__Vcc, _19__nG, _18___B1, _17__B2, _16__B3, _15__B4, _14__B5, _13__B6, _12__B7, _11__B8
  _74125 u_74125_1 ();  // open: B0__2, A0__1, B1__5, A1__4, B2__12, A2__13, B3__9, A3__10, Vcc__14, O0__3, O1__6, O2__11, O3__8, GND__7
  _7404 u_7404_1 ();  // open: _1__1A, _2__1Y, _3__2A, _4__2Y, _5__3A, _6__3Y, _7__GND, _14__Vcc, _13__6A, _12__6Y, _11__5A, _10__5Y, _9__4A, _8__4Y
  _7432 u_7432_1 ();  // open: _1__1A, _2__1B, _3__1Y, _4__2A, _5__2B, _6__2Y, _7__GND, _14__Vcc, _13__4B, _12__4A, _11__4Y, _10__3B, _9__3A, _8__3Y
  _7474 u_7474_1 ();  // open: _1__CLR1, _2__D1, _3__CLK1, _4__PR1, _5__Q1, _6__nQ1, _7__GND, _14__Vcc, _13__CLR2, _12__D2, _11__CLK2, _10__PR2, _9__Q2, _8__nQ2
  _74182 u_74182_1 ();  // open: Cn_x, Cn_y, Cn_z, G, P, G0, P0, Cn, G1, P1, G2, P2, G3, P3, Vcc, GND
  _74521 u_74521_1 ();  // open: _2__A0, _3__B0, _4__A1, _5__B1, _6__A2, _7__B2, _8__A3, _9__B3, _11__A4, _12__B4, _13__A5, _14__B5, _15__A6, _16__B6, _17__A7, _18__B7, _1__nI__A_B, _19__nO__A_B, _20__Vcc, _10__GND
  // _74xx19 74xx19_1: pin names not known
  _74138 u_74138_1 ();  // open: _1__A, _2__B, _3__C, _4__G2A, _5__G2B, _6__G1, _7__Y7, _8__GND, _16__Vcc, _15__Y0, _14__Y1, _13__Y2, _12__Y3, _11__Y4, _10__Y5, _9__Y6
  _74157 u_74157_1 ();  // open: _1__S, _2__A1, _3__B1, _4__Y1, _5__A2, _6__B2, _7__Y2, _8__GND, _16__Vcc, _15__G, _14__A4, _13__B4, _12__Y4, _11__A3, _10__B3, _9__Y3
  _74253 u_74253_1 ();  // open: _1__1G, _2__Sb, _3__1C3, _4__1C2, _5__1C1, _6__1C0, _7__1Y, _8__GND, _16__Vcc, _15__2G, _14__Sa, _13__2C3, _12__2C2, _11__2C1, _10__2C0, _9__2Y
  _74381 u_74381_1 ();  // open: Cin, B0, A0, B1, A1, B2, A2, B3, Vcc, GND, A3, F0, F1, F2, C0, C1, C2, C3, nP, nG
  _7407 u_7407_1 ();  // open: _1__1A, _2__1Y, _3__2A, _4__2Y, _5__3A, _6__3Y, _7__GND, _14__Vcc, _13__6A, _12__6Y, _11__5A, _10__5Y, _9__4A, _8__4Y
  _7420 u_7420_1 ();  // open: _1__1A, _2__1B, _3__NC, _4__1C, _5__1D, _6__1Y, _7__GND, _14__Vcc, _13__2D, _12__2C, _11__NC, _10__2B, _9__2A, _8__2Y
  // _74xx37 74xx37_1: pin names not known
  _7476 u_7476_1 ();  // open: _1__CLK1, _2__PR1, _3__CLR1, _4__J1, _5__VCC, _6__CLK2, _7__PR2, _8__CLR2, _16__K1, _15__Q1, _14__nQ1, _13__GND, _12__K2, _11__Q2, _10__nQ2, _9__J2
  _74139 u_74139_1 ();  // open: _1__1G, _2__1A, _3__1B, _4__1Y0, _5__1Y1, _6__1Y2, _7__1Y3, _8__GND, _16__Vcc, _15__2G, _14__2A, _13__2B, _12__2Y0, _11__2Y1, _10__2Y2, _9__2Y3
  // _74160 74160_1: pin names not known
  // _74193 74193_1: pin names not known
  _74260 u_74260_1 ();  // open: _1__1A, _2__1B, _3__1E, _4__1C, _5__1D, _6__1Y, _7__GND, _14__Vcc, _13__2D, _12__2C, _11__2E, _10__2B, _9__2A, _8__2Y
  _74540 u_74540_1 ();  // open: _1__E1, _2__A1, _3__A2, _4__A3, _5__A4, _6__A5, _7__A6, _8__A7, _9__A8, _10__GND, _20__Vcc, _19__E2, _18___B1, _17__B2, _16__B3, _15__B4, _14__B5, _13__B6, _12__B7, _11__B8
  _74574 u_74574_1 ();  // open: D0__2, D1__3, D2__4, D3__5, D4__6, D5__7, D6__8, D7__9, nOE__1, CLK__11, GND__10, Vcc__20, Q0__19, Q1__18, Q2__17, Q3__16, Q4__15, Q5__14, Q6__13, Q7__12
  _7408 u_7408_1 ();  // open: _1__1A, _2__1B, _3__1Y, _4__2A, _5__2B, _6__2Y, _7__GND, _14__Vcc, _13__4B, _12__4A, _11__4Y, _10__3B, _9__3A, _8__3Y
  _7421 u_7421_1 ();  // open: _1__1A, _2__1B, _3__NC, _4__1C, _5__1D, _6__1Y, _7__GND, _14__Vcc, _13__2D, _12__2C, _11__NC, _10__2B, _9__2A, _8__2Y
  // _74xx40 74xx40_1: pin names not known
  _7483 u_7483_1 ();  // open: _1__A4, _2__S3, _3__A3, _4__B3, _5__Vcc, _6__S2, _7__B2, _8__A2, _16__B4, _15__S4, _14__Cout, _13__Cin, _12__GND, _11__B1, _10__A1, _9__S1
  _74147 u_74147_1 ();  // open: _1__I4, _2__I5, _3__I6, _4__I7, _5__I8, _6__A2, _7__A1, _8__GND, _16__Vcc, _15__NC, _14__A3, _13__I3, _12__I2, _11__I1, _10__I9, _9__A0
  _74161 u_74161_1 ();  // open: _1__nMR, _2__CP, _3__D0, _4__D1, _5__D2, _6__D3, _7__CEP, _8__GND, _16__Vcc, _15__TC, _14__Q0, _13__Q1, _12__Q2, _11__O3, _10__CET, _9__nPE
  _74194 u_74194_1 ();  // open: _1__nMR, _2__Dsr, _3__D0, _4__D1, _5__D2, _6__D3, _7__Dsl, _8__GND, _16__Vcc, _154__Q0, _14__Q1, _13__Q2, _12__Q3, _11__CP, _10__S1, _9__S0
  _74273 u_74273_1 ();  // open: D0_3, D1_4, D2_7, D3_8, D4_13, D5_14, D6_17, D7_18, nMR_1, CLK_11, Vcc_20, GND_10, Q0_2, Q1_5, Q2_6, Q3_9, Q4_12, Q5_15, Q6_16, Q7_19
  _74541 u_74541_1 ();  // open: _1__E1, _2__A1, _3__A2, _4__A3, _5__A4, _6__A5, _7__A6, _8__A7, _9__A8, _10__GND, _20__Vcc, _19__E2, _18___B1, _17__B2, _16__B3, _15__B4, _14__B5, _13__B6, _12__B7, _11__B8
  _7410 u_7410_1 ();  // open: _1__1A, _2__1B, _3__2A, _4__2B, _5__2C, _6__2Y, _7__GND, _14__Vcc, _13__1C, _12__1Y, _11__3C, _10__3B, _9__3A, _8__3Y
  // _74xx24 74xx24_1: pin names not known
  _7486 u_7486_1 ();  // open: _1__1A, _2__1B, _3__1Y, _4__2A, _5__2B, _6__2Y, _7__GND, _14__Vcc, _13__4B, _12__4A, _11__4Y, _10__3B, _9__3A, _8__3Y
  _74148 u_74148_1 ();  // open: _1__I4, _2__I5, _3__I6, _4__I7, _5__nEI__NC, _6__A2, _7__A1, _8__GND, _16__Vcc, _15__nEO__NC, _14__nGS__NC, _13__I3, _12__I2, _11__I1, _10__I0, _9__A0
  _74163 u_74163_1 ();  // open: _1__nMR, _2__CP, _3__D0, _4__D1, _5__D2, _6__D3, _7__CEP, _8__GND, _16__Vcc, _15__TC, _14__Q0, _13__Q1, _12__Q2, _11__O3, _10__CET, _9__nPE
  _74283 u_74283_1 ();  // open: _7__C0, _5__A1, _6__B1, _3__A2, _2__B2, _14__A3, _15__B3, _12__A4, _11__B4, _8__GND, _16__Vcc, _4__S1, _1__S2, _13__S3, _10__S4, _9__C4
  // _74xx590 74xx590_1: pin names not known
  // _74xx42 74xx42_1: pin names not known
  _74198 u_74198_1 ();  // open: _1__S0, _2__Dsr, _3__P0, _4__Q0, _5__P1, _6__Q1, _7__P2, _8__Q2, _9__P3, _10__Q3, _11__CP, _12__GND, _24__Vcc, _23__S1, _22__Dsl, _21__P7, _20__Q7, _19__P6, _18__Q6, _17__P5, _16__Q5, _15__P4, _14__Q4, _13__nMR
  _7411 u_7411_1 ();  // open: _1__1A, _2__1B, _3__2A, _4__2B, _5__2C, _6__2Y, _7__GND, _14__Vcc, _13__1C, _12__1Y, _11__3C, _10__3B, _9__3A, _8__3Y
  _7425 u_7425_1 ();  // open: _1__1A, _2__1B, _3__NC, _4__1C, _5__1D, _6__1Y, _7__GND, _14__Vcc, _13__2D, _12__2C, _11__NC, _10__2B, _9__2A, _8__2Y
  _7489 u_7489_1 ();  // open: _1__A0, _2__nCS, _3__nWE, _4__D1, _5__nO1, _6__D2, _7__nO2, _8__GND, _16__Vcc, _15__A1, _14__A2, _13__A3, _12__D4, _11__nO4, _10__D3, _9__nO3
  // _74166 74166_1: pin names not known
  _74238 u_74238_1 ();  // open: _1__A0, _2__A1, _3__A2, _4__E1_prime, _5__E2_prime, _6__E3, _7__Y7, _8__GND, _16__Vcc, _15__Y0, _14__Y1, _13__Y2, _12__Y3, _11__Y4, _10__Y5, _9__Y6
  _74371 u_74371_1 ();  // open: _1__AD_A, _2__AD_B, _3__AD_C, _4__AD_D, _5__AD_E, _6__DO_1, _7__DO_2, _8__DO_3, _9__DO_4, _10__GND, _20__Vcc, _19__AD_H, _18__AD_G, _17__AD_F, _16__nS_2, _15__nS_1, _14__DO_8, _13__DO_7, _12__DO_6, _11__DO_5
  // _74670 74670_1: pin names not known
  _7413 u_7413_1 ();  // open: _1A_1, _1B_2, _1C_4, _1D_5, _2A_9, _2B_10, _2C_12, _2D_13, Vcc_14, Gnd_7, _1Y_6, _2Y_8, NC, NC_2
  // _74109 74109_1: pin names not known
  _74150 u_74150_1 ();  // open: _1__E7, _2__E6, _3__E5, _4__E4, _5__E3, _6__E2, _7__E1, _8__E0, _9__nG, _10__W, _11__D, _12__GND, _24__Vcc, _23__E8, _22__E9, _21__E10, _20__E11, _19__E12, _18__E13, _17__E14, _16__E15, _15__A, _14__B, _13__C
  // _74173 74173_1: pin names not known
  _7427 u_7427_1 ();  // open: _1__1A, _2__1B, _3__2A, _4__2B, _5__2C, _6__2Y, _7__GND, _14__Vcc, _13__1C, _12__1Y, _11__3C, _10__3B, _9__3A, _8__3Y
  _7448 u_7448_1 ();  // open: _1__B, _2__C, _3__nLT, _4__NC, _5__nRBI, _6__D, _7__A, _8__GND, _16__Vcc, _15__f, _14__g, _13__a, _12__b, _11__c, _10__d, _9__e
  _74151 u_74151_1 ();  // open: _1__D3, _2__D2, _3__D1, _4__D0, _5__Y, _6__W, _7__nG, _8__GND, _16__Vcc, _15__D4, _14__D5, _13__D6, _12__D7, _11__A, _10__B, _9__C
  _74240 u_74240_1 ();  // open: _2__1A1, _4__1A2, _6__1A3, _8__1A4, _1__n1G, _11__2A1, _13__2A2, _15__2A3, _17__2A4, _19__n2G, _10__GND, _20__Vcc, _18__1Y1, _16__1Y2, _14__1Y3, _12__1Y4, _9__2Y1, _7__2Y2, _5__2Y3, _3__2Y4
  _74374 u_74374_1 ();  // open: D0__2, D1__3, D2__4, D3__5, D4__6, D5__7, D6__8, D7__9, nOE__1, CLK__11, Q0__19, Q1__18, Q2__17, Q3__16, Q4__15, Q5__14, Q6__13, Q7__12, GND__10, Vcc__20
  _74682 u_74682_1 ();  // open: _1__A___B, _2__A0, _3__B0, _4__A1, _5__B1, _6__A2, _7__B2, _8__A3, _9__B3, _10__GND, _20__Vcc, _19__A___B, _18__B7, _17__A7, _16__B6, _15__A6, _14__B5, _13__A5, _12__B4, _11__A4

  // Notes on the sheet:
  //   Quad 2-Input NAND
  //   6 Hex Inverters
  //   dual 2-wide
  //   2-input AOI
  //   dual 4-bit latches
  //   dual 4 to 1 MUX
  //   hex D-type flip-flop
  //   with reset; positive-edge
  //   dual quad line driver
  //   4 bit ALU
  //   triple 3-input OR
  //   Quad 2-Input NOR
  //   Dual 4-Input NAND
  //   8-input NAND
  //   13-input NAND
  //   4 to 16 decoder
  //   3-state octal
  //   bus transceiver
  //   6 Hex Inverters
  //   quad 2-input
  //   OR
  //   dual D
  //   flip-flop
  //   3 to 8 decoder
  //   quad 2 to 1
  //   MUX
  //   Carry Lookahead
  //   Generator
  //   dual 4 to 1 MUX
  //   8-bit magnitude
  //   comparator
  //   4 bit ALU
  //   6 Hex Inverter Buffer
  //   dual 4-input
  //   dual 5-input
  //   NAND
  //   dual JK
  //   flip-flop
  //   dual 2 to 4 
  //   decoder
  //   NOR
  //   octal line driver
  //   inverted
  //   Octal D-Type F/F
  //   Edge-triggered Tri-State
  //   Quad 2-Input AND
  //   dual 4-input
  //   4-bit binary
  //   full adder
  //   10 to 4 priority
  //   sync. 4-bit
  //   binary counter
  //   w/ async. clear
  //   universal shift register
  //   4-bit bidirectional
  //   octal line driver
  //   AND
  //   encoder
  //   8-Bit Register w/Clear
  //   Triple 3-Input NAND
  //   quad 2-input
  //   XOR
  //   8 to 3 priority
  //   encoder
  //   sync. 4-bit
  //   binary counter
  //   w/ sync. clear
  //   8-bit bidirectional
  //   universal shift register
  //   4-bit binary full
  //   adder w/fast carry
  //   Triple 3-Input AND
  //   dual 4-input
  //   NOR
  //   64-bit RAM
  //   16 to 1 MUX
  //   3-to-8 line
  //   decoder/demultiplexer
  //   256x8 ROM
  //   Dual 4-Input NAND
  //   triple 3-input
  //   decoder
  //   8 to 1 MUX
  //   8-bit magnitude
  //   comparator
  //   octal 3-state inverting buffer
  //   Octal D-Type F/F
  //   Edge-triggered Tri-State
  //   BCD to 7-segment
  //   NOR
endmodule

module _7400 (
  input  _1__1A,
  input  _14__Vcc,
  input  _2__1B,
  input  _13__4B,
  input  _12__4A,
  input  _4__2A,
  input  _5__2B,
  input  _10__3B,
  input  _9__3A,
  input  _7__GND,
  output _3__1Y,
  output _11__4Y,
  output _6__2Y,
  output _8__3Y
);

  nand nand_1 (_3__1Y, _2__1B, _1__1A);
  nand nand_2 (_6__2Y, _5__2B, _4__2A);
  nand nand_3 (_11__4Y, _13__4B, _12__4A);
  nand nand_4 (_8__3Y, _10__3B, _9__3A);

  // Notes on the sheet:
  //   7400: quad NAND
endmodule

module _7402 (
  input  _14__Vcc,
  input  _2__1A,
  input  _3__1B,
  input  _12__4B,
  input  _11__4A,
  input  _5__2A,
  input  _6__2B,
  input  _9__3B,
  input  _7__GND,
  input  _8__3A,
  output _1__1Y,
  output _13__4Y,
  output _4__2Y,
  output _10__3Y
);

  nor nor_1 (_1__1Y, _2__1A, _3__1B);
  nor nor_2 (_4__2Y, _5__2A, _6__2B);
  nor nor_3 (_13__4Y, _11__4A, _12__4B);
  nor nor_4 (_10__3Y, _8__3A, _9__3B);

  // Notes on the sheet:
  //   7402: quad NOR
endmodule

module _7404 (
  input  _1__1A,
  input  _14__Vcc,
  input  _13__6A,
  input  _3__2A,
  input  _11__5A,
  input  _5__3A,
  input  _9__4A,
  input  _7__GND,
  output _2__1Y,
  output _12__6Y,
  output _4__2Y,
  output _10__5Y,
  output _6__3Y,
  output _8__4Y
);

  not not_1 (_2__1Y, _1__1A);
  not not_2 (_4__2Y, _3__2A);
  not not_3 (_6__3Y, _5__3A);
  not not_4 (_12__6Y, _13__6A);
  not not_5 (_10__5Y, _11__5A);
  not not_6 (_8__4Y, _9__4A);

  // Notes on the sheet:
  //   7407: hex inverter
endmodule

module _7407 (
  input  _1__1A,
  input  _14__Vcc,
  input  _13__6A,
  input  _3__2A,
  input  _11__5A,
  input  _5__3A,
  input  _9__4A,
  input  _7__GND,
  output _2__1Y,
  output _12__6Y,
  output _4__2Y,
  output _10__5Y,
  output _6__3Y,
  output _8__4Y
);

  buf buffer_1 (_2__1Y, _1__1A);
  buf buffer_2 (_4__2Y, _3__2A);
  buf buffer_3 (_6__3Y, _5__3A);
  buf buffer_4 (_12__6Y, _13__6A);
  buf buffer_5 (_10__5Y, _11__5A);
  buf buffer_6 (_8__4Y, _9__4A);

  // Notes on the sheet:
  //   7407: hex buffer
endmodule

module _7408 (
  input  _1__1A,
  input  _14__Vcc,
  input  _2__1B,
  input  _13__4B,
  input  _12__4A,
  input  _4__2A,
  input  _5__2B,
  input  _10__3B,
  input  _9__3A,
  input  _7__GND,
  output _3__1Y,
  output _11__4Y,
  output _6__2Y,
  output _8__3Y
);

  and and_1 (_3__1Y, _2__1B, _1__1A);
  and and_2 (_6__2Y, _5__2B, _4__2A);
  and and_3 (_11__4Y, _13__4B, _12__4A);
  and and_4 (_8__3Y, _10__3B, _9__3A);

  // Notes on the sheet:
  //   7408: quad AND
endmodule

module _7410 (
  input  _1__1A,
  input  _14__Vcc,
  input  _2__1B,
  input  _13__1C,
  input  _3__2A,
  input  _4__2B,
  input  _11__3C,
  input  _5__2C,
  input  _10__3B,
  input  _9__3A,
  input  _7__GND,
  output _12__1Y,
  output _6__2Y,
  output _8__3Y
);

  nand nand_1 (_6__2Y, _5__2C, _4__2B, _3__2A);
  nand nand_2 (_12__1Y, _2__1B, _1__1A, _13__1C);
  nand nand_3 (_8__3Y, _11__3C, _10__3B, _9__3A);

  // Notes on the sheet:
  //   7410: triple 3-input NAND 
endmodule

module _7411 (
  input  _1__1A,
  input  _14__Vcc,
  input  _2__1B,
  input  _13__1C,
  input  _3__2A,
  input  _4__2B,
  input  _11__3C,
  input  _5__2C,
  input  _10__3B,
  input  _9__3A,
  input  _7__GND,
  output _12__1Y,
  output _6__2Y,
  output _8__3Y
);

  and and_1 (_6__2Y, _5__2C, _3__2A);
  and and_2 (_12__1Y, _2__1B, _13__1C);
  and and_3 (_8__3Y, _11__3C, _9__3A);

  // Notes on the sheet:
  //   7411: triple 3-input AND 
endmodule

module _7413 (
  input  _1A_1,
  input  _1B_2,
  input  _1C_4,
  input  _1D_5,
  input  _2A_9,
  input  _2B_10,
  input  _2C_12,
  input  _2D_13,
  input  Vcc_14,
  input  Gnd_7,
  output _1Y_6,
  output _2Y_8,
  output NC,
  output NC_2
);

  // NAND_Gate nand_1 has open pins: out=_1Y_6
  // NAND_Gate nand_2 has open pins: out=_2Y_8

  // Notes on the sheet:
  //   _2A_9: pull=up
  //   _1B_2: pull=up
  //   _2B_10: pull=up
  //   Vcc_14: pull=down
  //   _1A_1: pull=up
  //   _1C_4: pull=up
  //   _2C_12: pull=up
endmodule

module _7414 (
  input  _1A_1,
  input  _2A_3,
  input  _3A_5,
  input  _4A_9,
  input  _5A_11,
  input  _6A_13,
  input  Vcc_14,
  input  Gnd_7,
  output _1Y_2,
  output _2Y_4,
  output _3Y_6,
  output _4Y_8,
  output _5Y_10,
  output _6Y_12
);

  not not_1 (_1Y_2, _1A_1);
  not not_2 (_2Y_4, _2A_3);
  not not_3 (_3Y_6, _3A_5);
  not not_4 (_4Y_8, _4A_9);
  not not_5 (_5Y_10, _5A_11);
  not not_6 (_6Y_12, _6A_13);

  // Notes on the sheet:
  //   Vcc_14: pull=down
  //   _6A_13: pull=up
  //   _5A_11: pull=up
  //   _2A_3: pull=up
  //   _3A_5: pull=up
  //   _4A_9: pull=up
  //   _1A_1: pull=up
endmodule

module _7418 (
  input  _1A_1,
  input  _1B_2,
  input  _1C_4,
  input  _1D_5,
  input  _2A_9,
  input  _2B_10,
  input  _2C_12,
  input  _2D_13,
  input  Vcc_14,
  input  Gnd_7,
  output _1Y_6,
  output _2Y_8
);

  // NAND_Gate nand_1 has open pins: out=_1Y_6
  // NAND_Gate nand_2 has open pins: out=_2Y_8

  // Notes on the sheet:
  //   _2C_12: pull=up
  //   _2A_9: pull=up
  //   _2B_10: pull=up
  //   _1A_1: pull=up
  //   _1B_2: pull=up
  //   _1C_4: pull=up
  //   Vcc_14: pull=down
  //   incomplete?
endmodule

module _7419 (
  input  _1A_1,
  input  _2A_3,
  input  _3A_5,
  input  _4A_9,
  input  _5A_11,
  input  _6A_13,
  input  Vcc_14,
  input  Gnd_7,
  output _1Y_2,
  output _2Y_4,
  output _3Y_6,
  output _4Y_8,
  output _5Y_10,
  output _6Y_12,
  output Power_Test_imaginary
);

  wire not_1_out;

  not not_1 (not_1_out, Gnd_7);
  not not_2 (_1Y_2, _1A_1);
  not not_3 (_2Y_4, _2A_3);
  not not_4 (_3Y_6, _3A_5);
  not not_5 (_4Y_8, _4A_9);
  not not_6 (_5Y_10, _5A_11);
  not not_7 (_6Y_12, _6A_13);
  // AND_Gate and_1: pin names not known; wires that end beside it: Vcc_14, Vcc_14, not_1_out, Power_Test_imaginary

  // Notes on the sheet:
  //   _4A_9: pull=up
  //   _6A_13: pull=up
  //   Vcc_14: pull=down
  //   _3A_5: pull=up
  //   _2A_3: pull=up
  //   _5A_11: pull=up
  //   _1A_1: pull=up
  //   74xx19 Hex Inverters
  //   Copyright 2005 Technological Services Company
endmodule

module _7420 (
  input  _1__1A,
  input  _14__Vcc,
  input  _2__1B,
  input  _13__2D,
  input  _3__NC,
  input  _12__2C,
  input  _4__1C,
  input  _11__NC,
  input  _5__1D,
  input  _10__2B,
  input  _9__2A,
  input  _7__GND,
  output _6__1Y,
  output _8__2Y
);

  nand nand_1 (_6__1Y, _5__1D, _4__1C, _2__1B, _1__1A);
  nand nand_2 (_8__2Y, _13__2D, _12__2C, _10__2B, _9__2A);

  // Notes on the sheet:
  //   7420: dual 4-input NAND
endmodule

module _7421 (
  input  _1__1A,
  input  _14__Vcc,
  input  _2__1B,
  input  _13__2D,
  input  _3__NC,
  input  _12__2C,
  input  _4__1C,
  input  _11__NC,
  input  _5__1D,
  input  _10__2B,
  input  _9__2A,
  input  _7__GND,
  output _6__1Y,
  output _8__2Y
);

  and and_1 (_6__1Y, _5__1D, _4__1C, _2__1B, _1__1A);
  and and_2 (_8__2Y, _13__2D, _12__2C, _10__2B, _9__2A);

  // Notes on the sheet:
  //   7421: dual 4-input AND
endmodule

module _7425 (
  input  _1__1A,
  input  _14__Vcc,
  input  _2__1B,
  input  _13__2D,
  input  _3__NC,
  input  _12__2C,
  input  _4__1C,
  input  _11__NC,
  input  _5__1D,
  input  _10__2B,
  input  _9__2A,
  input  _7__GND,
  output _6__1Y,
  output _8__2Y
);

  nor nor_1 (_6__1Y, _5__1D, _4__1C, _2__1B, _1__1A);
  nor nor_2 (_8__2Y, _13__2D, _12__2C, _10__2B, _9__2A);

  // Notes on the sheet:
  //   7425: dual 4-input NOR
endmodule

module _7427 (
  input  _1__1A,
  input  _14__Vcc,
  input  _2__1B,
  input  _13__1C,
  input  _3__2A,
  input  _4__2B,
  input  _11__3C,
  input  _5__2C,
  input  _10__3B,
  input  _9__3A,
  input  _7__GND,
  output _12__1Y,
  output _6__2Y,
  output _8__3Y
);

  nor nor_1 (_6__2Y, _5__2C, _4__2B, _3__2A);
  nor nor_2 (_12__1Y, _2__1B, _1__1A, _13__1C);
  nor nor_3 (_8__3Y, _11__3C, _10__3B, _9__3A);

  // Notes on the sheet:
  //   7427: triple 3-input NOR 
endmodule

module _7430 (
  input  _1__1A,
  input  _14__Vcc,
  input  _2__1B,
  input  _13__NC,
  input  _3__1C,
  input  _12__1H,
  input  _4__1D,
  input  _11__1G,
  input  _5__1E,
  input  _10__NC,
  input  _6__1F,
  input  _9__NC,
  input  _7__GND,
  output _8__3Y
);

  nand nand_1 (_8__3Y, _6__1F, _5__1E, _4__1D, _3__1C, _2__1B, _1__1A, _12__1H, _11__1G);

  // Notes on the sheet:
  //   7430: 8-input NAND 
endmodule

module _7432 (
  input  _1__1A,
  input  _14__Vcc,
  input  _2__1B,
  input  _13__4B,
  input  _12__4A,
  input  _4__2A,
  input  _5__2B,
  input  _10__3B,
  input  _9__3A,
  input  _7__GND,
  output _3__1Y,
  output _11__4Y,
  output _6__2Y,
  output _8__3Y
);

  or or_1 (_3__1Y, _2__1B, _1__1A);
  or or_2 (_6__2Y, _5__2B, _4__2A);
  or or_3 (_11__4Y, _13__4B, _12__4A);
  or or_4 (_8__3Y, _10__3B, _9__3A);

  // Notes on the sheet:
  //   7432: quad OR
endmodule

module _7448 (
  input  _1__B,
  input  _16__Vcc,
  input  _2__C,
  input  _3__nLT,
  input  _4__NC,
  input  _5__nRBI,
  input  _6__D,
  input  _7__A,
  input  _8__GND,
  output _15__f,
  output _14__g,
  output _13__a,
  output _12__b,
  output _11__c,
  output _10__d,
  output _9__e
);

  wire nand_1_out, nand_2_out, nand_3_out, nand_4_out, nand_5_out, nand_6_out, nand_7_out, nand_8_out,
       nand_9_out, nand_10_out, nand_11_out, nand_12_out, nand_13_out, nand_14_out, nand_15_out, nand_16_out,
       nand_17_out, nand_18_out, nand_19_out, nand_20_out, nand_21_out, nand_22_out, nand_23_out,
       nand_24_out, nand_25_out, not_1_out, not_2_out, not_3_out;

  nand nand_1 (nand_1_out, _7__A, _3__nLT);
  nand nand_2 (nand_2_out, _1__B, _3__nLT);
  nand nand_3 (nand_3_out, _2__C, _3__nLT);
  not not_1 (not_1_out, _6__D);
  not not_2 (not_2_out, _5__nRBI);
  nand nand_4 (nand_4_out, nand_1_out, nand_8_out);
  nand nand_5 (nand_5_out, nand_2_out, nand_8_out);
  nand nand_6 (nand_6_out, nand_3_out, nand_8_out);
  nand nand_7 (nand_7_out, not_1_out, nand_8_out);
  nand nand_8 (nand_8_out, _3__nLT, not_2_out, not_1_out, nand_3_out, nand_2_out, nand_1_out);
  nand nand_9 (nand_9_out, nand_5_out, nand_7_out);
  nand nand_10 (nand_10_out, nand_1_out, nand_6_out);
  nand nand_11 (nand_11_out, nand_4_out, nand_3_out);
  nand nand_12 (nand_12_out, nand_5_out, nand_7_out);
  nand nand_13 (nand_13_out, nand_4_out, nand_2_out, nand_6_out);
  nand nand_14 (nand_14_out, nand_1_out, nand_5_out, nand_6_out);
  nand nand_15 (nand_15_out, nand_6_out, nand_7_out);
  nand nand_16 (nand_16_out, nand_1_out, nand_5_out, nand_3_out);
  nand nand_17 (nand_17_out, nand_4_out, nand_2_out, nand_3_out);
  nand nand_18 (nand_18_out, nand_1_out, nand_2_out, nand_6_out);
  nand nand_19 (nand_19_out, nand_4_out, nand_5_out, nand_6_out);
  not not_3 (not_3_out, nand_4_out);
  nand nand_20 (nand_20_out, nand_2_out, nand_6_out);
  nand nand_21 (nand_21_out, nand_4_out, nand_5_out);
  nand nand_22 (nand_22_out, nand_5_out, nand_3_out);
  nand nand_23 (nand_23_out, nand_4_out, nand_3_out, not_1_out);
  nand nand_24 (nand_24_out, nand_4_out, nand_5_out, nand_6_out);
  nand nand_25 (nand_25_out, nand_2_out, not_1_out);
  and and_1 (_13__a, nand_9_out, nand_10_out, nand_11_out);
  and and_2 (_12__b, nand_12_out, nand_13_out, nand_14_out);
  and and_3 (_11__c, nand_15_out, nand_16_out);
  and and_4 (_10__d, nand_17_out, nand_18_out, nand_19_out);
  and and_5 (_9__e, not_3_out, nand_20_out);
  and and_6 (_15__f, nand_21_out, nand_22_out, nand_23_out);
  and and_7 (_14__g, nand_24_out, nand_25_out);

  // Notes on the sheet:
  //   7448: BCD to 7-segment decoder
endmodule

module _7451 (
  input  _1__1A,
  input  _14__Vcc,
  input  _2__2A,
  input  _13__1B,
  input  _3__2B,
  input  _12__NC,
  input  _4__2C,
  input  _11__NC,
  input  _5__2D,
  input  _10__1D,
  input  _9__1C,
  input  _7__GND,
  output _6__2Y,
  output _8__1Y
);

  wire and_1_out, and_2_out, and_3_out, and_4_out;

  nor nor_1 (_8__1Y, and_3_out, and_4_out);
  and and_1 (and_1_out, _2__2A, _3__2B);
  and and_2 (and_2_out, _4__2C, _5__2D);
  and and_3 (and_3_out, _1__1A, _13__1B);
  and and_4 (and_4_out, _10__1D, _9__1C);
  nor nor_2 (_6__2Y, and_2_out, and_1_out);

  // Notes on the sheet:
  //   7451: dual 2-wide 2-input AND-OR-Invert gate
endmodule

module _7474 (
  input  _1__CLR1,
  input  _14__Vcc,
  input  _2__D1,
  input  _13__CLR2,
  input  _3__CLK1,
  input  _12__D2,
  input  _4__PR1,
  input  _11__CLK2,
  input  _10__PR2,
  input  _7__GND,
  output _5__Q1,
  output _6__nQ1,
  output _9__Q2,
  output _8__nQ2
);

  D_Flip_Flop #(.Pre_Clr_Positions("LEGACY"), .enable("true"), .NewFFLayout("false")) d_ff_1 (
    .clk(_3__CLK1), .D(_2__D1), .Q(_5__Q1), .Qn(_6__nQ1), .preset(_4__PR1), .reset(_1__CLR1));  // open: en
  D_Flip_Flop #(.Pre_Clr_Positions("LEGACY"), .enable("true"), .NewFFLayout("false")) d_ff_2 (
    .clk(_11__CLK2), .D(_12__D2), .Q(_9__Q2), .Qn(_8__nQ2), .preset(_10__PR2), .reset(_13__CLR2));  // open: en

  // Notes on the sheet:
  //   7474: dual D-type flip flop
endmodule

module _7476 (
  input  _1__CLK1,
  input  _16__K1,
  input  _2__PR1,
  input  _3__CLR1,
  input  _4__J1,
  input  _13__GND,
  input  _5__VCC,
  input  _12__K2,
  input  _6__CLK2,
  input  _7__PR2,
  input  _8__CLR2,
  input  _9__J2,
  output _15__Q1,
  output _14__nQ1,
  output _11__Q2,
  output _10__nQ2
);

  J_K_Flip_Flop #(.Pre_Clr_Positions("LEGACY"), .enable("true"), .NewFFLayout("false")) j_k_ff_1 (
    .J(_4__J1), .clk(_1__CLK1), .K(_16__K1), .Q(_15__Q1), .Qn(_14__nQ1), .preset(_2__PR1), .reset(_3__CLR1));  // open: en
  J_K_Flip_Flop #(.Pre_Clr_Positions("LEGACY"), .enable("true"), .NewFFLayout("false")) j_k_ff_2 (
    .J(_9__J2), .clk(_6__CLK2), .K(_12__K2), .Q(_11__Q2), .Qn(_10__nQ2), .preset(_7__PR2), .reset(_8__CLR2));  // open: en

  // Notes on the sheet:
  //   7476: dual JK-type flip flop
endmodule

module _7483 (
  input  _1__A4,
  input  _16__B4,
  input  _3__A3,
  input  _14__Cout,
  input  _4__B3,
  input  _13__Cin,
  input  _5__Vcc,
  input  _12__GND,
  input  _11__B1,
  input  _7__B2,
  input  _10__A1,
  input  _8__A2,
  output _2__S3,
  output _15__S4,
  output _6__S2,
  output _9__S1
);

  wire and_1_out, and_2_out, and_3_out, and_4_out, and_5_out, and_6_out, and_7_out, and_8_out, and_9_out,
       and_10_out, and_11_out, and_12_out, and_13_out, and_14_out, nand_1_out, nand_2_out, nand_3_out,
       nand_4_out, nor_1_out, nor_2_out, nor_3_out, nor_4_out, nor_6_out, nor_7_out, nor_8_out, not_1_out,
       not_2_out, not_3_out, not_4_out, not_5_out, not_6_out;

  nand nand_1 (nand_1_out, _16__B4, _1__A4);
  nor nor_1 (nor_1_out, _16__B4, _1__A4);
  nand nand_2 (nand_2_out, _4__B3, _3__A3);
  nor nor_2 (nor_2_out, _4__B3, _3__A3);
  nand nand_3 (nand_3_out, _7__B2, _8__A2);
  nor nor_3 (nor_3_out, _7__B2, _8__A2);
  nand nand_4 (nand_4_out, _11__B1, _10__A1);
  nor nor_4 (nor_4_out, _11__B1, _10__A1);
  and and_1 (and_1_out, nor_2_out, nand_1_out);
  and and_2 (and_2_out, nor_3_out, nand_1_out, nand_2_out);
  and and_3 (and_3_out, nor_4_out, nand_2_out);
  and and_4 (and_4_out, nand_2_out, nand_4_out);
  not not_1 (not_1_out, nor_1_out);
  and and_5 (and_5_out, nor_3_out, nand_2_out);
  and and_6 (and_6_out, nor_4_out, nand_2_out, nand_3_out);
  and and_7 (and_7_out, nand_2_out, nand_4_out);
  not not_2 (not_2_out, _13__Cin);
  not not_3 (not_3_out, nor_2_out);
  and and_8 (and_8_out, nor_4_out, nand_3_out);
  and and_9 (and_9_out, nand_3_out, nand_4_out, not_2_out);
  not not_4 (not_4_out, nor_3_out);
  and and_10 (and_10_out, nand_4_out, not_2_out);
  not not_5 (not_5_out, nor_4_out);
  not not_6 (not_6_out, not_2_out);
  nor nor_5 (_14__Cout, and_1_out, and_3_out);
  and and_11 (and_11_out, nand_1_out, not_1_out);
  and and_12 (and_12_out, nand_2_out, not_3_out);
  and and_13 (and_13_out, nand_3_out, not_4_out);
  and and_14 (and_14_out, nand_4_out, not_5_out);
  xor xor_1 (_15__S4, and_11_out, nor_6_out);
  not nor_6 (nor_6_out, and_5_out);  // NOR_Gate
  xor xor_2 (_2__S3, and_12_out, nor_7_out);
  nor nor_7 (nor_7_out, nor_3_out, and_8_out, and_9_out);
  xor xor_3 (_6__S2, and_13_out, nor_8_out);
  nor nor_8 (nor_8_out, nor_4_out, and_10_out);
  xor xor_4 (_9__S1, and_14_out, not_6_out);

  // Notes on the sheet:
  //   7483: 4-bit full adder
endmodule

module _7486 (
  input  _1__1A,
  input  _14__Vcc,
  input  _2__1B,
  input  _13__4B,
  input  _12__4A,
  input  _4__2A,
  input  _5__2B,
  input  _10__3B,
  input  _9__3A,
  input  _7__GND,
  output _3__1Y,
  output _11__4Y,
  output _6__2Y,
  output _8__3Y
);

  xor xor_1 (_3__1Y, _2__1B, _1__1A);
  xor xor_2 (_6__2Y, _5__2B, _4__2A);
  xor xor_3 (_11__4Y, _13__4B, _12__4A);
  xor xor_4 (_8__3Y, _10__3B, _9__3A);

  // Notes on the sheet:
  //   7486: quad XOR
endmodule

module _7489 (
  input  _1__A0,
  input  _16__Vcc,
  input  _2__nCS,
  input  _15__A1,
  input  _3__nWE,
  input  _14__A2,
  input  _4__D1,
  input  _13__A3,
  input  _12__D4,
  input  _6__D2,
  input  _10__D3,
  input  _8__GND,
  output _5__nO1,
  output _11__nO4,
  output _7__nO2,
  output _9__nO3
);

  wire not_1_out, not_2_out, or_1_out;
  wire [3:0] ram_1_data;

  not not_1 (not_1_out, _2__nCS);
  not not_2 (not_2_out, _3__nWE);
  or or_1 (or_1_out, not_2_out, not_1_out);
  RAM #(.addrWidth(4), .dataWidth(4), .bus("separate")) ram_1 (
    .addr({_13__A3, _14__A2, _15__A1, _1__A0}), .din({_12__D4, _10__D3, _6__D2, _4__D1}), .data(ram_1_data),
    .sel(not_1_out), .clk(not_2_out), .ld(or_1_out));  // open: str, clr
  assign {_11__nO4, _9__nO3, _7__nO2, _5__nO1} = ~ram_1_data;  // NOT_Gate not_3, 4 bits wide

  // Notes on the sheet:
  //   7489: 64-bit RAM
endmodule

module _74116 (
  input  _1__nMRa,
  input  _24__Vcc,
  input  _2__nE0a,
  input  _3__nE1a,
  input  _22__D3b,
  input  _4__D0a,
  input  _20__D2b,
  input  _6__D1a,
  input  _18__D1b,
  input  _8__D2a,
  input  _16__D0b,
  input  _10__D3a,
  input  _15__nE1b,
  input  _14__nE0b,
  input  _12__GND,
  input  _13__nMRb,
  output _23__Q3b,
  output _21__Q2b,
  output _5__Q0a,
  output _19__Q1b,
  output _7__Q1a,
  output _17__Q0b,
  output _9__Q2a,
  output _11__Q3a
);

  wire and_1_out, and_2_out, not_1_out, not_2_out;

  not not_1 (not_1_out, _1__nMRa);
  and and_1 (and_1_out, ~_2__nE0a, ~_3__nE1a);  // AND_Gate
  D_Flip_Flop #(.trigger("high"), .Pre_Clr_Positions("LEGACY"), .enable("true"), .NewFFLayout("false")) d_ff_1 (
    .clk(and_1_out), .D(_4__D0a), .Q(_5__Q0a), .reset(not_1_out));  // open: Qn, preset, en
  D_Flip_Flop #(.trigger("high"), .Pre_Clr_Positions("LEGACY"), .enable("true"), .NewFFLayout("false")) d_ff_2 (
    .clk(and_1_out), .D(_6__D1a), .Q(_7__Q1a), .reset(not_1_out));  // open: Qn, preset, en
  D_Flip_Flop #(.trigger("high"), .Pre_Clr_Positions("LEGACY"), .enable("true"), .NewFFLayout("false")) d_ff_3 (
    .clk(and_1_out), .D(_8__D2a), .Q(_9__Q2a), .reset(not_1_out));  // open: Qn, preset, en
  D_Flip_Flop #(.trigger("high"), .Pre_Clr_Positions("LEGACY"), .enable("true"), .NewFFLayout("false")) d_ff_4 (
    .clk(and_1_out), .D(_10__D3a), .Q(_11__Q3a), .reset(not_1_out));  // open: Qn, preset, en
  D_Flip_Flop #(.trigger("high"), .Pre_Clr_Positions("LEGACY"), .enable("true"), .NewFFLayout("false")) d_ff_5 (
    .clk(and_2_out), .D(_22__D3b), .Q(_23__Q3b), .reset(not_2_out));  // open: Qn, preset, en
  D_Flip_Flop #(.trigger("high"), .Pre_Clr_Positions("LEGACY"), .enable("true"), .NewFFLayout("false")) d_ff_6 (
    .clk(and_2_out), .D(_20__D2b), .Q(_21__Q2b), .reset(not_2_out));  // open: Qn, preset, en
  D_Flip_Flop #(.trigger("high"), .Pre_Clr_Positions("LEGACY"), .enable("true"), .NewFFLayout("false")) d_ff_7 (
    .clk(and_2_out), .D(_18__D1b), .Q(_19__Q1b), .reset(not_2_out));  // open: Qn, preset, en
  D_Flip_Flop #(.trigger("high"), .Pre_Clr_Positions("LEGACY"), .enable("true"), .NewFFLayout("false")) d_ff_8 (
    .clk(and_2_out), .D(_16__D0b), .Q(_17__Q0b), .reset(not_2_out));  // open: Qn, preset, en
  and and_2 (and_2_out, ~_15__nE1b, ~_14__nE0b);  // AND_Gate
  not not_2 (not_2_out, _13__nMRb);

  // Notes on the sheet:
  //   74116: dual 4-bit latches
endmodule

module _74125 (
  input  B0__2,
  input  A0__1,
  input  B1__5,
  input  A1__4,
  input  B2__12,
  input  A2__13,
  input  B3__9,
  input  A3__10,
  input  Vcc__14,
  input  GND__7,
  output O0__3,
  output O1__6,
  output O2__11,
  output O3__8
);

  wire not_1_out, not_2_out, not_3_out, not_4_out;

  not not_1 (not_1_out, A0__1);
  not not_2 (not_2_out, A1__4);
  not not_3 (not_3_out, A2__13);
  not not_4 (not_4_out, A3__10);
  assign O0__3 = not_1_out ? B0__2 : 1'bz;  // Controlled_Buffer controlled_buffer_1
  assign O1__6 = not_2_out ? B1__5 : 1'bz;  // Controlled_Buffer controlled_buffer_2
  assign O2__11 = not_3_out ? B2__12 : 1'bz;  // Controlled_Buffer controlled_buffer_3
  assign O3__8 = not_4_out ? B3__9 : 1'bz;  // Controlled_Buffer controlled_buffer_4
endmodule

module _74133 (
  input  _1__A,
  input  _16__Vcc,
  input  _2__B,
  input  _15__M,
  input  _3__C,
  input  _14__L,
  input  _4__D,
  input  _13__K,
  input  _5__E,
  input  _12__J,
  input  _6__F,
  input  _11__I,
  input  _7__G,
  input  _10__H,
  input  _8__GND,
  output _9__Y
);

  nand nand_1 (_9__Y, _7__G, _6__F, _5__E, _4__D, _3__C, _2__B, _1__A, _15__M, _14__L, _13__K, _12__J, _11__I, _10__H);

  // Notes on the sheet:
  //   74133: 13-input NAND
endmodule

module _74138 (
  input  _1__A,
  input  _16__Vcc,
  input  _2__B,
  input  _3__C,
  input  _4__G2A,
  input  _5__G2B,
  input  _6__G1,
  input  _8__GND,
  output _15__Y0,
  output _14__Y1,
  output _13__Y2,
  output _12__Y3,
  output _11__Y4,
  output _7__Y7,
  output _10__Y5,
  output _9__Y6
);

  wire and_1_out, and_2_out, and_3_out, and_4_out, and_5_out, and_6_out, and_7_out, and_8_out, and_9_out,
       decoder_1_out0, decoder_1_out1, decoder_1_out2, decoder_1_out3, decoder_1_out4, decoder_1_out5,
       decoder_1_out6, decoder_1_out7, not_1_out, not_2_out;

  not not_1 (not_1_out, _4__G2A);
  not not_2 (not_2_out, _5__G2B);
  and and_1 (and_1_out, and_2_out, decoder_1_out7);
  not not_3 (_7__Y7, and_1_out);
  and and_2 (and_2_out, not_1_out, not_2_out, _6__G1);
  Decoder #(.select(3), .enable("false")) decoder_1 (
    .out0(decoder_1_out0), .out1(decoder_1_out1), .out2(decoder_1_out2), .out3(decoder_1_out3),
    .out4(decoder_1_out4), .out5(decoder_1_out5), .out6(decoder_1_out6), .out7(decoder_1_out7),
    .sel({_3__C, _2__B, _1__A}));
  and and_3 (and_3_out, and_2_out, decoder_1_out0);
  not not_4 (_15__Y0, and_3_out);
  not not_5 (_14__Y1, and_4_out);
  and and_4 (and_4_out, and_2_out, decoder_1_out1);
  not not_6 (_13__Y2, and_5_out);
  and and_5 (and_5_out, and_2_out, decoder_1_out2);
  and and_6 (and_6_out, and_2_out, decoder_1_out3);
  not not_7 (_12__Y3, and_6_out);
  and and_7 (and_7_out, and_2_out, decoder_1_out4);
  not not_8 (_11__Y4, and_7_out);
  and and_8 (and_8_out, and_2_out, decoder_1_out5);
  not not_9 (_10__Y5, and_8_out);
  not not_10 (_9__Y6, and_9_out);
  and and_9 (and_9_out, and_2_out, decoder_1_out6);

  // Notes on the sheet:
  //   74138: 3-Line to 8-Line Decoder
endmodule

module _74139 (
  input  _1__1G,
  input  _16__Vcc,
  input  _2__1A,
  input  _15__2G,
  input  _3__1B,
  input  _14__2A,
  input  _13__2B,
  input  _8__GND,
  output _4__1Y0,
  output _5__1Y1,
  output _12__2Y0,
  output _6__1Y2,
  output _11__2Y1,
  output _7__1Y3,
  output _10__2Y2,
  output _9__2Y3
);

  wire decoder_1_out0, decoder_1_out1, decoder_1_out2, decoder_1_out3, decoder_2_out0, decoder_2_out1,
       decoder_2_out2, decoder_2_out3, not_1_out, not_2_out, not_3_out, not_4_out, not_5_out, not_6_out,
       not_7_out, not_8_out, not_9_out, not_10_out;

  not not_1 (not_1_out, _1__1G);
  and and_1 (_4__1Y0, not_1_out, not_2_out);
  not not_2 (not_2_out, decoder_1_out0);
  and and_2 (_5__1Y1, not_1_out, not_3_out);
  not not_3 (not_3_out, decoder_1_out1);
  and and_3 (_6__1Y2, not_1_out, not_4_out);
  not not_4 (not_4_out, decoder_1_out2);
  and and_4 (_7__1Y3, not_1_out, not_5_out);
  not not_5 (not_5_out, decoder_1_out3);
  Decoder #(.select(2), .enable("false")) decoder_1 (
    .out0(decoder_1_out0), .out1(decoder_1_out1), .out2(decoder_1_out2), .out3(decoder_1_out3),
    .sel({_3__1B, _2__1A}));
  Decoder #(.select(2), .enable("false")) decoder_2 (
    .out0(decoder_2_out0), .out1(decoder_2_out1), .out2(decoder_2_out2), .out3(decoder_2_out3),
    .sel({_13__2B, _14__2A}));
  not not_6 (not_6_out, _15__2G);
  not not_7 (not_7_out, decoder_2_out0);
  not not_8 (not_8_out, decoder_2_out1);
  not not_9 (not_9_out, decoder_2_out2);
  not not_10 (not_10_out, decoder_2_out3);
  and and_5 (_12__2Y0, not_6_out, not_7_out);
  and and_6 (_11__2Y1, not_6_out, not_8_out);
  and and_7 (_10__2Y2, not_6_out, not_9_out);
  and and_8 (_9__2Y3, not_6_out, not_10_out);

  // Notes on the sheet:
  //   74139: Dual 2-Line to 4-Line Decoder
endmodule

module _74147 (
  input  _1__I4,
  input  _16__Vcc,
  input  _2__I5,
  input  _15__NC,
  input  _3__I6,
  input  _4__I7,
  input  _13__I3,
  input  _5__I8,
  input  _12__I2,
  input  _11__I1,
  input  _10__I9,
  input  _8__GND,
  output _14__A3,
  output _6__A2,
  output _7__A1,
  output _9__A0
);

  Priority_Encoder #(.select(4)) priority_encoder_1 (
    .in0(_11__I1), .in1(_12__I2), .in2(_13__I3), .in3(_1__I4), .in4(_2__I5), .in5(_3__I6), .in6(_4__I7),
    .in7(_5__I8), .in8(_10__I9), .out({_14__A3, _6__A2, _7__A1, _9__A0}));  // open: in9, in10, in11, in12, in13, in14, in15, gs, en_out, en_in

  // Notes on the sheet:
  //   74147: 9-Line to 4-Line Priority Encoder
endmodule

module _74148 (
  input  _1__I4,
  input  _16__Vcc,
  input  _2__I5,
  input  _15__nEO__NC,
  input  _3__I6,
  input  _14__nGS__NC,
  input  _4__I7,
  input  _13__I3,
  input  _5__nEI__NC,
  input  _12__I2,
  input  _6__A2,
  input  _11__I1,
  input  _7__A1,
  input  _10__I0,
  input  _8__GND,
  input  _9__A0
);

  Priority_Encoder priority_encoder_1 (
    .in0(_10__I0), .in1(_11__I1), .in2(_12__I2), .in3(_13__I3), .in4(_1__I4), .in5(_2__I5), .in6(_3__I6),
    .in7(_4__I7), .out({_7__A1, _6__A2, _9__A0}));  // open: gs, en_out, en_in

  // Notes on the sheet:
  //   74148: 9-Line to 4-Line Priority Encoder
  //   NOTE: Pins 5, 14, and 15 have connections normally, but I chose not to model them
endmodule

module _74150 (
  input  _1__E7,
  input  _24__Vcc,
  input  _2__E6,
  input  _23__E8,
  input  _3__E5,
  input  _22__E9,
  input  _4__E4,
  input  _21__E10,
  input  _5__E3,
  input  _20__E11,
  input  _6__E2,
  input  _19__E12,
  input  _7__E1,
  input  _18__E13,
  input  _8__E0,
  input  _17__E14,
  input  _9__nG,
  input  _16__E15,
  input  _15__A,
  input  _11__D,
  input  _14__B,
  input  _12__GND,
  input  _13__C,
  output _10__W
);

  wire multiplexer_1_out, not_1_out;

  or or_1 (_10__W, _9__nG, not_1_out);
  Multiplexer #(.select(4), .enable("false")) multiplexer_1 (
    .in0(_8__E0), .in1(_7__E1), .in2(_6__E2), .in3(_5__E3), .in4(_4__E4), .in5(_3__E5), .in6(_2__E6),
    .in7(_1__E7), .in8(_23__E8), .in9(_22__E9), .in10(_21__E10), .in11(_20__E11), .in12(_19__E12),
    .in13(_18__E13), .in14(_17__E14), .in15(_16__E15), .out(multiplexer_1_out),
    .sel({_11__D, _13__C, _14__B, _15__A}));
  not not_1 (not_1_out, multiplexer_1_out);

  // Notes on the sheet:
  //   74150: 16-Line to 1-Line Multiplexer
endmodule

module _74151 (
  input  _1__D3,
  input  _16__Vcc,
  input  _2__D2,
  input  _15__D4,
  input  _3__D1,
  input  _14__D5,
  input  _4__D0,
  input  _13__D6,
  input  _12__D7,
  input  _11__A,
  input  _7__nG,
  input  _10__B,
  input  _8__GND,
  input  _9__C,
  output _5__Y,
  output _6__W
);

  wire multiplexer_1_out, not_2_out;

  not not_1 (_5__Y, _6__W);
  or or_1 (_6__W, not_2_out, _7__nG);
  not not_2 (not_2_out, multiplexer_1_out);
  Multiplexer #(.select(3), .enable("false")) multiplexer_1 (
    .in0(_4__D0), .in1(_3__D1), .in2(_2__D2), .in3(_1__D3), .in4(_15__D4), .in5(_14__D5), .in6(_13__D6),
    .in7(_12__D7), .out(multiplexer_1_out), .sel({_9__C, _10__B, _11__A}));

  // Notes on the sheet:
  //   74151: 8-Line to 1-Line Multiplexer
endmodule

module _74153 (
  input  _1__nG1,
  input  _16__Vcc,
  input  _2__B,
  input  _15__nG2,
  input  _3__1C3,
  input  _14__A,
  input  _4__1C2,
  input  _13__2C3,
  input  _5__1C1,
  input  _12__2C2,
  input  _6__1C0,
  input  _11__2C1,
  input  _10__2C0,
  input  _8__GND,
  output _7__Y1,
  output _9__Y2
);

  wire multiplexer_1_out, multiplexer_2_out, not_1_out, not_2_out;

  not not_1 (not_1_out, _1__nG1);
  Multiplexer #(.select(2), .enable("false")) multiplexer_1 (
    .in0(_6__1C0), .in1(_5__1C1), .in2(_4__1C2), .in3(_3__1C3), .out(multiplexer_1_out), .sel({_2__B, _14__A}));
  and and_1 (_7__Y1, multiplexer_1_out, not_1_out);
  not not_2 (not_2_out, _15__nG2);
  Multiplexer #(.select(2), .enable("false")) multiplexer_2 (
    .in0(_10__2C0), .in1(_11__2C1), .in2(_12__2C2), .in3(_13__2C3), .out(multiplexer_2_out),
    .sel({_2__B, _14__A}));
  and and_2 (_9__Y2, multiplexer_2_out, not_2_out);

  // Notes on the sheet:
  //   74153: Dual 4-Line to 1-Line Multiplexer
endmodule

module _74154 (
  input  _24__Vcc,
  input  _23__A,
  input  _22__B,
  input  _21__C,
  input  _20__D,
  input  _19__G2,
  input  _18__G1,
  input  _12__GND,
  output _1__Y0,
  output _2__Y1,
  output _3__Y2,
  output _4__Y3,
  output _5__Y4,
  output _6__Y5,
  output _7__Y6,
  output _8__Y7,
  output _17__Y15,
  output _9__Y8,
  output _16__Y14,
  output _10__Y9,
  output _15__Y13,
  output _11__Y10,
  output _14__Y12,
  output _13__Y11
);

  wire and_12_out, decoder_1_out0, decoder_1_out1, decoder_1_out2, decoder_1_out3, decoder_1_out4,
       decoder_1_out5, decoder_1_out6, decoder_1_out7, decoder_1_out8, decoder_1_out9, decoder_1_out10,
       decoder_1_out11, decoder_1_out12, decoder_1_out13, decoder_1_out14, decoder_1_out15, not_1_out,
       not_2_out, not_3_out, not_4_out, not_5_out, not_6_out, not_7_out, not_8_out, not_9_out, not_10_out,
       not_11_out, not_12_out, not_13_out, not_14_out, not_15_out, not_16_out, not_17_out, not_18_out;

  not not_1 (not_1_out, decoder_1_out0);
  and and_1 (_1__Y0, not_1_out, and_12_out);
  not not_2 (not_2_out, decoder_1_out1);
  and and_2 (_2__Y1, not_2_out, and_12_out);
  not not_3 (not_3_out, decoder_1_out2);
  and and_3 (_3__Y2, not_3_out, and_12_out);
  not not_4 (not_4_out, decoder_1_out3);
  and and_4 (_4__Y3, not_4_out, and_12_out);
  not not_5 (not_5_out, decoder_1_out4);
  and and_5 (_5__Y4, not_5_out, and_12_out);
  not not_6 (not_6_out, decoder_1_out5);
  and and_6 (_6__Y5, not_6_out, and_12_out);
  not not_7 (not_7_out, decoder_1_out6);
  and and_7 (_7__Y6, not_7_out, and_12_out);
  not not_8 (not_8_out, decoder_1_out7);
  and and_8 (_8__Y7, not_8_out, and_12_out);
  not not_9 (not_9_out, decoder_1_out8);
  and and_9 (_9__Y8, not_9_out, and_12_out);
  not not_10 (not_10_out, decoder_1_out9);
  and and_10 (_10__Y9, not_10_out, and_12_out);
  not not_11 (not_11_out, decoder_1_out10);
  and and_11 (_11__Y10, not_11_out, and_12_out);
  and and_12 (and_12_out, not_12_out, not_13_out);
  Decoder #(.select(4), .enable("false")) decoder_1 (
    .out0(decoder_1_out0), .out1(decoder_1_out1), .out2(decoder_1_out2), .out3(decoder_1_out3),
    .out4(decoder_1_out4), .out5(decoder_1_out5), .out6(decoder_1_out6), .out7(decoder_1_out7),
    .out8(decoder_1_out8), .out9(decoder_1_out9), .out10(decoder_1_out10), .out11(decoder_1_out11),
    .out12(decoder_1_out12), .out13(decoder_1_out13), .out14(decoder_1_out14), .out15(decoder_1_out15),
    .sel({_20__D, _21__C, _22__B, _23__A}));
  not not_12 (not_12_out, _19__G2);
  not not_13 (not_13_out, _18__G1);
  not not_14 (not_14_out, decoder_1_out15);
  and and_13 (_17__Y15, not_14_out, and_12_out);
  not not_15 (not_15_out, decoder_1_out14);
  and and_14 (_16__Y14, not_15_out, and_12_out);
  not not_16 (not_16_out, decoder_1_out13);
  and and_15 (_15__Y13, not_16_out, and_12_out);
  not not_17 (not_17_out, decoder_1_out12);
  and and_16 (_14__Y12, not_17_out, and_12_out);
  not not_18 (not_18_out, decoder_1_out11);
  and and_17 (_13__Y11, not_18_out, and_12_out);

  // Notes on the sheet:
  //   74154: 4-Line to 16-Line Decoder
endmodule

module _74157 (
  input  _1__S,
  input  _16__Vcc,
  input  _2__A1,
  input  _15__G,
  input  _3__B1,
  input  _14__A4,
  input  _13__B4,
  input  _5__A2,
  input  _6__B2,
  input  _11__A3,
  input  _10__B3,
  input  _8__GND,
  output _4__Y1,
  output _12__Y4,
  output _7__Y2,
  output _9__Y3
);

  wire multiplexer_1_out, multiplexer_2_out, multiplexer_3_out, multiplexer_4_out, not_1_out;

  Multiplexer #(.enable("false")) multiplexer_1 (.in0(_2__A1), .in1(_3__B1), .out(multiplexer_1_out), .sel(_1__S));
  and and_1 (_4__Y1, multiplexer_1_out, not_1_out);
  Multiplexer #(.enable("false")) multiplexer_2 (.in0(_5__A2), .in1(_6__B2), .out(multiplexer_2_out), .sel(_1__S));
  and and_2 (_7__Y2, multiplexer_2_out, not_1_out);
  not not_1 (not_1_out, _15__G);
  Multiplexer #(.enable("false")) multiplexer_3 (.in0(_14__A4), .in1(_13__B4), .out(multiplexer_3_out), .sel(_1__S));
  and and_3 (_12__Y4, multiplexer_3_out, not_1_out);
  Multiplexer #(.enable("false")) multiplexer_4 (.in0(_11__A3), .in1(_10__B3), .out(multiplexer_4_out), .sel(_1__S));
  and and_4 (_9__Y3, multiplexer_4_out, not_1_out);

  // Notes on the sheet:
  //   74157: Quad 2-Line to 1-Line Multiplexer
endmodule

module _74161 (
  input  _1__nMR,
  input  _16__Vcc,
  input  _2__CP,
  input  _3__D0,
  input  _4__D1,
  input  _5__D2,
  input  _6__D3,
  input  _7__CEP,
  input  _10__CET,
  input  _8__GND,
  input  _9__nPE,
  output _15__TC,
  output _14__Q0,
  output _13__Q1,
  output _12__Q2,
  output _11__O3
);

  wire and_1_out, counter_1_carry, not_1_out, not_2_out;

  not not_1 (not_1_out, _1__nMR);
  and and_1 (and_1_out, _7__CEP, _9__nPE, _10__CET);
  Counter #(.width(4), .max('hf)) counter_1 (
    .load(not_2_out), .D({_6__D3, _5__D2, _4__D1, _3__D0}), .count(and_1_out),
    .Q({_11__O3, _12__Q2, _13__Q1, _14__Q0}), .carry(counter_1_carry), .clk(_2__CP), .clr(not_1_out));
  and and_2 (_15__TC, counter_1_carry, _10__CET);
  not not_2 (not_2_out, _9__nPE);

  // Notes on the sheet:
  //   74161: Synchronous 4-bit Binary Counter with Asynchronous Clear 
endmodule

module _74163 (
  input  _1__nMR,
  input  _16__Vcc,
  input  _2__CP,
  input  _3__D0,
  input  _4__D1,
  input  _5__D2,
  input  _6__D3,
  input  _7__CEP,
  input  _10__CET,
  input  _8__GND,
  input  _9__nPE,
  output _15__TC,
  output _14__Q0,
  output _13__Q1,
  output _12__Q2,
  output _11__O3
);

  wire and_1_out, and_2_out, counter_1_carry, not_1_out, not_2_out;
  wire [3:0] multiplexer_1_out;

  not not_1 (not_1_out, _1__nMR);
  Multiplexer #(.width(4), .enable("false")) multiplexer_1 (
    .in0({_6__D3, _5__D2, _4__D1, _3__D0}), .in1(4'b0000), .out(multiplexer_1_out), .sel(not_1_out));
  and and_1 (and_1_out, _7__CEP, and_2_out, _10__CET);
  not not_2 (not_2_out, and_2_out);
  Counter #(.width(4), .max('hf)) counter_1 (
    .load(not_2_out), .D(multiplexer_1_out), .count(and_1_out), .Q({_11__O3, _12__Q2, _13__Q1, _14__Q0}),
    .carry(counter_1_carry), .clk(_2__CP));  // open: clr
  and and_2 (and_2_out, ~not_1_out, _9__nPE);  // AND_Gate
  and and_3 (_15__TC, counter_1_carry, _10__CET);

  // Notes on the sheet:
  //   74163: Synchronous 4-bit Binary Counter with Synchronous Clear 
endmodule

module _74174 (
  input  _1__MR_prime,
  input  _16__Vcc,
  input  _3__D0,
  input  _14__D5,
  input  _4__D1,
  input  _13__D4,
  input  _6__D2,
  input  _11__D3,
  input  _8__GND,
  input  _9__CP,
  output _2__Q0,
  output _15__Q5,
  output _5__Q1,
  output _12__Q4,
  output _7__Q2,
  output _10__Q3
);

  wire not_1_out;

  not not_1 (not_1_out, _1__MR_prime);
  D_Flip_Flop #(.trigger("high"), .Pre_Clr_Positions("LEGACY"), .enable("true"), .NewFFLayout("false")) d_ff_1 (
    .clk(_9__CP), .D(_3__D0), .Q(_2__Q0), .reset(not_1_out));  // open: Qn, preset, en
  D_Flip_Flop #(.trigger("high"), .Pre_Clr_Positions("LEGACY"), .enable("true"), .NewFFLayout("false")) d_ff_2 (
    .clk(_9__CP), .D(_4__D1), .Q(_5__Q1), .reset(not_1_out));  // open: Qn, preset, en
  D_Flip_Flop #(.trigger("high"), .Pre_Clr_Positions("LEGACY"), .enable("true"), .NewFFLayout("false")) d_ff_3 (
    .clk(_9__CP), .D(_6__D2), .Q(_7__Q2), .reset(not_1_out));  // open: Qn, preset, en
  D_Flip_Flop #(.trigger("high"), .Pre_Clr_Positions("LEGACY"), .enable("true"), .NewFFLayout("false")) d_ff_4 (
    .clk(_9__CP), .D(_14__D5), .Q(_15__Q5), .reset(not_1_out));  // open: Qn, preset, en
  D_Flip_Flop #(.trigger("high"), .Pre_Clr_Positions("LEGACY"), .enable("true"), .NewFFLayout("false")) d_ff_5 (
    .clk(_9__CP), .D(_13__D4), .Q(_12__Q4), .reset(not_1_out));  // open: Qn, preset, en
  D_Flip_Flop #(.trigger("high"), .Pre_Clr_Positions("LEGACY"), .enable("true"), .NewFFLayout("false")) d_ff_6 (
    .clk(_9__CP), .D(_11__D3), .Q(_10__Q3), .reset(not_1_out));  // open: Qn, preset, en

  // Notes on the sheet:
  //   74174: Hex D-type flip-flop with reset; positive-edge trigger
endmodule

module _74182 (
  input  G0,
  input  P0,
  input  Cn,
  input  G1,
  input  P1,
  input  G2,
  input  P2,
  input  G3,
  input  P3,
  input  Vcc,
  input  GND,
  output Cn_x,
  output Cn_y,
  output Cn_z,
  output G,
  output P
);

  wire and_1_out, and_2_out, and_3_out, and_4_out, and_5_out, and_6_out, and_7_out, and_8_out, and_9_out,
       and_10_out, and_11_out, and_12_out, and_13_out, not_1_out;

  nor nor_1 (Cn_x, and_2_out, and_1_out);
  and and_1 (and_1_out, G0, not_1_out);
  and and_2 (and_2_out, G0, P0);
  not not_1 (not_1_out, Cn);
  nor nor_2 (Cn_y, and_3_out, and_4_out, and_5_out);
  and and_3 (and_3_out, G1, P1);
  and and_4 (and_4_out, G0, P0, G1);
  and and_5 (and_5_out, not_1_out, G0, G1);
  nor nor_3 (Cn_z, and_6_out, and_8_out);
  and and_6 (and_6_out, G2, P2);
  and and_7 (and_7_out, G1, P1, G2);
  and and_8 (and_8_out, G0, G1);
  and and_9 (and_9_out, not_1_out, G1);
  and and_10 (and_10_out, G3, P3);
  and and_11 (and_11_out, G2, P2, G3);
  or or_1 (G, and_10_out, and_12_out);
  and and_12 (and_12_out, G1, G2);
  and and_13 (and_13_out, G0, G2);
  or or_2 (P, P0, P2);
endmodule

module _74194 (
  input  _1__nMR,
  input  _16__Vcc,
  input  _2__Dsr,
  input  _3__D0,
  input  _4__D1,
  input  _5__D2,
  input  _6__D3,
  input  _11__CP,
  input  _7__Dsl,
  input  _10__S1,
  input  _8__GND,
  input  _9__S0,
  output _154__Q0,
  output _14__Q1,
  output _13__Q2,
  output _12__Q3
);

  wire and_1_out, and_2_out, and_3_out, and_4_out, and_5_out, and_6_out, and_7_out, and_8_out, and_9_out,
       and_10_out, and_11_out, and_12_out, and_13_out, nor_1_out, not_1_out, not_2_out, not_3_out, or_1_out,
       or_2_out, or_3_out, or_4_out, or_5_out;

  not not_1 (not_1_out, _9__S0);
  not not_2 (not_2_out, _10__S1);
  nor nor_1 (nor_1_out, not_1_out, not_2_out);
  and and_1 (and_1_out, not_2_out, not_1_out);
  and and_2 (and_2_out, _7__Dsl, not_1_out);
  and and_3 (and_3_out, _6__D3, nor_1_out);
  and and_4 (and_4_out, _13__Q2, not_2_out);
  and and_5 (and_5_out, _12__Q3, not_1_out);
  and and_6 (and_6_out, _5__D2, nor_1_out);
  and and_7 (and_7_out, _14__Q1, not_2_out);
  and and_8 (and_8_out, _13__Q2, not_1_out);
  and and_9 (and_9_out, _4__D1, nor_1_out);
  and and_10 (and_10_out, _154__Q0, not_2_out);
  and and_11 (and_11_out, _14__Q1, not_1_out);
  and and_12 (and_12_out, _3__D0, nor_1_out);
  and and_13 (and_13_out, _2__Dsr, not_2_out);
  not not_3 (not_3_out, _1__nMR);
  or or_1 (or_1_out, _11__CP, and_1_out);
  or or_2 (or_2_out, and_2_out, and_3_out, and_4_out);
  or or_3 (or_3_out, and_5_out, and_6_out, and_7_out);
  or or_4 (or_4_out, and_8_out, and_9_out, and_10_out);
  or or_5 (or_5_out, and_11_out, and_12_out, and_13_out);
  D_Flip_Flop #(.Pre_Clr_Positions("LEGACY"), .enable("true"), .NewFFLayout("false")) d_ff_1 (
    .clk(or_1_out), .D(or_2_out), .Q(_12__Q3), .reset(not_3_out));  // open: Qn, preset, en
  D_Flip_Flop #(.Pre_Clr_Positions("LEGACY"), .enable("true"), .NewFFLayout("false")) d_ff_2 (
    .clk(or_1_out), .D(or_3_out), .Q(_13__Q2), .reset(not_3_out));  // open: Qn, preset, en
  D_Flip_Flop #(.Pre_Clr_Positions("LEGACY"), .enable("true"), .NewFFLayout("false")) d_ff_3 (
    .clk(or_1_out), .D(or_4_out), .Q(_14__Q1), .reset(not_3_out));  // open: Qn, preset, en
  D_Flip_Flop #(.Pre_Clr_Positions("LEGACY"), .enable("true"), .NewFFLayout("false")) d_ff_4 (
    .clk(or_1_out), .D(or_5_out), .Q(_154__Q0), .reset(not_3_out));  // open: Qn, preset, en

  // Notes on the sheet:
  //   74198: 8-bit universal shift register
endmodule

module _74198 (
  input  _1__S0,
  input  _24__Vcc,
  input  _2__Dsr,
  input  _23__S1,
  input  _3__P0,
  input  _22__Dsl,
  input  _21__P7,
  input  _5__P1,
  input  _19__P6,
  input  _7__P2,
  input  _17__P5,
  input  _9__P3,
  input  _15__P4,
  input  _11__CP,
  input  _12__GND,
  input  _13__nMR,
  output _4__Q0,
  output _20__Q7,
  output _6__Q1,
  output _18__Q6,
  output _8__Q2,
  output _16__Q5,
  output _10__Q3,
  output _14__Q4
);

  wire and_1_out, and_2_out, and_3_out, and_4_out, and_5_out, and_6_out, and_7_out, and_8_out, and_9_out,
       and_10_out, and_11_out, and_12_out, and_13_out, and_14_out, and_15_out, and_16_out, and_17_out,
       and_18_out, and_19_out, and_20_out, and_21_out, and_22_out, and_23_out, and_24_out, and_25_out,
       nor_1_out, not_1_out, not_2_out, not_3_out, or_1_out, or_2_out, or_3_out, or_4_out, or_5_out,
       or_6_out, or_7_out, or_8_out, or_9_out;

  not not_1 (not_1_out, _1__S0);
  not not_2 (not_2_out, _23__S1);
  nor nor_1 (nor_1_out, not_1_out, not_2_out);
  and and_1 (and_1_out, not_2_out, not_1_out);
  and and_2 (and_2_out, _22__Dsl, not_1_out);
  and and_3 (and_3_out, _21__P7, nor_1_out);
  and and_4 (and_4_out, _18__Q6, not_2_out);
  and and_5 (and_5_out, _20__Q7, not_1_out);
  and and_6 (and_6_out, _19__P6, nor_1_out);
  and and_7 (and_7_out, _16__Q5, not_2_out);
  and and_8 (and_8_out, _18__Q6, not_1_out);
  and and_9 (and_9_out, _17__P5, nor_1_out);
  and and_10 (and_10_out, _14__Q4, not_2_out);
  and and_11 (and_11_out, _16__Q5, not_1_out);
  and and_12 (and_12_out, _15__P4, nor_1_out);
  and and_13 (and_13_out, _10__Q3, not_2_out);
  and and_14 (and_14_out, _14__Q4, not_1_out);
  and and_15 (and_15_out, _9__P3, nor_1_out);
  and and_16 (and_16_out, _8__Q2, not_2_out);
  and and_17 (and_17_out, _10__Q3, not_1_out);
  and and_18 (and_18_out, _7__P2, nor_1_out);
  and and_19 (and_19_out, _6__Q1, not_2_out);
  and and_20 (and_20_out, _8__Q2, not_1_out);
  and and_21 (and_21_out, _5__P1, nor_1_out);
  and and_22 (and_22_out, _4__Q0, not_2_out);
  and and_23 (and_23_out, _6__Q1, not_1_out);
  and and_24 (and_24_out, _3__P0, nor_1_out);
  and and_25 (and_25_out, _2__Dsr, not_2_out);
  or or_1 (or_1_out, _11__CP, and_1_out);
  or or_2 (or_2_out, and_2_out, and_3_out, and_4_out);
  or or_3 (or_3_out, and_5_out, and_6_out, and_7_out);
  or or_4 (or_4_out, and_8_out, and_9_out, and_10_out);
  or or_5 (or_5_out, and_11_out, and_12_out, and_13_out);
  or or_6 (or_6_out, and_14_out, and_15_out, and_16_out);
  or or_7 (or_7_out, and_17_out, and_18_out, and_19_out);
  or or_8 (or_8_out, and_20_out, and_21_out, and_22_out);
  or or_9 (or_9_out, and_23_out, and_24_out, and_25_out);
  D_Flip_Flop #(.Pre_Clr_Positions("LEGACY"), .enable("true"), .NewFFLayout("false")) d_ff_1 (
    .clk(or_1_out), .D(or_2_out), .Q(_20__Q7), .reset(not_3_out));  // open: Qn, preset, en
  D_Flip_Flop #(.Pre_Clr_Positions("LEGACY"), .enable("true"), .NewFFLayout("false")) d_ff_2 (
    .clk(or_1_out), .D(or_3_out), .Q(_18__Q6), .reset(not_3_out));  // open: Qn, preset, en
  D_Flip_Flop #(.Pre_Clr_Positions("LEGACY"), .enable("true"), .NewFFLayout("false")) d_ff_3 (
    .clk(or_1_out), .D(or_4_out), .Q(_16__Q5), .reset(not_3_out));  // open: Qn, preset, en
  D_Flip_Flop #(.Pre_Clr_Positions("LEGACY"), .enable("true"), .NewFFLayout("false")) d_ff_4 (
    .clk(or_1_out), .D(or_5_out), .Q(_14__Q4), .reset(not_3_out));  // open: Qn, preset, en
  not not_3 (not_3_out, _13__nMR);
  D_Flip_Flop #(.Pre_Clr_Positions("LEGACY"), .enable("true"), .NewFFLayout("false")) d_ff_5 (
    .clk(or_1_out), .D(or_6_out), .Q(_10__Q3), .reset(not_3_out));  // open: Qn, preset, en
  D_Flip_Flop #(.Pre_Clr_Positions("LEGACY"), .enable("true"), .NewFFLayout("false")) d_ff_6 (
    .clk(or_1_out), .D(or_7_out), .Q(_8__Q2), .reset(not_3_out));  // open: Qn, preset, en
  D_Flip_Flop #(.Pre_Clr_Positions("LEGACY"), .enable("true"), .NewFFLayout("false")) d_ff_7 (
    .clk(or_1_out), .D(or_8_out), .Q(_6__Q1), .reset(not_3_out));  // open: Qn, preset, en
  D_Flip_Flop #(.Pre_Clr_Positions("LEGACY"), .enable("true"), .NewFFLayout("false")) d_ff_8 (
    .clk(or_1_out), .D(or_9_out), .Q(_4__Q0), .reset(not_3_out));  // open: Qn, preset, en

  // Notes on the sheet:
  //   74198: 8-bit universal shift register
endmodule

module _74238 (
  input  _1__A0,
  input  _16__Vcc,
  input  _2__A1,
  input  _3__A2,
  input  _4__E1_prime,
  input  _5__E2_prime,
  input  _6__E3,
  input  _8__GND,
  output _15__Y0,
  output _14__Y1,
  output _13__Y2,
  output _12__Y3,
  output _11__Y4,
  output _7__Y7,
  output _10__Y5,
  output _9__Y6
);

  wire and_1_out;

  and and_1 (and_1_out, ~_4__E1_prime, ~_5__E2_prime, _6__E3);  // AND_Gate
  Demultiplexer #(.select(3), .enable("false")) demultiplexer_1 (
    .out0(_15__Y0), .out1(_14__Y1), .out2(_13__Y2), .out3(_12__Y3), .out4(_11__Y4), .out5(_10__Y5),
    .out6(_9__Y6), .out7(_7__Y7), .in(and_1_out), .sel({_3__A2, _2__A1, _1__A0}));

  // Notes on the sheet:
  //   74238: 3-to-8 line decoder/demultiplexer; non-inverting
endmodule

module _74240 (
  input  _2__1A1,
  input  _4__1A2,
  input  _6__1A3,
  input  _8__1A4,
  input  _1__n1G,
  input  _11__2A1,
  input  _13__2A2,
  input  _15__2A3,
  input  _17__2A4,
  input  _19__n2G,
  input  _10__GND,
  input  _20__Vcc,
  output _18__1Y1,
  output _16__1Y2,
  output _14__1Y3,
  output _12__1Y4,
  output _9__2Y1,
  output _7__2Y2,
  output _5__2Y3,
  output _3__2Y4
);

  wire not_1_out, not_2_out;

  assign _18__1Y1 = not_1_out ? ~_2__1A1 : 1'bz;  // Controlled_Inverter controlled_inverter_1
  assign _16__1Y2 = not_1_out ? ~_4__1A2 : 1'bz;  // Controlled_Inverter controlled_inverter_2
  assign _14__1Y3 = not_1_out ? ~_6__1A3 : 1'bz;  // Controlled_Inverter controlled_inverter_3
  assign _12__1Y4 = not_1_out ? ~_8__1A4 : 1'bz;  // Controlled_Inverter controlled_inverter_4
  not not_1 (not_1_out, _1__n1G);
  assign _9__2Y1 = not_2_out ? ~_11__2A1 : 1'bz;  // Controlled_Inverter controlled_inverter_5
  assign _7__2Y2 = not_2_out ? ~_13__2A2 : 1'bz;  // Controlled_Inverter controlled_inverter_6
  assign _5__2Y3 = not_2_out ? ~_15__2A3 : 1'bz;  // Controlled_Inverter controlled_inverter_7
  assign _3__2Y4 = not_2_out ? ~_17__2A4 : 1'bz;  // Controlled_Inverter controlled_inverter_8
  not not_2 (not_2_out, _19__n2G);
endmodule

module _74244 (
  input  _20__Vcc,
  input  _1__E1,
  input  _2__1A0,
  input  _4__1A1,
  input  _6__1A2,
  input  _8__1A3,
  input  _19__E2,
  input  _17__2A0,
  input  _15__2A1,
  input  _13__2A2,
  input  _11__2A3,
  input  _10__GND,
  output _18__1Y0,
  output _16__1Y1,
  output _14__1Y2,
  output _12__1Y3,
  output _3__2Y0,
  output _5__2Y1,
  output _7__2Y2,
  output _9__2Y3
);

  wire not_1_out, not_2_out;

  not not_1 (not_1_out, _1__E1);
  assign _18__1Y0 = not_1_out ? _2__1A0 : 1'bz;  // Controlled_Buffer controlled_buffer_1
  assign _16__1Y1 = not_1_out ? _4__1A1 : 1'bz;  // Controlled_Buffer controlled_buffer_2
  assign _14__1Y2 = not_1_out ? _6__1A2 : 1'bz;  // Controlled_Buffer controlled_buffer_3
  assign _12__1Y3 = not_1_out ? _8__1A3 : 1'bz;  // Controlled_Buffer controlled_buffer_4
  not not_2 (not_2_out, _19__E2);
  assign _3__2Y0 = not_2_out ? _17__2A0 : 1'bz;  // Controlled_Buffer controlled_buffer_5
  assign _5__2Y1 = not_2_out ? _15__2A1 : 1'bz;  // Controlled_Buffer controlled_buffer_6
  assign _7__2Y2 = not_2_out ? _13__2A2 : 1'bz;  // Controlled_Buffer controlled_buffer_7
  assign _9__2Y3 = not_2_out ? _11__2A3 : 1'bz;  // Controlled_Buffer controlled_buffer_8
endmodule

module _74245 (
  input  _20__Vcc,
  input  _1__DIR,
  input  _2__A1,
  input  _19__nG,
  input  _3__A2,
  input  _4__A3,
  input  _5__A4,
  input  _6__A5,
  input  _7__A6,
  input  _8__A7,
  input  _9__A8,
  input  _10__GND,
  output _18___B1,
  output _17__B2,
  output _16__B3,
  output _15__B4,
  output _14__B5,
  output _13__B6,
  output _12__B7,
  output _11__B8
);

  wire and_1_out, and_2_out;

  and and_1 (and_1_out, _1__DIR, ~_19__nG);  // AND_Gate
  assign _18___B1 = and_1_out ? _2__A1 : 1'bz;  // Controlled_Buffer controlled_buffer_1
  assign _17__B2 = and_1_out ? _3__A2 : 1'bz;  // Controlled_Buffer controlled_buffer_2
  assign _16__B3 = and_1_out ? _4__A3 : 1'bz;  // Controlled_Buffer controlled_buffer_3
  assign _15__B4 = and_1_out ? _5__A4 : 1'bz;  // Controlled_Buffer controlled_buffer_4
  assign _14__B5 = and_1_out ? _6__A5 : 1'bz;  // Controlled_Buffer controlled_buffer_5
  assign _13__B6 = and_1_out ? _7__A6 : 1'bz;  // Controlled_Buffer controlled_buffer_6
  assign _12__B7 = and_1_out ? _8__A7 : 1'bz;  // Controlled_Buffer controlled_buffer_7
  assign _11__B8 = and_1_out ? _9__A8 : 1'bz;  // Controlled_Buffer controlled_buffer_8
  and and_2 (and_2_out, ~_1__DIR, ~_19__nG);  // AND_Gate
  assign _2__A1 = and_2_out ? _18___B1 : 1'bz;  // Controlled_Buffer controlled_buffer_9
  assign _3__A2 = and_2_out ? _17__B2 : 1'bz;  // Controlled_Buffer controlled_buffer_10
  assign _4__A3 = and_2_out ? _16__B3 : 1'bz;  // Controlled_Buffer controlled_buffer_11
  assign _5__A4 = and_2_out ? _15__B4 : 1'bz;  // Controlled_Buffer controlled_buffer_12
  assign _6__A5 = and_2_out ? _14__B5 : 1'bz;  // Controlled_Buffer controlled_buffer_13
  assign _7__A6 = and_2_out ? _13__B6 : 1'bz;  // Controlled_Buffer controlled_buffer_14
  assign _8__A7 = and_2_out ? _12__B7 : 1'bz;  // Controlled_Buffer controlled_buffer_15
  assign _9__A8 = and_2_out ? _11__B8 : 1'bz;  // Controlled_Buffer controlled_buffer_16
endmodule

module _74253 (
  input  _1__1G,
  input  _16__Vcc,
  input  _2__Sb,
  input  _15__2G,
  input  _3__1C3,
  input  _14__Sa,
  input  _4__1C2,
  input  _13__2C3,
  input  _5__1C1,
  input  _12__2C2,
  input  _6__1C0,
  input  _11__2C1,
  input  _10__2C0,
  input  _8__GND,
  output _7__1Y,
  output _9__2Y
);

  wire multiplexer_1_out, multiplexer_2_out, not_1_out, not_3_out;
  wire [1:0] not_4_out;

  not not_1 (not_1_out, _1__1G);
  not not_2 (not_4_out[1], _2__Sb);
  Multiplexer #(.select(2), .enable("false")) multiplexer_1 (
    .in0(_3__1C3), .in1(_4__1C2), .in2(_5__1C1), .in3(_6__1C0), .out(multiplexer_1_out), .sel(not_4_out));
  and and_1 (_7__1Y, multiplexer_1_out, not_1_out);
  Multiplexer #(.select(2), .enable("false")) multiplexer_2 (
    .in0(_13__2C3), .in1(_12__2C2), .in2(_11__2C1), .in3(_10__2C0), .out(multiplexer_2_out), .sel(not_4_out));
  not not_3 (not_3_out, _15__2G);
  not not_4 (not_4_out[0], _14__Sa);
  and and_2 (_9__2Y, multiplexer_2_out, not_3_out);

  // Notes on the sheet:
  //   74253: Dual 4-Lin to 1-Line Multiplexer
endmodule

module _74260 (
  input  _1__1A,
  input  _14__Vcc,
  input  _2__1B,
  input  _13__2D,
  input  _3__1E,
  input  _12__2C,
  input  _4__1C,
  input  _11__2E,
  input  _5__1D,
  input  _10__2B,
  input  _9__2A,
  input  _7__GND,
  output _6__1Y,
  output _8__2Y
);

  nor nor_1 (_6__1Y, _4__1C, _2__1B);
  nor nor_2 (_8__2Y, _12__2C, _10__2B);

  // Notes on the sheet:
  //   74260: dual 5-input NOR
endmodule

module _74273 (
  input  D0_3,
  input  D1_4,
  input  D2_7,
  input  D3_8,
  input  D4_13,
  input  D5_14,
  input  D6_17,
  input  D7_18,
  input  nMR_1,
  input  CLK_11,
  input  Vcc_20,
  input  GND_10,
  output Q0_2,
  output Q1_5,
  output Q2_6,
  output Q3_9,
  output Q4_12,
  output Q5_15,
  output Q6_16,
  output Q7_19
);

  wire not_1_out;

  not not_1 (not_1_out, nMR_1);
  Register register_1 (
    .D({D7_18, D6_17, D5_14, D4_13, D3_8, D2_7, D1_4, D0_3}),
    .Q({Q7_19, Q6_16, Q5_15, Q4_12, Q3_9, Q2_6, Q1_5, Q0_2}), .clk(CLK_11), .clr(not_1_out));  // open: en
endmodule

module _74283 (
  input  _7__C0,
  input  _5__A1,
  input  _6__B1,
  input  _3__A2,
  input  _2__B2,
  input  _14__A3,
  input  _15__B3,
  input  _12__A4,
  input  _11__B4,
  input  _16__Vcc,
  input  _8__GND,
  output _4__S1,
  output _1__S2,
  output _13__S3,
  output _10__S4,
  output _9__C4
);

  wire _2_out, _3_out, _5_out, _6_p5, _7_out, _9_out, _10_p6, _11_p6, _12_out, _14_out, _15_out, _16_p8,
       _17_p6, _18_out, buffer_1_out, buffer_2_out, buffer_3_out, buffer_4_out, nand_1_out, nand_2_out,
       nand_3_out, nand_4_out, nor_1_out, nor_2_out, nor_3_out, nor_4_out, nor_5_out, nor_6_p4, nor_7_p5,
       not_1_out, not_2_out;

  not not_1 (not_1_out, _7__C0);
  // NOR_Gate nor_1 has open pins: out=nor_1_out
  // NAND_Gate nand_1 has open pins: out=nand_1_out
  // NOR_Gate nor_2 has open pins: out=nor_2_out
  // NAND_Gate nand_2 has open pins: out=nand_2_out
  // NOR_Gate nor_3 has open pins: out=nor_3_out
  // NAND_Gate nand_3 has open pins: out=nand_3_out
  // NOR_Gate nor_4 has open pins: out=nor_4_out
  // NAND_Gate nand_4 has open pins: out=nand_4_out
  not not_2 (not_2_out, not_1_out);
  // AND_Gate _2 has open pins: out=_2_out
  // AND_Gate _3 has open pins: out=_3_out
  buf buffer_1 (buffer_1_out, nor_1_out);
  // AND_Gate _5 has open pins: out=_5_out
  // AND_Gate _6: pin names not known; wires that end beside it: not_1_out, nand_1_out, nand_2_out, nand_2_out, _6_p5
  // AND_Gate _7 has open pins: out=_7_out
  buf buffer_2 (buffer_2_out, nor_2_out);
  // AND_Gate _9 has open pins: out=_9_out
  // AND_Gate _10: pin names not known; wires that end beside it: not_1_out, nand_1_out, nand_2_out, nand_3_out, nand_2_out, _10_p6
  // AND_Gate _11: pin names not known; wires that end beside it: nand_3_out, nand_2_out, nand_3_out, nor_1_out, nand_3_out, _11_p6
  // AND_Gate _12 has open pins: out=_12_out
  buf buffer_3 (buffer_3_out, nor_3_out);
  // AND_Gate _14 has open pins: out=_14_out
  // AND_Gate _15 has open pins: out=_15_out
  // AND_Gate _16: pin names not known; wires that end beside it: nand_3_out, nand_4_out, nand_2_out, nand_3_out, nand_4_out, nor_1_out, nand_3_out, _16_p8
  // AND_Gate _17: pin names not known; wires that end beside it: nor_1_out, nand_3_out, nand_4_out, nor_2_out, nand_4_out, _17_p6
  // AND_Gate _18 has open pins: out=_18_out
  buf buffer_4 (buffer_4_out, nor_4_out);
  // NOR_Gate nor_5 has open pins: out=nor_5_out
  // NOR_Gate nor_6: pin names not known; wires that end beside it: _6_p5, _7_out, buffer_2_out, nor_6_p4
  // NOR_Gate nor_7: pin names not known; wires that end beside it: _10_p6, _11_p6, _12_out, buffer_3_out, nor_7_p5
  // NOR_Gate nor_8 has open pins: out=_9__C4
  // XOR_Gate xor_1 has open pins: out=_4__S1
  // XOR_Gate xor_2 has open pins: out=_1__S2
  // XOR_Gate xor_3 has open pins: out=_13__S3
  // XOR_Gate xor_4 has open pins: out=_10__S4
endmodule

module _74371 (
  input  _1__AD_A,
  input  _20__Vcc,
  input  _2__AD_B,
  input  _19__AD_H,
  input  _3__AD_C,
  input  _18__AD_G,
  input  _4__AD_D,
  input  _17__AD_F,
  input  _5__AD_E,
  input  _16__nS_2,
  input  _6__DO_1,
  input  _15__nS_1,
  input  _7__DO_2,
  input  _14__DO_8,
  input  _8__DO_3,
  input  _13__DO_7,
  input  _9__DO_4,
  input  _12__DO_6,
  input  _10__GND,
  input  _11__DO_5
);

  wire or_1_out;

  or or_1 (or_1_out, _16__nS_2, _15__nS_1);
  ROM rom_1 (
    .addr({_19__AD_H, _18__AD_G, _17__AD_F, _5__AD_E, _4__AD_D, _3__AD_C, _2__AD_B, _1__AD_A}),
    .data({_14__DO_8, _13__DO_7, _12__DO_6, _11__DO_5, _9__DO_4, _8__DO_3, _7__DO_2, _6__DO_1}),
    .sel(or_1_out));

  // Notes on the sheet:
  //   74371: 2048-bit ROM, 256x8
endmodule

module _74374 (
  input  Vcc__20,
  input  D0__2,
  input  D1__3,
  input  D2__4,
  input  D3__5,
  input  D4__6,
  input  D5__7,
  input  D6__8,
  input  D7__9,
  input  nOE__1,
  input  CLK__11,
  input  GND__10,
  output Q0__19,
  output Q1__18,
  output Q2__17,
  output Q3__16,
  output Q4__15,
  output Q5__14,
  output Q6__13,
  output Q7__12
);

  wire not_1_out;
  wire [7:0] register_1_q;

  not not_1 (not_1_out, nOE__1);
  Register register_1 (
    .D({D7__9, D6__8, D5__7, D4__6, D3__5, D2__4, D1__3, D0__2}), .en(not_1_out), .Q(register_1_q),
    .clk(CLK__11));  // open: clr
  assign {Q7__12, Q6__13, Q5__14, Q4__15, Q3__16, Q2__17, Q1__18, Q0__19} = not_1_out ? register_1_q : 8'bz;  // Controlled_Buffer controlled_buffer_1
endmodule

module _74381 (
  input  Cin,
  input  B0,
  input  A0,
  input  B1,
  input  A1,
  input  B2,
  input  A2,
  input  B3,
  input  Vcc,
  input  GND,
  input  A3,
  input  F0,
  input  F1,
  input  F2,
  output C0,
  output C1,
  output C2,
  output C3,
  output nP,
  output nG
);

  wire and_1_out, and_2_out, and_3_out, and_4_out, and_5_out, and_6_out, and_7_out, and_8_out, and_9_out,
       and_10_out, and_11_out, and_12_out, and_13_out, and_14_out, and_15_out, and_16_out, and_17_out,
       and_18_out, and_19_out, and_20_out, and_21_out, and_22_out, and_23_out, and_24_out, and_25_out,
       and_26_out, and_27_out, and_28_out, and_29_out, and_30_out, and_31_out, and_32_out, and_33_out,
       and_34_out, and_35_out, and_36_out, and_37_out, and_38_out, and_39_out, and_40_out, and_41_out,
       and_42_out, and_43_out, and_44_out, nand_1_out, nand_2_out, nand_3_out, nand_4_out, nand_5_out,
       nor_1_out, nor_2_out, nor_3_out, nor_4_out, nor_5_out, nor_6_out, nor_7_out, nor_8_out, nor_9_out,
       nor_10_out, nor_11_out, nor_12_out, nor_13_out, not_1_out, not_2_out, not_3_out, not_4_out, not_5_out,
       not_6_out, not_7_out, not_8_out, not_9_out, not_10_out, not_11_out, not_12_out, not_13_out, not_14_out;

  not not_1 (not_1_out, F0);
  not not_2 (not_2_out, F1);
  not not_3 (not_3_out, F2);
  not not_4 (not_4_out, B0);
  not not_5 (not_5_out, A0);
  not not_6 (not_6_out, B1);
  not not_7 (not_7_out, A1);
  not not_8 (not_8_out, B2);
  not not_9 (not_9_out, A2);
  not not_10 (not_10_out, B3);
  not not_11 (not_11_out, A3);
  not not_12 (not_12_out, not_1_out);
  not not_13 (not_13_out, not_2_out);
  not not_14 (not_14_out, not_3_out);
  nand nand_1 (nand_1_out, not_1_out, not_2_out);
  nand nand_2 (nand_2_out, not_2_out, not_3_out);
  and and_1 (and_1_out, not_5_out, not_4_out, nand_3_out, nand_2_out);
  and and_2 (and_2_out, nand_1_out, nand_3_out, nand_4_out, not_4_out, A0);
  and and_3 (and_3_out, nand_2_out, nand_4_out, B0, not_5_out);
  and and_4 (and_4_out, not_5_out, not_4_out, nand_1_out, nand_4_out, nor_10_out);
  and and_5 (and_5_out, nand_2_out, nand_3_out, not_4_out, A0);
  and and_6 (and_6_out, nand_2_out, nand_3_out, B0, not_5_out);
  and and_7 (and_7_out, nand_1_out, nand_4_out, B0, A0);
  and and_8 (and_8_out, not_7_out, not_6_out, nand_3_out, nand_2_out);
  and and_9 (and_9_out, nand_1_out, nand_3_out, nand_4_out, not_6_out, A1);
  and and_10 (and_10_out, nand_2_out, nand_4_out, B1, not_7_out);
  and and_11 (and_11_out, not_7_out, not_6_out, nand_1_out, nand_4_out, nor_10_out);
  and and_12 (and_12_out, nand_2_out, nand_3_out, not_6_out, A1);
  and and_13 (and_13_out, nand_2_out, nand_3_out, B1, not_7_out);
  and and_14 (and_14_out, nand_1_out, nand_4_out, B1, A1);
  and and_15 (and_15_out, not_9_out, not_8_out, nand_3_out, nand_2_out);
  and and_16 (and_16_out, nand_1_out, nand_3_out, nand_4_out, not_8_out, A2);
  and and_17 (and_17_out, nand_2_out, nand_4_out, B2, not_9_out);
  and and_18 (and_18_out, not_9_out, not_8_out, nand_1_out, nand_4_out, nor_10_out);
  and and_19 (and_19_out, nand_2_out, nand_3_out, not_8_out, A2);
  and and_20 (and_20_out, nand_2_out, nand_3_out, B2, not_9_out);
  and and_21 (and_21_out, nand_1_out, nand_4_out, B2, A2);
  and and_22 (and_22_out, not_11_out, not_10_out, nand_3_out, nand_2_out);
  and and_23 (and_23_out, nand_1_out, nand_3_out, nand_4_out, not_10_out, A3);
  and and_24 (and_24_out, nand_2_out, nand_4_out, B3, not_11_out);
  and and_25 (and_25_out, not_11_out, not_10_out, nand_1_out, nand_4_out, nor_10_out);
  and and_26 (and_26_out, nand_2_out, nand_3_out, not_10_out, A3);
  and and_27 (and_27_out, nand_2_out, nand_3_out, B3, not_11_out);
  and and_28 (and_28_out, nand_1_out, nand_4_out, B3, A3);
  nand nand_3 (nand_3_out, not_1_out, not_13_out);
  nand nand_4 (nand_4_out, not_12_out, not_13_out, not_3_out);
  and and_29 (and_29_out, not_2_out, not_1_out);
  and and_30 (and_30_out, not_1_out, not_14_out);
  and and_31 (and_31_out, not_2_out, not_14_out);
  nor nor_1 (nor_1_out, and_1_out, and_2_out, and_3_out);
  nor nor_2 (nor_2_out, and_4_out, and_5_out, and_6_out, and_7_out);
  nor nor_3 (nor_3_out, and_8_out, and_9_out, and_10_out);
  nor nor_4 (nor_4_out, and_11_out, and_12_out, and_13_out, and_14_out);
  nor nor_5 (nor_5_out, and_15_out, and_16_out, and_17_out);
  nor nor_6 (nor_6_out, and_18_out, and_19_out, and_20_out, and_21_out);
  nor nor_7 (nor_7_out, and_22_out, and_23_out, and_24_out);
  nor nor_8 (nor_8_out, and_25_out, and_26_out, and_27_out, and_28_out);
  nor nor_9 (nor_9_out, and_29_out, not_14_out);
  nor nor_10 (nor_10_out, and_30_out, and_31_out);
  nand nand_5 (nand_5_out, Cin, nor_9_out);
  and and_32 (and_32_out, Cin, nor_1_out, nor_9_out);
  and and_33 (and_33_out, nor_1_out, nor_2_out, nor_9_out);
  and and_34 (and_34_out, Cin, nor_1_out, nor_3_out, nor_9_out);
  and and_35 (and_35_out, nor_1_out, nor_3_out, nor_2_out, nor_9_out);
  and and_36 (and_36_out, nor_3_out, nor_4_out, nor_9_out);
  and and_37 (and_37_out, Cin, nor_1_out, nor_3_out, nor_5_out, nor_9_out);
  and and_38 (and_38_out, nor_1_out, nor_3_out, nor_5_out, nor_2_out, nor_9_out);
  and and_39 (and_39_out, nor_3_out, nor_5_out, nor_4_out, nor_9_out);
  and and_40 (and_40_out, nor_5_out, nor_6_out, nor_9_out);
  nand nand_6 (nP, nor_1_out, nor_3_out, nor_5_out, nor_7_out);
  and and_41 (and_41_out, nor_1_out, nor_3_out, nor_5_out, nor_7_out, nor_2_out);
  and and_42 (and_42_out, nor_3_out, nor_5_out, nor_7_out, nor_4_out);
  and and_43 (and_43_out, nor_5_out, nor_7_out, nor_6_out);
  and and_44 (and_44_out, nor_7_out, nor_8_out);
  nor nor_11 (nor_11_out, and_32_out, and_33_out);
  nor nor_12 (nor_12_out, and_34_out, and_35_out, and_36_out);
  nor nor_13 (nor_13_out, and_37_out, and_38_out, and_39_out, and_40_out);
  nor nor_14 (nG, and_41_out, and_42_out, and_43_out, and_44_out);
  xor xor_1 (C0, nand_5_out, nor_2_out);
  xor xor_2 (C1, nor_11_out, nor_4_out);
  xor xor_3 (C2, nor_12_out, nor_6_out);
  xor xor_4 (C3, nor_13_out, nor_8_out);
endmodule

module _74382 (
  input  Cin,
  input  B0,
  input  A0,
  input  B1,
  input  A1,
  input  B2,
  input  A2,
  input  B3,
  input  Vcc,
  input  GND,
  input  A3,
  input  F0,
  input  F1,
  input  F2,
  output C0,
  output C1,
  output C2,
  output C3,
  output OVR,
  output Cout
);

  wire and_1_out, and_2_out, and_3_out, and_4_out, and_5_out, and_6_out, and_7_out, and_8_out, and_9_out,
       and_10_out, and_11_out, and_12_out, and_13_out, and_14_out, and_15_out, and_16_out, and_17_out,
       and_18_out, and_19_out, and_20_out, and_21_out, and_22_out, and_23_out, and_24_out, and_25_out,
       and_26_out, and_27_out, and_28_out, and_29_out, and_30_out, and_31_out, and_32_out, and_33_out,
       and_34_out, and_35_out, and_36_out, and_37_out, and_38_out, and_39_out, and_40_out, and_41_out,
       and_42_out, and_43_out, and_44_out, and_45_out, nand_1_out, nand_2_out, nand_3_out, nand_4_out,
       nand_5_out, nand_6_out, nor_1_out, nor_2_out, nor_3_out, nor_4_out, nor_5_out, nor_6_out, nor_7_out,
       nor_8_out, nor_9_out, nor_10_out, nor_11_out, nor_12_out, nor_13_out, nor_14_out, not_1_out,
       not_2_out, not_3_out, not_4_out, not_5_out, not_6_out, not_8_out, not_9_out, not_10_out, not_11_out,
       not_12_out, not_13_out, not_14_out;

  not not_1 (not_1_out, F0);
  not not_2 (not_2_out, F1);
  not not_3 (not_3_out, F2);
  not not_4 (not_4_out, B0);
  not not_5 (not_5_out, A0);
  not not_6 (not_6_out, B1);
  not not_7 (not_6_out, A1);
  not not_8 (not_8_out, B2);
  not not_9 (not_9_out, A2);
  not not_10 (not_10_out, B3);
  not not_11 (not_11_out, A3);
  not not_12 (not_12_out, not_1_out);
  not not_13 (not_13_out, not_2_out);
  not not_14 (not_14_out, not_3_out);
  nand nand_1 (nand_1_out, not_1_out, not_2_out);
  nand nand_2 (nand_2_out, not_2_out, not_3_out);
  and and_1 (and_1_out, not_5_out, not_4_out, nand_3_out, nand_2_out);
  and and_2 (and_2_out, nand_1_out, nand_3_out, nand_4_out, not_4_out);
  and and_3 (and_3_out, nand_2_out, nand_4_out, B0, not_5_out);
  and and_4 (and_4_out, not_5_out, not_4_out, nand_1_out, nand_4_out, nor_10_out);
  and and_5 (and_5_out, nand_2_out, nand_3_out, not_4_out, A0);
  and and_6 (and_6_out, nand_2_out, nand_3_out, B0, not_5_out);
  and and_7 (and_7_out, nand_1_out, nand_4_out, B0, A0);
  and and_8 (and_8_out, not_6_out, not_6_out, nand_3_out, nand_2_out);
  and and_9 (and_9_out, nand_1_out, nand_3_out, nand_4_out, not_6_out, A1);
  and and_10 (and_10_out, nand_2_out, nand_4_out, B1, not_6_out);
  and and_11 (and_11_out, not_6_out, not_6_out, nand_1_out, nand_4_out, nor_10_out);
  and and_12 (and_12_out, nand_2_out, nand_3_out, not_6_out, A1);
  and and_13 (and_13_out, nand_2_out, nand_3_out, B1, not_6_out);
  and and_14 (and_14_out, nand_1_out, nand_4_out, B1, A1);
  and and_15 (and_15_out, not_9_out, not_8_out, nand_3_out, nand_2_out);
  and and_16 (and_16_out, nand_1_out, nand_3_out, nand_4_out, not_8_out, A2);
  and and_17 (and_17_out, nand_2_out, nand_4_out, B2, not_9_out);
  and and_18 (and_18_out, not_9_out, not_8_out, nand_1_out, nand_4_out, nor_10_out);
  and and_19 (and_19_out, nand_2_out, nand_3_out, not_8_out, A2);
  and and_20 (and_20_out, nand_2_out, nand_3_out, B2, not_9_out);
  and and_21 (and_21_out, nand_1_out, nand_4_out, B2, A2);
  and and_22 (and_22_out, not_11_out, not_10_out, nand_3_out, nand_2_out);
  and and_23 (and_23_out, nand_1_out, nand_3_out, nand_4_out, not_10_out, A3);
  and and_24 (and_24_out, nand_2_out, nand_4_out, B3, not_11_out);
  and and_25 (and_25_out, not_11_out, not_10_out, nand_1_out, nand_4_out, nor_10_out);
  and and_26 (and_26_out, nand_2_out, nand_3_out, not_10_out, A3);
  and and_27 (and_27_out, nand_2_out, nand_3_out, B3, not_11_out);
  and and_28 (and_28_out, nand_1_out, nand_4_out, B3, A3);
  nand nand_3 (nand_3_out, not_1_out, not_13_out);
  nand nand_4 (nand_4_out, not_12_out, not_13_out, not_3_out);
  and and_29 (and_29_out, not_2_out, not_1_out);
  and and_30 (and_30_out, not_1_out, not_14_out);
  and and_31 (and_31_out, not_2_out, not_14_out);
  nor nor_1 (nor_1_out, and_1_out, and_2_out, and_3_out);
  nor nor_2 (nor_2_out, and_4_out, and_5_out, and_6_out, and_7_out);
  nor nor_3 (nor_3_out, and_8_out, and_9_out, and_10_out);
  nor nor_4 (nor_4_out, and_11_out, and_12_out, and_13_out, and_14_out);
  nor nor_5 (nor_5_out, and_15_out, and_16_out, and_17_out);
  nor nor_6 (nor_6_out, and_18_out, and_19_out, and_20_out, and_21_out);
  nor nor_7 (nor_7_out, and_22_out, and_23_out, and_24_out);
  nor nor_8 (nor_8_out, and_25_out, and_26_out, and_27_out, and_28_out);
  nor nor_9 (nor_9_out, and_29_out, not_14_out);
  nor nor_10 (nor_10_out, and_30_out, and_31_out);
  nand nand_5 (nand_5_out, Cin, nor_9_out);
  and and_32 (and_32_out, Cin, nor_1_out, nor_9_out);
  and and_33 (and_33_out, nor_1_out, nor_2_out, nor_9_out);
  and and_34 (and_34_out, Cin, nor_1_out, nor_3_out, nor_9_out);
  and and_35 (and_35_out, nor_1_out, nor_3_out, nor_2_out, nor_9_out);
  and and_36 (and_36_out, nor_3_out, nor_4_out, nor_9_out);
  and and_37 (and_37_out, Cin, nor_1_out, nor_3_out, nor_5_out, nor_9_out);
  and and_38 (and_38_out, nor_1_out, nor_3_out, nor_5_out, nor_2_out, nor_9_out);
  and and_39 (and_39_out, nor_3_out, nor_5_out, nor_4_out, nor_9_out);
  and and_40 (and_40_out, nor_5_out, nor_6_out, nor_6_out);
  and and_41 (and_41_out, nor_1_out, nor_3_out, nor_5_out, nor_7_out, nor_2_out);
  and and_42 (and_42_out, nor_3_out, nor_5_out, nor_7_out, nor_4_out);
  and and_43 (and_43_out, nor_5_out, nor_7_out, nor_6_out);
  and and_44 (and_44_out, nor_7_out, nor_8_out);
  nand nand_6 (nand_6_out, Cin, nor_1_out, nor_3_out, nor_5_out, nor_7_out);
  nor nor_11 (nor_11_out, and_32_out, and_33_out);
  nor nor_12 (nor_12_out, and_34_out, and_35_out, and_36_out);
  nor nor_13 (nor_13_out, and_37_out, and_38_out, and_39_out, and_40_out);
  nor nor_14 (nor_14_out, and_41_out, and_42_out, and_43_out, and_44_out);
  and and_45 (and_45_out, nor_14_out, nand_6_out);
  nand nand_7 (Cout, nor_14_out, nand_6_out);
  xor xor_1 (C0, nand_5_out, nor_2_out);
  xor xor_2 (C1, nor_11_out, nor_4_out);
  xor xor_3 (C2, nor_12_out, nor_6_out);
  xor xor_4 (C3, nor_13_out, nor_8_out);
  xor xor_5 (OVR, nor_13_out, and_45_out);
endmodule

module _74521 (
  input  _2__A0,
  input  _3__B0,
  input  _4__A1,
  input  _5__B1,
  input  _6__A2,
  input  _7__B2,
  input  _8__A3,
  input  _9__B3,
  input  _11__A4,
  input  _12__B4,
  input  _13__A5,
  input  _14__B5,
  input  _15__A6,
  input  _16__B6,
  input  _17__A7,
  input  _18__B7,
  input  _1__nI__A_B,
  input  _10__GND,
  input  _20__Vcc,
  output _19__nO__A_B
);

  wire not_1_out, not_2_out, not_3_out, not_4_out, not_5_out, not_6_out, not_7_out, not_8_out, not_9_out,
       not_10_out, not_11_out, not_12_out, not_13_out, not_14_out, not_15_out, not_16_out, not_17_out,
       xnor_1_out, xnor_2_out, xnor_3_out, xnor_4_out, xnor_5_out, xnor_6_out, xnor_7_out, xnor_8_out;

  not not_1 (not_1_out, _2__A0);
  not not_2 (not_2_out, _3__B0);
  not not_3 (not_3_out, _4__A1);
  not not_4 (not_4_out, _5__B1);
  not not_5 (not_5_out, _6__A2);
  not not_6 (not_6_out, _7__B2);
  not not_7 (not_7_out, _8__A3);
  not not_8 (not_8_out, _9__B3);
  not not_9 (not_9_out, _11__A4);
  not not_10 (not_10_out, _12__B4);
  not not_11 (not_11_out, _13__A5);
  not not_12 (not_12_out, _14__B5);
  not not_13 (not_13_out, _15__A6);
  not not_14 (not_14_out, _16__B6);
  not not_15 (not_15_out, _17__A7);
  not not_16 (not_16_out, _18__B7);
  not not_17 (not_17_out, _1__nI__A_B);
  xnor xnor_1 (xnor_1_out, not_1_out, not_2_out);
  xnor xnor_2 (xnor_2_out, not_3_out, not_4_out);
  xnor xnor_3 (xnor_3_out, not_5_out, not_6_out);
  xnor xnor_4 (xnor_4_out, not_7_out, not_8_out);
  xnor xnor_5 (xnor_5_out, not_9_out, not_10_out);
  xnor xnor_6 (xnor_6_out, not_11_out, not_12_out);
  xnor xnor_7 (xnor_7_out, not_13_out, not_14_out);
  xnor xnor_8 (xnor_8_out, not_15_out, not_16_out);
  nand nand_1 (_19__nO__A_B, xnor_1_out, xnor_2_out, xnor_3_out, xnor_4_out, xnor_5_out, xnor_6_out, xnor_7_out, xnor_8_out, not_17_out);
endmodule

module _74540 (
  input  _20__Vcc,
  input  _1__E1,
  input  _2__A1,
  input  _19__E2,
  input  _3__A2,
  input  _4__A3,
  input  _5__A4,
  input  _6__A5,
  input  _7__A6,
  input  _8__A7,
  input  _9__A8,
  input  _10__GND,
  output _18___B1,
  output _17__B2,
  output _16__B3,
  output _15__B4,
  output _14__B5,
  output _13__B6,
  output _12__B7,
  output _11__B8
);

  wire and_1_out;

  and and_1 (and_1_out, ~_19__E2, ~_1__E1);  // AND_Gate
  assign _18___B1 = and_1_out ? ~_2__A1 : 1'bz;  // Controlled_Inverter controlled_inverter_1
  assign _17__B2 = and_1_out ? ~_3__A2 : 1'bz;  // Controlled_Inverter controlled_inverter_2
  assign _16__B3 = and_1_out ? ~_4__A3 : 1'bz;  // Controlled_Inverter controlled_inverter_3
  assign _15__B4 = and_1_out ? ~_5__A4 : 1'bz;  // Controlled_Inverter controlled_inverter_4
  assign _14__B5 = and_1_out ? ~_6__A5 : 1'bz;  // Controlled_Inverter controlled_inverter_5
  assign _13__B6 = and_1_out ? ~_7__A6 : 1'bz;  // Controlled_Inverter controlled_inverter_6
  assign _12__B7 = and_1_out ? ~_8__A7 : 1'bz;  // Controlled_Inverter controlled_inverter_7
  assign _11__B8 = and_1_out ? ~_9__A8 : 1'bz;  // Controlled_Inverter controlled_inverter_8
endmodule

module _74541 (
  input  _20__Vcc,
  input  _1__E1,
  input  _2__A1,
  input  _19__E2,
  input  _3__A2,
  input  _4__A3,
  input  _5__A4,
  input  _6__A5,
  input  _7__A6,
  input  _8__A7,
  input  _9__A8,
  input  _10__GND,
  output _18___B1,
  output _17__B2,
  output _16__B3,
  output _15__B4,
  output _14__B5,
  output _13__B6,
  output _12__B7,
  output _11__B8
);

  wire and_1_out;

  and and_1 (and_1_out, ~_19__E2, ~_1__E1);  // AND_Gate
  assign _18___B1 = and_1_out ? _2__A1 : 1'bz;  // Controlled_Buffer controlled_buffer_1
  assign _17__B2 = and_1_out ? _3__A2 : 1'bz;  // Controlled_Buffer controlled_buffer_2
  assign _16__B3 = and_1_out ? _4__A3 : 1'bz;  // Controlled_Buffer controlled_buffer_3
  assign _15__B4 = and_1_out ? _5__A4 : 1'bz;  // Controlled_Buffer controlled_buffer_4
  assign _14__B5 = and_1_out ? _6__A5 : 1'bz;  // Controlled_Buffer controlled_buffer_5
  assign _13__B6 = and_1_out ? _7__A6 : 1'bz;  // Controlled_Buffer controlled_buffer_6
  assign _12__B7 = and_1_out ? _8__A7 : 1'bz;  // Controlled_Buffer controlled_buffer_7
  assign _11__B8 = and_1_out ? _9__A8 : 1'bz;  // Controlled_Buffer controlled_buffer_8
endmodule

module _74574 (
  input  Vcc__20,
  input  D0__2,
  input  D1__3,
  input  D2__4,
  input  D3__5,
  input  D4__6,
  input  D5__7,
  input  D6__8,
  input  D7__9,
  input  nOE__1,
  input  CLK__11,
  input  GND__10,
  output Q0__19,
  output Q1__18,
  output Q2__17,
  output Q3__16,
  output Q4__15,
  output Q5__14,
  output Q6__13,
  output Q7__12
);

  wire not_1_out;
  wire [7:0] register_1_q;

  not not_1 (not_1_out, nOE__1);
  Register register_1 (
    .D({D7__9, D6__8, D5__7, D4__6, D3__5, D2__4, D1__3, D0__2}), .Q(register_1_q), .clk(CLK__11));  // open: en, clr
  assign {Q7__12, Q6__13, Q5__14, Q4__15, Q3__16, Q2__17, Q1__18, Q0__19} = not_1_out ? register_1_q : 8'bz;  // Controlled_Buffer controlled_buffer_1
endmodule

module _74682 (
  input  _20__Vcc,
  input  _2__A0,
  input  _3__B0,
  input  _18__B7,
  input  _4__A1,
  input  _17__A7,
  input  _5__B1,
  input  _16__B6,
  input  _6__A2,
  input  _15__A6,
  input  _7__B2,
  input  _14__B5,
  input  _8__A3,
  input  _13__A5,
  input  _9__B3,
  input  _12__B4,
  input  _10__GND,
  input  _11__A4,
  output _1__A___B,
  output _19__A___B
);

  wire and_1_out, and_2_out, and_3_out, and_4_out, and_5_out, and_6_out, and_7_out, and_8_out, not_1_out,
       not_2_out, not_3_out, not_4_out, not_5_out, not_6_out, not_7_out, not_8_out, not_9_out, not_10_out,
       not_11_out, not_12_out, not_13_out, not_14_out, not_15_out, not_16_out, not_17_out, not_18_out,
       not_19_out, not_20_out, not_21_out, not_22_out, not_23_out, not_24_out, xnor_1_out, xnor_3_out,
       xnor_4_out, xnor_5_out, xnor_6_out, xnor_8_out;

  not not_1 (not_1_out, _2__A0);
  not not_2 (not_2_out, _3__B0);
  not not_3 (not_3_out, _4__A1);
  not not_4 (not_4_out, _5__B1);
  not not_5 (not_5_out, _6__A2);
  not not_6 (not_6_out, _7__B2);
  not not_7 (not_7_out, _8__A3);
  not not_8 (not_8_out, _9__B3);
  not not_9 (not_9_out, _11__A4);
  not not_10 (not_10_out, _12__B4);
  not not_11 (not_11_out, _13__A5);
  not not_12 (not_12_out, _14__B5);
  not not_13 (not_13_out, _15__A6);
  not not_14 (not_14_out, _16__B6);
  not not_15 (not_15_out, _17__A7);
  not not_16 (not_16_out, _18__B7);
  xnor xnor_1 (xnor_1_out, not_1_out, not_2_out);
  xnor xnor_2 (not_16_out, not_3_out, not_4_out);
  xnor xnor_3 (xnor_3_out, not_5_out, not_6_out);
  xnor xnor_4 (xnor_4_out, not_7_out, not_8_out);
  xnor xnor_5 (xnor_5_out, not_9_out, not_10_out);
  xnor xnor_6 (xnor_6_out, not_11_out, not_12_out);
  xnor xnor_7 (xnor_4_out, not_13_out, not_14_out);
  xnor xnor_8 (xnor_8_out, not_15_out, not_16_out);
  not not_17 (not_17_out, not_15_out);
  not not_18 (not_18_out, not_13_out);
  not not_19 (not_19_out, not_11_out);
  not not_20 (not_20_out, not_9_out);
  not not_21 (not_21_out, not_7_out);
  not not_22 (not_22_out, not_5_out);
  not not_23 (not_23_out, not_3_out);
  not not_24 (not_24_out, not_1_out);
  and and_1 (and_1_out, xnor_1_out, not_16_out, xnor_3_out, xnor_4_out, xnor_5_out, xnor_6_out, xnor_4_out, not_16_out, not_17_out);
  and and_2 (and_2_out, xnor_1_out, not_16_out, xnor_3_out, xnor_4_out, xnor_5_out, xnor_6_out, not_14_out, not_18_out);
  and and_3 (and_3_out, xnor_1_out, not_16_out, xnor_3_out, xnor_4_out, xnor_5_out, not_12_out, not_19_out);
  and and_4 (and_4_out, xnor_1_out, not_16_out, xnor_3_out, xnor_4_out, not_10_out, not_20_out);
  and and_5 (and_5_out, not_16_out, not_8_out);
  buf and_6 (and_6_out, not_16_out);  // AND_Gate
  and and_7 (and_7_out, xnor_1_out, not_4_out, not_23_out);
  and and_8 (and_8_out, not_2_out, not_24_out);
  nand nand_1 (_19__A___B, xnor_1_out, not_16_out, xnor_3_out, xnor_4_out, xnor_5_out, xnor_6_out, xnor_4_out, xnor_8_out);
  nor nor_1 (_1__A___B, and_1_out, and_2_out, and_3_out, and_4_out, and_5_out, and_6_out, and_7_out, and_8_out);

  // Notes on the sheet:
  //   74682: 8-bit magnitude comparator 
endmodule

module _744075 (
  input  _1__1A,
  input  _14__Vcc,
  input  _2__1B,
  input  _13__1C,
  input  _3__2A,
  input  _4__2B,
  input  _11__3C,
  input  _5__2C,
  input  _10__3B,
  input  _9__3A,
  input  _7__GND,
  output _12__1Y,
  output _6__2Y,
  output _8__3Y
);

  or or_1 (_6__2Y, _5__2C, _4__2B, _3__2A);
  or or_2 (_12__1Y, _2__1B, _1__1A, _13__1C);
  or or_3 (_8__3Y, _11__3C, _10__3B, _9__3A);

  // Notes on the sheet:
  //   744075: triple 3-input OR 
endmodule

module test (
  input  in_1,
  input  in_2,
  input  in_3,
  input  in_4,
  input  in_5,
  input  in_6,
  input  in_7,
  input  in_8,
  input  in_9,
  input  in_10,
  input  in_11,
  input  in_12,
  output out_13,
  output out_14,
  output out_15,
  output out_16,
  output out_17,
  output out_18
);

  _74382 u_74382_1 (
    .Cin(in_9), .A0(in_2), .B0(in_6), .A1(in_1), .B1(in_5), .A2(in_3), .B2(in_7), .A3(in_4), .B3(in_8),
    .F0(in_10), .F1(in_11), .F2(in_12), .Cout(out_17), .OVR(out_18), .C2(out_15), .C3(out_16), .C0(out_13),
    .C1(out_14));  // open: Vcc, GND
endmodule
