// Logisim project RAM.circ as structural Verilog: 1 circuit, main circuit RAM
module RAM (
  input  Clock,
  input  w_0__R_1,
  input  [23:0] Address,
  input  [15:0] Data,
  output [15:0] Data_Out
);

  wire n74138_1__7__y7, n74138_1__12__y3, n74138_1__13__y2, n74138_1__14__y1, n74138_1__15__y0, not_1_out,
       not_3_out, not_4_out, not_5_out, not_6_out, not_7_out, not_8_out, not_9_out, not_10_out, not_11_out,
       not_12_out, not_13_out, undriven;
  wire [7:0] n74245_1__11__b8, n74245_2__11__b8, n74245_3__11__b8, n74245_4__11__b8, n74245_5__18___b1,
       n74245_10__18___b1, ram_5_data, ram_6_data, ram_7_data, ram_8_data;

  _74138 u_74138_1 (
    ._1__A(Address[19]), ._2__B(Address[20]), ._3__C(Address[21]), ._4__G2A(1'b0), ._5__G2B(1'b0),
    ._6__G1(1'b1), ._7__Y7(n74138_1__7__y7), ._15__Y0(n74138_1__15__y0), ._14__Y1(n74138_1__14__y1),
    ._13__Y2(n74138_1__13__y2), ._12__Y3(n74138_1__12__y3), ._11__Y4(n74138_1__7__y7),
    ._10__Y5(n74138_1__7__y7), ._9__Y6(n74138_1__7__y7));  // open: _8__GND, _16__Vcc
  not not_1 (not_1_out, n74138_1__15__y0);
  not not_2 (Clock, n74138_1__14__y1);
  not not_3 (not_3_out, n74138_1__13__y2);
  not not_4 (not_4_out, n74138_1__12__y3);
  _74245 u_74245_1 (
    ._1__DIR(1'b1), ._2__A1(Data[7]), ._3__A2(Data[6]), ._4__A3(Data[5]), ._5__A4(Data[4]), ._6__A5(Data[3]),
    ._7__A6(Data[2]), ._8__A7(Data[1]), ._9__A8(Data[0]), ._19__nG(w_0__R_1), ._18___B1(n74245_1__11__b8[7]),
    ._17__B2(n74245_1__11__b8[6]), ._16__B3(n74245_1__11__b8[5]), ._15__B4(n74245_1__11__b8[4]),
    ._14__B5(n74245_1__11__b8[3]), ._13__B6(n74245_1__11__b8[2]), ._12__B7(n74245_1__11__b8[1]),
    ._11__B8(n74245_1__11__b8[0]));  // open: _10__GND, _20__Vcc
  not not_5 (not_5_out, w_0__R_1);
  RAM_part #(.addrWidth(19)) ram_1 (
    .addr(Address[18:0]), .data(n74245_1__11__b8), .sel(not_1_out), .clk(Clock), .ld(w_0__R_1));  // open: clr
  _74245 u_74245_2 (
    ._1__DIR(1'b1), ._2__A1(Data[7]), ._3__A2(Data[6]), ._4__A3(Data[5]), ._5__A4(Data[4]), ._6__A5(Data[3]),
    ._7__A6(Data[2]), ._8__A7(Data[1]), ._9__A8(Data[0]), ._19__nG(w_0__R_1), ._18___B1(n74245_2__11__b8[7]),
    ._17__B2(n74245_2__11__b8[6]), ._16__B3(n74245_2__11__b8[5]), ._15__B4(n74245_2__11__b8[4]),
    ._14__B5(n74245_2__11__b8[3]), ._13__B6(n74245_2__11__b8[2]), ._12__B7(n74245_2__11__b8[1]),
    ._11__B8(n74245_2__11__b8[0]));  // open: _10__GND, _20__Vcc
  not not_6 (not_6_out, w_0__R_1);
  RAM_part #(.addrWidth(19)) ram_2 (
    .addr(Address[18:0]), .data(n74245_2__11__b8), .sel(Clock), .clk(undriven), .ld(w_0__R_1));  // open: clr
  _74245 u_74245_3 (
    ._1__DIR(1'b1), ._2__A1(Data[7]), ._3__A2(Data[6]), ._4__A3(Data[5]), ._5__A4(Data[4]), ._6__A5(Data[3]),
    ._7__A6(Data[2]), ._8__A7(Data[1]), ._9__A8(Data[0]), ._19__nG(w_0__R_1), ._18___B1(n74245_3__11__b8[7]),
    ._17__B2(n74245_3__11__b8[6]), ._16__B3(n74245_3__11__b8[5]), ._15__B4(n74245_3__11__b8[4]),
    ._14__B5(n74245_3__11__b8[3]), ._13__B6(n74245_3__11__b8[2]), ._12__B7(n74245_3__11__b8[1]),
    ._11__B8(n74245_3__11__b8[0]));  // open: _10__GND, _20__Vcc
  not not_7 (not_7_out, w_0__R_1);
  RAM_part #(.addrWidth(19)) ram_3 (
    .addr(Address[18:0]), .data(n74245_3__11__b8), .sel(not_3_out), .clk(undriven), .ld(w_0__R_1));  // open: clr
  _74245 u_74245_4 (
    ._1__DIR(1'b1), ._2__A1(Data[7]), ._3__A2(Data[6]), ._4__A3(Data[5]), ._5__A4(Data[4]), ._6__A5(Data[3]),
    ._7__A6(Data[2]), ._8__A7(Data[1]), ._9__A8(Data[0]), ._19__nG(w_0__R_1), ._18___B1(n74245_4__11__b8[7]),
    ._17__B2(n74245_4__11__b8[6]), ._16__B3(n74245_4__11__b8[5]), ._15__B4(n74245_4__11__b8[4]),
    ._14__B5(n74245_4__11__b8[3]), ._13__B6(n74245_4__11__b8[2]), ._12__B7(n74245_4__11__b8[1]),
    ._11__B8(n74245_4__11__b8[0]));  // open: _10__GND, _20__Vcc
  not not_8 (not_8_out, w_0__R_1);
  RAM_part #(.addrWidth(19)) ram_4 (
    .addr(Address[18:0]), .data(n74245_4__11__b8), .sel(not_4_out), .clk(undriven), .ld(w_0__R_1));  // open: clr
  _74245 u_74245_5 (
    ._1__DIR(1'b1), ._2__A1(n74245_1__11__b8[0]), ._3__A2(n74245_1__11__b8[1]), ._4__A3(n74245_1__11__b8[2]),
    ._5__A4(n74245_1__11__b8[3]), ._6__A5(n74245_1__11__b8[4]), ._7__A6(n74245_1__11__b8[5]),
    ._8__A7(n74245_1__11__b8[6]), ._9__A8(n74245_1__11__b8[7]), ._19__nG(not_5_out),
    ._18___B1(n74245_5__18___b1[0]), ._17__B2(n74245_5__18___b1[1]), ._16__B3(n74245_5__18___b1[2]),
    ._15__B4(n74245_5__18___b1[3]), ._14__B5(n74245_5__18___b1[4]), ._13__B6(n74245_5__18___b1[5]),
    ._12__B7(n74245_5__18___b1[6]), ._11__B8(n74245_5__18___b1[7]));  // open: _10__GND, _20__Vcc
  _74245 u_74245_6 (
    ._1__DIR(1'b1), ._2__A1(n74245_2__11__b8[0]), ._3__A2(n74245_2__11__b8[1]), ._4__A3(n74245_2__11__b8[2]),
    ._5__A4(n74245_2__11__b8[3]), ._6__A5(n74245_2__11__b8[4]), ._7__A6(n74245_2__11__b8[5]),
    ._8__A7(n74245_2__11__b8[6]), ._9__A8(n74245_2__11__b8[7]), ._19__nG(not_6_out),
    ._18___B1(n74245_5__18___b1[0]), ._17__B2(n74245_5__18___b1[1]), ._16__B3(n74245_5__18___b1[2]),
    ._15__B4(n74245_5__18___b1[3]), ._14__B5(n74245_5__18___b1[4]), ._13__B6(n74245_5__18___b1[5]),
    ._12__B7(n74245_5__18___b1[6]), ._11__B8(n74245_5__18___b1[7]));  // open: _10__GND, _20__Vcc
  _74245 u_74245_7 (
    ._1__DIR(1'b1), ._2__A1(n74245_3__11__b8[0]), ._3__A2(n74245_3__11__b8[1]), ._4__A3(n74245_3__11__b8[2]),
    ._5__A4(n74245_3__11__b8[3]), ._6__A5(n74245_3__11__b8[4]), ._7__A6(n74245_3__11__b8[5]),
    ._8__A7(n74245_3__11__b8[6]), ._9__A8(n74245_3__11__b8[7]), ._19__nG(not_7_out),
    ._18___B1(n74245_5__18___b1[0]), ._17__B2(n74245_5__18___b1[1]), ._16__B3(n74245_5__18___b1[2]),
    ._15__B4(n74245_5__18___b1[3]), ._14__B5(n74245_5__18___b1[4]), ._13__B6(n74245_5__18___b1[5]),
    ._12__B7(n74245_5__18___b1[6]), ._11__B8(n74245_5__18___b1[7]));  // open: _10__GND, _20__Vcc
  _74245 u_74245_8 (
    ._1__DIR(1'b1), ._2__A1(n74245_4__11__b8[0]), ._3__A2(n74245_4__11__b8[1]), ._4__A3(n74245_4__11__b8[2]),
    ._5__A4(n74245_4__11__b8[3]), ._6__A5(n74245_4__11__b8[4]), ._7__A6(n74245_4__11__b8[5]),
    ._8__A7(n74245_4__11__b8[6]), ._9__A8(n74245_4__11__b8[7]), ._19__nG(not_8_out),
    ._18___B1(n74245_5__18___b1[0]), ._17__B2(n74245_5__18___b1[1]), ._16__B3(n74245_5__18___b1[2]),
    ._15__B4(n74245_5__18___b1[3]), ._14__B5(n74245_5__18___b1[4]), ._13__B6(n74245_5__18___b1[5]),
    ._12__B7(n74245_5__18___b1[6]), ._11__B8(n74245_5__18___b1[7]));  // open: _10__GND, _20__Vcc
  RAM_part #(.addrWidth(19)) ram_5 (
    .addr(Address[18:0]), .data(ram_5_data), .sel(not_1_out), .clk(Clock), .ld(w_0__R_1));  // open: clr
  RAM_part #(.addrWidth(19)) ram_6 (
    .addr(Address[18:0]), .data(ram_6_data), .sel(Clock), .clk(Clock), .ld(w_0__R_1));  // open: clr
  RAM_part #(.addrWidth(19)) ram_7 (
    .addr(Address[18:0]), .data(ram_7_data), .sel(not_3_out), .clk(Clock), .ld(w_0__R_1));  // open: clr
  RAM_part #(.addrWidth(19)) ram_8 (
    .addr(Address[18:0]), .data(ram_8_data), .sel(not_4_out), .clk(Clock), .ld(w_0__R_1));  // open: clr
  _74245 u_74245_9 (
    ._1__DIR(1'b1), ._2__A1(Data[15]), ._3__A2(Data[14]), ._4__A3(Data[13]), ._5__A4(Data[12]),
    ._6__A5(Data[11]), ._7__A6(Data[10]), ._8__A7(Data[9]), ._9__A8(Data[8]), ._19__nG(w_0__R_1),
    ._18___B1(ram_5_data[7]), ._17__B2(ram_5_data[6]), ._16__B3(ram_5_data[5]), ._15__B4(ram_5_data[4]),
    ._14__B5(ram_5_data[3]), ._13__B6(ram_5_data[2]), ._12__B7(ram_5_data[1]), ._11__B8(ram_5_data[0]));  // open: _10__GND, _20__Vcc
  not not_9 (not_9_out, w_0__R_1);
  _74245 u_74245_10 (
    ._1__DIR(1'b1), ._2__A1(ram_5_data[0]), ._3__A2(ram_5_data[1]), ._4__A3(ram_5_data[2]),
    ._5__A4(ram_5_data[3]), ._6__A5(ram_5_data[4]), ._7__A6(ram_5_data[5]), ._8__A7(ram_5_data[6]),
    ._9__A8(ram_5_data[7]), ._19__nG(not_9_out), ._18___B1(n74245_10__18___b1[0]),
    ._17__B2(n74245_10__18___b1[1]), ._16__B3(n74245_10__18___b1[2]), ._15__B4(n74245_10__18___b1[3]),
    ._14__B5(n74245_10__18___b1[4]), ._13__B6(n74245_10__18___b1[5]), ._12__B7(n74245_10__18___b1[6]),
    ._11__B8(n74245_10__18___b1[7]));  // open: _10__GND, _20__Vcc
  _74245 u_74245_11 (
    ._1__DIR(1'b1), ._2__A1(Data[15]), ._3__A2(Data[14]), ._4__A3(Data[13]), ._5__A4(Data[12]),
    ._6__A5(Data[11]), ._7__A6(Data[10]), ._8__A7(Data[9]), ._9__A8(Data[8]), ._19__nG(w_0__R_1),
    ._18___B1(ram_6_data[7]), ._17__B2(ram_6_data[6]), ._16__B3(ram_6_data[5]), ._15__B4(ram_6_data[4]),
    ._14__B5(ram_6_data[3]), ._13__B6(ram_6_data[2]), ._12__B7(ram_6_data[1]), ._11__B8(ram_6_data[0]));  // open: _10__GND, _20__Vcc
  not not_10 (not_10_out, w_0__R_1);
  _74245 u_74245_12 (
    ._1__DIR(1'b1), ._2__A1(ram_6_data[0]), ._3__A2(ram_6_data[1]), ._4__A3(ram_6_data[2]),
    ._5__A4(ram_6_data[3]), ._6__A5(ram_6_data[4]), ._7__A6(ram_6_data[5]), ._8__A7(ram_6_data[6]),
    ._9__A8(ram_6_data[7]), ._19__nG(not_10_out), ._18___B1(n74245_10__18___b1[0]),
    ._17__B2(n74245_10__18___b1[1]), ._16__B3(n74245_10__18___b1[2]), ._15__B4(n74245_10__18___b1[3]),
    ._14__B5(n74245_10__18___b1[4]), ._13__B6(n74245_10__18___b1[5]), ._12__B7(n74245_10__18___b1[6]),
    ._11__B8(n74245_10__18___b1[7]));  // open: _10__GND, _20__Vcc
  _74245 u_74245_13 (
    ._1__DIR(1'b1), ._2__A1(Data[15]), ._3__A2(Data[14]), ._4__A3(Data[13]), ._5__A4(Data[12]),
    ._6__A5(Data[11]), ._7__A6(Data[10]), ._8__A7(Data[9]), ._9__A8(Data[8]), ._19__nG(w_0__R_1),
    ._18___B1(ram_7_data[7]), ._17__B2(ram_7_data[6]), ._16__B3(ram_7_data[5]), ._15__B4(ram_7_data[4]),
    ._14__B5(ram_7_data[3]), ._13__B6(ram_7_data[2]), ._12__B7(ram_7_data[1]), ._11__B8(ram_7_data[0]));  // open: _10__GND, _20__Vcc
  not not_11 (not_11_out, w_0__R_1);
  _74245 u_74245_14 (
    ._1__DIR(1'b1), ._2__A1(ram_7_data[0]), ._3__A2(ram_7_data[1]), ._4__A3(ram_7_data[2]),
    ._5__A4(ram_7_data[3]), ._6__A5(ram_7_data[4]), ._7__A6(ram_7_data[5]), ._8__A7(ram_7_data[6]),
    ._9__A8(ram_7_data[7]), ._19__nG(not_11_out), ._18___B1(n74245_10__18___b1[0]),
    ._17__B2(n74245_10__18___b1[1]), ._16__B3(n74245_10__18___b1[2]), ._15__B4(n74245_10__18___b1[3]),
    ._14__B5(n74245_10__18___b1[4]), ._13__B6(n74245_10__18___b1[5]), ._12__B7(n74245_10__18___b1[6]),
    ._11__B8(n74245_10__18___b1[7]));  // open: _10__GND, _20__Vcc
  _74245 u_74245_15 (
    ._1__DIR(1'b1), ._2__A1(Data[15]), ._3__A2(Data[14]), ._4__A3(Data[13]), ._5__A4(Data[12]),
    ._6__A5(Data[11]), ._7__A6(Data[10]), ._8__A7(Data[9]), ._9__A8(Data[8]), ._19__nG(w_0__R_1),
    ._18___B1(ram_8_data[7]), ._17__B2(ram_8_data[6]), ._16__B3(ram_8_data[5]), ._15__B4(ram_8_data[4]),
    ._14__B5(ram_8_data[3]), ._13__B6(ram_8_data[2]), ._12__B7(ram_8_data[1]), ._11__B8(ram_8_data[0]));  // open: _10__GND, _20__Vcc
  not not_12 (not_12_out, w_0__R_1);
  _74245 u_74245_16 (
    ._1__DIR(1'b1), ._2__A1(ram_8_data[0]), ._3__A2(ram_8_data[1]), ._4__A3(ram_8_data[2]),
    ._5__A4(ram_8_data[3]), ._6__A5(ram_8_data[4]), ._7__A6(ram_8_data[5]), ._8__A7(ram_8_data[6]),
    ._9__A8(ram_8_data[7]), ._19__nG(not_12_out), ._18___B1(n74245_10__18___b1[0]),
    ._17__B2(n74245_10__18___b1[1]), ._16__B3(n74245_10__18___b1[2]), ._15__B4(n74245_10__18___b1[3]),
    ._14__B5(n74245_10__18___b1[4]), ._13__B6(n74245_10__18___b1[5]), ._12__B7(n74245_10__18___b1[6]),
    ._11__B8(n74245_10__18___b1[7]));  // open: _10__GND, _20__Vcc
  not not_13 (not_13_out, n74138_1__7__y7);
  LED Address_Fault (.in(not_13_out));
  // also tied to GND on the sheet: {Address[22], Address[23]}
endmodule
