// Logisim project Registers.circ as structural Verilog: 6 circuits, main circuit Registers
module Registers (
  input  [15:0] Instruction,
  input  r_0____W_1,
  input  Bus_Select,
  input  [15:0] Memory_In,
  input  [15:0] C_Bus,
  input  [3:0] C_Bus_Select,
  input  [3:0] A_Bus_Select,
  input  B_Bus_Select_1,
  input  B_Bus_Select_0,
  input  CLK,
  output [7:0] SEG_Address,
  output [15:0] OFF_Address,
  output [15:0] Memory_Out,
  output [15:0] A_Bus,
  output [15:0] B_Bus
);

  wire and_1_out, and_2_out, and_3_out, n74125_1_o0__3, n74125_1_o1__6, n74125_2_o0__3, n74139_1__10__2y2,
       n74139_1__11__2y1, n74139_1__12__2y0, n74154_1__1__y0, n74154_1__2__y1, n74154_1__3__y2,
       n74154_1__4__y3, n74154_1__5__y4, n74154_1__6__y5, n74154_1__7__y6, n74154_1__8__y7, n74154_1__9__y8,
       n74154_1__11__y10, n74154_2__2__y1, n74154_2__3__y2, n74154_2__4__y3, n74154_2__5__y4,
       n74154_2__6__y5, n74154_2__7__y6, n74154_2__8__y7, n74154_2__9__y8, n74245_1__11__b8,
       n74245_1__12__b7, n74245_1__13__b6, n74245_1__14__b5, n74245_1__15__b4, n74245_1__16__b3,
       n74245_2__11__b8, n74245_2__12__b7, not_1_out, not_2_out, not_3_out, or_1_out, or_2_out, undriven;
  wire [2:0] bit_extender_1_out;

  _74154 u_74154_1 (
    ._1__Y0(n74154_1__1__y0), ._2__Y1(n74154_1__2__y1), ._3__Y2(n74154_1__3__y2), ._4__Y3(n74154_1__4__y3),
    ._5__Y4(n74154_1__5__y4), ._6__Y5(n74154_1__6__y5), ._7__Y6(n74154_1__7__y6), ._8__Y7(n74154_1__8__y7),
    ._9__Y8(n74154_1__9__y8), ._11__Y10(n74154_1__11__y10), ._12__GND(undriven), ._23__A(C_Bus_Select[0]),
    ._22__B(C_Bus_Select[1]), ._21__C(C_Bus_Select[2]), ._20__D(C_Bus_Select[3]), ._19__G2(1'b0),
    ._18__G1(1'b0));  // open: _10__Y9, _24__Vcc, _17__Y15, _16__Y14, _15__Y13, _14__Y12, _13__Y11
  _74154 u_74154_2 (
    ._2__Y1(n74154_2__2__y1), ._3__Y2(n74154_2__3__y2), ._4__Y3(n74154_2__4__y3), ._5__Y4(n74154_2__5__y4),
    ._6__Y5(n74154_2__6__y5), ._7__Y6(n74154_2__7__y6), ._8__Y7(n74154_2__8__y7), ._9__Y8(n74154_2__9__y8),
    ._23__A(A_Bus_Select[0]), ._22__B(A_Bus_Select[1]), ._21__C(A_Bus_Select[2]), ._20__D(A_Bus_Select[3]),
    ._19__G2(1'b0), ._18__G1(1'b0));  // open: _1__Y0, _10__Y9, _11__Y10, _12__GND, _24__Vcc, _17__Y15, _16__Y14, _15__Y13, _14__Y12, _13__Y11
  _74139 u_74139_1 (
    ._15__2G(1'b0), ._14__2A(B_Bus_Select_0), ._13__2B(B_Bus_Select_1), ._12__2Y0(n74139_1__12__2y0),
    ._11__2Y1(n74139_1__11__2y1), ._10__2Y2(n74139_1__10__2y2));  // open: _1__1G, _2__1A, _3__1B, _4__1Y0, _5__1Y1, _6__1Y2, _7__1Y3, _8__GND, _16__Vcc, _9__2Y3
  not not_1 (not_1_out, r_0____W_1);
  _74245 u_74245_1 (
    ._1__DIR(r_0____W_1), ._4__A3(n74154_1__8__y7), ._5__A4(n74154_1__7__y6), ._6__A5(n74154_1__6__y5),
    ._7__A6(n74154_1__5__y4), ._8__A7(n74154_1__4__y3), ._9__A8(n74154_1__3__y2), ._19__nG(1'b0),
    ._16__B3(n74245_1__16__b3), ._15__B4(n74245_1__15__b4), ._14__B5(n74245_1__14__b5),
    ._13__B6(n74245_1__13__b6), ._12__B7(n74245_1__12__b7), ._11__B8(n74245_1__11__b8));  // open: _2__A1, _3__A2, _10__GND, _20__Vcc, _18___B1, _17__B2
  _74245 u_74245_2 (
    ._1__DIR(not_1_out), ._2__A1(n74154_2__9__y8), ._3__A2(n74154_2__8__y7), ._4__A3(n74154_2__7__y6),
    ._5__A4(n74154_2__6__y5), ._6__A5(n74154_2__5__y4), ._7__A6(n74154_2__4__y3), ._8__A7(n74154_2__3__y2),
    ._9__A8(n74154_2__2__y1), ._19__nG(1'b0), ._18___B1(n74245_1__16__b3), ._17__B2(n74245_1__15__b4),
    ._16__B3(n74245_1__14__b5), ._15__B4(n74245_1__13__b6), ._14__B5(n74245_1__12__b7),
    ._13__B6(n74245_1__11__b8), ._12__B7(n74245_2__12__b7), ._11__B8(n74245_2__11__b8));  // open: _10__GND, _20__Vcc
  _74125 u_74125_1 (
    .B0__2(n74154_1__9__y8), .A0__1(not_1_out), .B1__5(n74154_1__11__y10), .A1__4(not_1_out),
    .B2__12(n74154_1__1__y0), .A2__13(not_1_out), .B3__9(n74154_1__2__y1), .A3__10(not_1_out),
    .O0__3(n74125_1_o0__3), .O1__6(n74125_1_o1__6), .O2__11(n74245_2__11__b8), .O3__8(n74245_2__12__b7));  // open: Vcc__14, GND__7
  _74125 u_74125_2 (
    .B0__2(undriven), .A0__1(not_1_out), .B1__5(n74139_1__10__2y2), .A1__4(r_0____W_1),
    .B2__12(n74139_1__12__2y0), .A2__13(r_0____W_1), .B3__9(n74139_1__11__2y1), .A3__10(r_0____W_1),
    .O0__3(n74125_2_o0__3), .O1__6(n74125_2_o0__3), .O2__11(n74125_1_o0__3), .O3__8(n74125_1_o1__6));  // open: Vcc__14, GND__7
  Bit_Extender #(.in_width(16), .out_width(3)) bit_extender_1 (.in(Instruction), .out(bit_extender_1_out));
  not not_2 (not_2_out, bit_extender_1_out[2]);
  and and_1 (and_1_out, not_2_out, and_2_out);
  or or_1 (or_1_out, n74245_1__16__b3, and_1_out);
  not not_3 (not_3_out, bit_extender_1_out[1]);
  and and_2 (and_2_out, bit_extender_1_out[0], not_3_out);
  and and_3 (and_3_out, and_2_out, bit_extender_1_out[2]);
  or or_2 (or_2_out, n74245_1__15__b4, and_3_out);
  MAR mar_1 (
    .CLK(r_0____W_1), .r_0____W_1(r_0____W_1), .Bus_Select(Bus_Select), .nOffset_Enable(or_1_out),
    .Instruction_In(Instruction), .C_Bus(C_Bus), .Offset_Out(OFF_Address), .A_Bus(A_Bus),
    .nBase_Enable(or_2_out), .Segment_Out(SEG_Address));
  Register16 INT (.R___W(r_0____W_1), .Data_In(C_Bus), .CLK(CLK), .Data_Out(A_Bus), .nEnable(n74245_1__13__b6));
  Register16 A0 (.R___W(r_0____W_1), .Data_In(C_Bus), .CLK(CLK), .Data_Out(A_Bus), .nEnable(n74245_2__11__b8));
  Register16 B0 (.R___W(r_0____W_1), .Data_In(C_Bus), .CLK(CLK), .Data_Out(B_Bus), .nEnable(n74125_1_o0__3));
  MDR mdr_1 (
    .CLK(CLK), .r_0____W_1(n74245_1__14__b5), .Bus_Select(Bus_Select), .nEnable(r_0____W_1),
    .Memory_In(Memory_In), .C_Bus(C_Bus), .Memory_Out(Memory_Out), .A_Bus(A_Bus));
  Register16 SP (.R___W(r_0____W_1), .Data_In(C_Bus), .CLK(CLK), .Data_Out(A_Bus), .nEnable(n74245_1__12__b7));
  Register16 A1 (.R___W(r_0____W_1), .Data_In(C_Bus), .CLK(CLK), .Data_Out(A_Bus), .nEnable(n74245_2__12__b7));
  Register16 B1 (.R___W(r_0____W_1), .Data_In(C_Bus), .CLK(CLK), .Data_Out(B_Bus), .nEnable(n74125_1_o1__6));
  // AND_Gate and_4 has open pins: in0=bit_extender_1_out[1], in1=bit_extender_1_out[2], out=open
  IMM imm_1 (.Instruction(Instruction), .R___W(r_0____W_1), .nEnable(n74125_2_o0__3), .CLK(CLK), .C_Bus(B_Bus));
  Register16 PC (.R___W(r_0____W_1), .Data_In(C_Bus), .CLK(CLK), .Data_Out(A_Bus), .nEnable(n74245_1__11__b8));
endmodule

module IMM (
  input  [15:0] Instruction,
  input  R___W,
  input  nEnable,
  input  CLK,
  output [15:0] C_Bus
);

  wire [12:0] bit_extender_1_out;
  wire [15:0] bit_extender_2_out;

  Bit_Extender #(.in_width(16), .out_width(13)) bit_extender_1 (.in(Instruction), .out(bit_extender_1_out));
  assign bit_extender_2_out = {{3{1'b0}}, bit_extender_1_out};  // Bit_Extender bit_extender_2
  Register16 register16_1 (.R___W(R___W), .Data_In(bit_extender_2_out), .CLK(CLK), .Data_Out(C_Bus), .nEnable(nEnable));
endmodule

module MAR (
  input  r_0____W_1,
  input  Bus_Select,
  input  nOffset_Enable,
  input  nBase_Enable,
  input  [15:0] Instruction_In,
  input  [15:0] C_Bus,
  input  CLK,
  output [15:0] Offset_Out,
  output [15:0] A_Bus,
  output [7:0] Segment_Out
);

  wire and_1_out, and_2_out, and_3_out, and_4_out, and_5_out, and_6_out, nand_1_out, nor_1_out, not_1_out,
       not_2_out, not_3_out, not_4_out, not_5_out;
  wire [7:0] n74244_1__3__2y0, n74245_1__18___b1, n74245_4__18___b1, n74374_2_q0__19;
  wire [15:0] n74374_1_q0__19;

  and and_1 (and_1_out, nOffset_Enable, r_0____W_1);
  and and_2 (and_2_out, nBase_Enable, r_0____W_1);
  _74245 u_74245_1 (
    ._1__DIR(1'b1), ._2__A1(Instruction_In[0]), ._3__A2(Instruction_In[1]), ._4__A3(Instruction_In[2]),
    ._5__A4(Instruction_In[3]), ._6__A5(Instruction_In[4]), ._7__A6(Instruction_In[5]),
    ._8__A7(Instruction_In[6]), ._9__A8(Instruction_In[7]), ._19__nG(and_3_out),
    ._18___B1(n74245_1__18___b1[0]), ._17__B2(n74245_1__18___b1[1]), ._16__B3(n74245_1__18___b1[2]),
    ._15__B4(n74245_1__18___b1[3]), ._14__B5(n74245_1__18___b1[4]), ._13__B6(n74245_1__18___b1[5]),
    ._12__B7(n74245_1__18___b1[6]), ._11__B8(n74245_1__18___b1[7]));  // open: _10__GND, _20__Vcc
  _74244 u_74244_1 (
    ._1__E1(and_1_out), ._2__1A0(Instruction_In[11]), ._4__1A1(Instruction_In[10]),
    ._6__1A2(Instruction_In[9]), ._8__1A3(Instruction_In[8]), ._19__E2(and_2_out),
    ._17__2A0(Instruction_In[15]), ._15__2A1(Instruction_In[14]), ._13__2A2(Instruction_In[13]),
    ._11__2A3(Instruction_In[12]), ._18__1Y0(n74244_1__3__2y0[7]), ._16__1Y1(n74244_1__3__2y0[6]),
    ._14__1Y2(n74244_1__3__2y0[5]), ._12__1Y3(n74244_1__3__2y0[4]), ._3__2Y0(n74244_1__3__2y0[0]),
    ._5__2Y1(n74244_1__3__2y0[1]), ._7__2Y2(n74244_1__3__2y0[2]), ._9__2Y3(n74244_1__3__2y0[3]));  // open: _10__GND, _20__Vcc
  _74245 u_74245_2 (
    ._1__DIR(1'b1), ._2__A1(C_Bus[0]), ._3__A2(C_Bus[1]), ._4__A3(C_Bus[2]), ._5__A4(C_Bus[3]),
    ._6__A5(C_Bus[4]), ._7__A6(C_Bus[5]), ._8__A7(C_Bus[6]), ._9__A8(C_Bus[7]), ._19__nG(and_4_out),
    ._18___B1(n74244_1__3__2y0[0]), ._17__B2(n74244_1__3__2y0[1]), ._16__B3(n74244_1__3__2y0[2]),
    ._15__B4(n74244_1__3__2y0[3]), ._14__B5(n74244_1__3__2y0[4]), ._13__B6(n74244_1__3__2y0[5]),
    ._12__B7(n74244_1__3__2y0[6]), ._11__B8(n74244_1__3__2y0[7]));  // open: _10__GND, _20__Vcc
  _74245 u_74245_3 (
    ._1__DIR(1'b1), ._2__A1(C_Bus[8]), ._3__A2(C_Bus[9]), ._4__A3(C_Bus[10]), ._5__A4(C_Bus[11]),
    ._6__A5(C_Bus[12]), ._7__A6(C_Bus[13]), ._8__A7(C_Bus[14]), ._9__A8(C_Bus[15]), ._19__nG(and_4_out),
    ._18___B1(n74245_1__18___b1[0]), ._17__B2(n74245_1__18___b1[1]), ._16__B3(n74245_1__18___b1[2]),
    ._15__B4(n74245_1__18___b1[3]), ._14__B5(n74245_1__18___b1[4]), ._13__B6(n74245_1__18___b1[5]),
    ._12__B7(n74245_1__18___b1[6]), ._11__B8(n74245_1__18___b1[7]));  // open: _10__GND, _20__Vcc
  _74245 u_74245_4 (
    ._1__DIR(1'b1), ._2__A1(Instruction_In[0]), ._3__A2(Instruction_In[1]), ._4__A3(Instruction_In[2]),
    ._5__A4(Instruction_In[3]), ._6__A5(Instruction_In[4]), ._7__A6(Instruction_In[5]),
    ._8__A7(Instruction_In[6]), ._9__A8(Instruction_In[7]), ._19__nG(and_3_out),
    ._18___B1(n74245_4__18___b1[0]), ._17__B2(n74245_4__18___b1[1]), ._16__B3(n74245_4__18___b1[2]),
    ._15__B4(n74245_4__18___b1[3]), ._14__B5(n74245_4__18___b1[4]), ._13__B6(n74245_4__18___b1[5]),
    ._12__B7(n74245_4__18___b1[6]), ._11__B8(n74245_4__18___b1[7]));  // open: _10__GND, _20__Vcc
  _74245 u_74245_5 (
    ._1__DIR(1'b1), ._2__A1(C_Bus[0]), ._3__A2(C_Bus[1]), ._4__A3(C_Bus[2]), ._5__A4(C_Bus[3]),
    ._6__A5(C_Bus[4]), ._7__A6(C_Bus[5]), ._8__A7(C_Bus[6]), ._9__A8(C_Bus[7]), ._19__nG(and_4_out),
    ._18___B1(n74245_4__18___b1[0]), ._17__B2(n74245_4__18___b1[1]), ._16__B3(n74245_4__18___b1[2]),
    ._15__B4(n74245_4__18___b1[3]), ._14__B5(n74245_4__18___b1[4]), ._13__B6(n74245_4__18___b1[5]),
    ._12__B7(n74245_4__18___b1[6]), ._11__B8(n74245_4__18___b1[7]));  // open: _10__GND, _20__Vcc
  and and_3 (and_3_out, Bus_Select, r_0____W_1);
  not not_1 (not_1_out, Bus_Select);
  and and_4 (and_4_out, not_1_out, r_0____W_1);
  not not_2 (not_2_out, r_0____W_1);
  not not_3 (not_3_out, nOffset_Enable);
  nor nor_1 (nor_1_out, nOffset_Enable, nBase_Enable);
  _74374 u_74374_1 (
    .D0__2(n74244_1__3__2y0[0]), .D1__3(n74244_1__3__2y0[1]), .D2__4(n74244_1__3__2y0[2]),
    .D3__5(n74244_1__3__2y0[3]), .D4__6(n74244_1__3__2y0[4]), .D5__7(n74244_1__3__2y0[5]),
    .D6__8(n74244_1__3__2y0[6]), .D7__9(n74244_1__3__2y0[7]), .nOE__1(nand_1_out), .CLK__11(CLK),
    .Q0__19(n74374_1_q0__19[0]), .Q1__18(n74374_1_q0__19[1]), .Q2__17(n74374_1_q0__19[2]),
    .Q3__16(n74374_1_q0__19[3]), .Q4__15(n74374_1_q0__19[4]), .Q5__14(n74374_1_q0__19[5]),
    .Q6__13(n74374_1_q0__19[6]), .Q7__12(n74374_1_q0__19[7]));  // open: GND__10, Vcc__20
  nand nand_1 (nand_1_out, not_2_out, not_3_out);
  _74374 u_74374_2 (
    .D0__2(n74245_4__18___b1[0]), .D1__3(n74245_4__18___b1[1]), .D2__4(n74245_4__18___b1[2]),
    .D3__5(n74245_4__18___b1[3]), .D4__6(n74245_4__18___b1[4]), .D5__7(n74245_4__18___b1[5]),
    .D6__8(n74245_4__18___b1[6]), .D7__9(n74245_4__18___b1[7]), .nOE__1(nBase_Enable), .CLK__11(CLK),
    .Q0__19(n74374_2_q0__19[0]), .Q1__18(n74374_2_q0__19[1]), .Q2__17(n74374_2_q0__19[2]),
    .Q3__16(n74374_2_q0__19[3]), .Q4__15(n74374_2_q0__19[4]), .Q5__14(n74374_2_q0__19[5]),
    .Q6__13(n74374_2_q0__19[6]), .Q7__12(n74374_2_q0__19[7]));  // open: GND__10, Vcc__20
  _74374 u_74374_3 (
    .D0__2(n74245_1__18___b1[0]), .D1__3(n74245_1__18___b1[1]), .D2__4(n74245_1__18___b1[2]),
    .D3__5(n74245_1__18___b1[3]), .D4__6(n74245_1__18___b1[4]), .D5__7(n74245_1__18___b1[5]),
    .D6__8(n74245_1__18___b1[6]), .D7__9(n74245_1__18___b1[7]), .nOE__1(nand_1_out), .CLK__11(CLK),
    .Q0__19(n74374_1_q0__19[8]), .Q1__18(n74374_1_q0__19[9]), .Q2__17(n74374_1_q0__19[10]),
    .Q3__16(n74374_1_q0__19[11]), .Q4__15(n74374_1_q0__19[12]), .Q5__14(n74374_1_q0__19[13]),
    .Q6__13(n74374_1_q0__19[14]), .Q7__12(n74374_1_q0__19[15]));  // open: GND__10, Vcc__20
  _74245 u_74245_6 (
    ._1__DIR(1'b0), ._2__A1(1'b0), ._3__A2(1'b0), ._4__A3(1'b0), ._5__A4(1'b0), ._6__A5(1'b0), ._7__A6(1'b0),
    ._8__A7(1'b0), ._9__A8(1'b0), ._19__nG(nBase_Enable), ._18___B1(A_Bus[8]), ._17__B2(A_Bus[9]),
    ._16__B3(A_Bus[10]), ._15__B4(A_Bus[11]), ._14__B5(A_Bus[12]), ._13__B6(A_Bus[13]), ._12__B7(A_Bus[14]),
    ._11__B8(A_Bus[15]));  // open: _10__GND, _20__Vcc
  not not_4 (not_4_out, r_0____W_1);
  _74245 u_74245_7 (
    ._1__DIR(1'b1), ._2__A1(n74374_1_q0__19[0]), ._3__A2(n74374_1_q0__19[1]), ._4__A3(n74374_1_q0__19[2]),
    ._5__A4(n74374_1_q0__19[3]), ._6__A5(n74374_1_q0__19[4]), ._7__A6(n74374_1_q0__19[5]),
    ._8__A7(n74374_1_q0__19[6]), ._9__A8(n74374_1_q0__19[7]), ._19__nG(and_6_out), ._18___B1(Offset_Out[0]),
    ._17__B2(Offset_Out[1]), ._16__B3(Offset_Out[2]), ._15__B4(Offset_Out[3]), ._14__B5(Offset_Out[4]),
    ._13__B6(Offset_Out[5]), ._12__B7(Offset_Out[6]), ._11__B8(Offset_Out[7]));  // open: _10__GND, _20__Vcc
  _74245 u_74245_8 (
    ._1__DIR(1'b1), ._2__A1(n74374_1_q0__19[8]), ._3__A2(n74374_1_q0__19[9]), ._4__A3(n74374_1_q0__19[10]),
    ._5__A4(n74374_1_q0__19[11]), ._6__A5(n74374_1_q0__19[12]), ._7__A6(n74374_1_q0__19[13]),
    ._8__A7(n74374_1_q0__19[14]), ._9__A8(n74374_1_q0__19[15]), ._19__nG(and_6_out),
    ._18___B1(Offset_Out[8]), ._17__B2(Offset_Out[9]), ._16__B3(Offset_Out[10]), ._15__B4(Offset_Out[11]),
    ._14__B5(Offset_Out[12]), ._13__B6(Offset_Out[13]), ._12__B7(Offset_Out[14]), ._11__B8(Offset_Out[15]));  // open: _10__GND, _20__Vcc
  _74245 u_74245_9 (
    ._1__DIR(1'b1), ._2__A1(n74374_1_q0__19[0]), ._3__A2(n74374_1_q0__19[1]), ._4__A3(n74374_1_q0__19[2]),
    ._5__A4(n74374_1_q0__19[3]), ._6__A5(n74374_1_q0__19[4]), ._7__A6(n74374_1_q0__19[5]),
    ._8__A7(n74374_1_q0__19[6]), ._9__A8(n74374_1_q0__19[7]), ._19__nG(and_5_out), ._18___B1(A_Bus[0]),
    ._17__B2(A_Bus[1]), ._16__B3(A_Bus[2]), ._15__B4(A_Bus[3]), ._14__B5(A_Bus[4]), ._13__B6(A_Bus[5]),
    ._12__B7(A_Bus[6]), ._11__B8(A_Bus[7]));  // open: _10__GND, _20__Vcc
  _74245 u_74245_10 (
    ._1__DIR(1'b1), ._2__A1(n74374_1_q0__19[8]), ._3__A2(n74374_1_q0__19[9]), ._4__A3(n74374_1_q0__19[10]),
    ._5__A4(n74374_1_q0__19[11]), ._6__A5(n74374_1_q0__19[12]), ._7__A6(n74374_1_q0__19[13]),
    ._8__A7(n74374_1_q0__19[14]), ._9__A8(n74374_1_q0__19[15]), ._19__nG(and_5_out), ._18___B1(A_Bus[8]),
    ._17__B2(A_Bus[9]), ._16__B3(A_Bus[10]), ._15__B4(A_Bus[11]), ._14__B5(A_Bus[12]), ._13__B6(A_Bus[13]),
    ._12__B7(A_Bus[14]), ._11__B8(A_Bus[15]));  // open: _10__GND, _20__Vcc
  _74245 u_74245_11 (
    ._1__DIR(1'b1), ._2__A1(n74374_2_q0__19[0]), ._3__A2(n74374_2_q0__19[1]), ._4__A3(n74374_2_q0__19[2]),
    ._5__A4(n74374_2_q0__19[3]), ._6__A5(n74374_2_q0__19[4]), ._7__A6(n74374_2_q0__19[5]),
    ._8__A7(n74374_2_q0__19[6]), ._9__A8(n74374_2_q0__19[7]), ._19__nG(and_6_out), ._18___B1(Segment_Out[0]),
    ._17__B2(Segment_Out[1]), ._16__B3(Segment_Out[2]), ._15__B4(Segment_Out[3]), ._14__B5(Segment_Out[4]),
    ._13__B6(Segment_Out[5]), ._12__B7(Segment_Out[6]), ._11__B8(Segment_Out[7]));  // open: _10__GND, _20__Vcc
  _74245 u_74245_12 (
    ._1__DIR(1'b1), ._2__A1(n74374_2_q0__19[0]), ._3__A2(n74374_2_q0__19[1]), ._4__A3(n74374_2_q0__19[2]),
    ._5__A4(n74374_2_q0__19[3]), ._6__A5(n74374_2_q0__19[4]), ._7__A6(n74374_2_q0__19[5]),
    ._8__A7(n74374_2_q0__19[6]), ._9__A8(n74374_2_q0__19[7]), ._19__nG(and_5_out), ._18___B1(A_Bus[0]),
    ._17__B2(A_Bus[1]), ._16__B3(A_Bus[2]), ._15__B4(A_Bus[3]), ._14__B5(A_Bus[4]), ._13__B6(A_Bus[5]),
    ._12__B7(A_Bus[6]), ._11__B8(A_Bus[7]));  // open: _10__GND, _20__Vcc
  not not_5 (not_5_out, Bus_Select);
  and and_5 (and_5_out, not_5_out, not_4_out);
  and and_6 (and_6_out, Bus_Select, not_4_out);
  LED Write_Fault (.in(nor_1_out));
  // also tied to GND on the sheet: {C_Bus[8], C_Bus[9], C_Bus[10], C_Bus[11], C_Bus[12], C_Bus[13], C_Bus[14], C_Bus[15], Instruction_In[8], Instruction_In[9], Instruction_In[10], Instruction_In[11], Instruction_In[12], Instruction_In[13], Instruction_In[14], Instruction_In[15]}

  // Notes on the sheet:
  //   Can I use a single Enable w/Bus Select?
  //   Segment
  //   Offset
endmodule

module MDR (
  input  r_0____W_1,
  input  Bus_Select,
  input  nEnable,
  input  [15:0] Memory_In,
  input  [15:0] C_Bus,
  input  CLK,
  output [15:0] Memory_Out,
  output [15:0] A_Bus
);

  wire and_1_out, and_2_out, and_3_out, and_4_out, not_1_out, not_2_out, not_3_out;
  wire [7:0] n74245_1__18___b1, n74245_2__18___b1;
  wire [15:0] register16_1_data_out;

  _74245 u_74245_1 (
    ._1__DIR(1'b1), ._2__A1(Memory_In[0]), ._3__A2(Memory_In[1]), ._4__A3(Memory_In[2]),
    ._5__A4(Memory_In[3]), ._6__A5(Memory_In[4]), ._7__A6(Memory_In[5]), ._8__A7(Memory_In[6]),
    ._9__A8(Memory_In[7]), ._19__nG(and_2_out), ._18___B1(n74245_1__18___b1[0]),
    ._17__B2(n74245_1__18___b1[1]), ._16__B3(n74245_1__18___b1[2]), ._15__B4(n74245_1__18___b1[3]),
    ._14__B5(n74245_1__18___b1[4]), ._13__B6(n74245_1__18___b1[5]), ._12__B7(n74245_1__18___b1[6]),
    ._11__B8(n74245_1__18___b1[7]));  // open: _10__GND, _20__Vcc
  _74245 u_74245_2 (
    ._1__DIR(1'b1), ._2__A1(Memory_In[8]), ._3__A2(Memory_In[9]), ._4__A3(Memory_In[10]),
    ._5__A4(Memory_In[11]), ._6__A5(Memory_In[12]), ._7__A6(Memory_In[13]), ._8__A7(Memory_In[14]),
    ._9__A8(Memory_In[15]), ._19__nG(and_2_out), ._18___B1(n74245_2__18___b1[0]),
    ._17__B2(n74245_2__18___b1[1]), ._16__B3(n74245_2__18___b1[2]), ._15__B4(n74245_2__18___b1[3]),
    ._14__B5(n74245_2__18___b1[4]), ._13__B6(n74245_2__18___b1[5]), ._12__B7(n74245_2__18___b1[6]),
    ._11__B8(n74245_2__18___b1[7]));  // open: _10__GND, _20__Vcc
  _74245 u_74245_3 (
    ._1__DIR(1'b1), ._2__A1(C_Bus[0]), ._3__A2(C_Bus[1]), ._4__A3(C_Bus[2]), ._5__A4(C_Bus[3]),
    ._6__A5(C_Bus[4]), ._7__A6(C_Bus[5]), ._8__A7(C_Bus[6]), ._9__A8(C_Bus[7]), ._19__nG(and_1_out),
    ._18___B1(n74245_1__18___b1[0]), ._17__B2(n74245_1__18___b1[1]), ._16__B3(n74245_1__18___b1[2]),
    ._15__B4(n74245_1__18___b1[3]), ._14__B5(n74245_1__18___b1[4]), ._13__B6(n74245_1__18___b1[5]),
    ._12__B7(n74245_1__18___b1[6]), ._11__B8(n74245_1__18___b1[7]));  // open: _10__GND, _20__Vcc
  _74245 u_74245_4 (
    ._1__DIR(1'b1), ._2__A1(C_Bus[8]), ._3__A2(C_Bus[9]), ._4__A3(C_Bus[10]), ._5__A4(C_Bus[11]),
    ._6__A5(C_Bus[12]), ._7__A6(C_Bus[13]), ._8__A7(C_Bus[14]), ._9__A8(C_Bus[15]), ._19__nG(and_1_out),
    ._18___B1(n74245_2__18___b1[0]), ._17__B2(n74245_2__18___b1[1]), ._16__B3(n74245_2__18___b1[2]),
    ._15__B4(n74245_2__18___b1[3]), ._14__B5(n74245_2__18___b1[4]), ._13__B6(n74245_2__18___b1[5]),
    ._12__B7(n74245_2__18___b1[6]), ._11__B8(n74245_2__18___b1[7]));  // open: _10__GND, _20__Vcc
  not not_1 (not_1_out, Bus_Select);
  and and_1 (and_1_out, not_1_out, r_0____W_1);
  and and_2 (and_2_out, Bus_Select, r_0____W_1);
  Register16 register16_1 (
    .R___W(r_0____W_1), .Data_In({n74245_2__18___b1, n74245_1__18___b1}), .CLK(CLK),
    .Data_Out(register16_1_data_out), .nEnable(nEnable));
  _74245 u_74245_5 (
    ._1__DIR(1'b1), ._2__A1(register16_1_data_out[0]), ._3__A2(register16_1_data_out[1]),
    ._4__A3(register16_1_data_out[2]), ._5__A4(register16_1_data_out[3]), ._6__A5(register16_1_data_out[4]),
    ._7__A6(register16_1_data_out[5]), ._8__A7(register16_1_data_out[6]), ._9__A8(register16_1_data_out[7]),
    ._19__nG(and_4_out), ._18___B1(Memory_Out[0]), ._17__B2(Memory_Out[1]), ._16__B3(Memory_Out[2]),
    ._15__B4(Memory_Out[3]), ._14__B5(Memory_Out[4]), ._13__B6(Memory_Out[5]), ._12__B7(Memory_Out[6]),
    ._11__B8(Memory_Out[7]));  // open: _10__GND, _20__Vcc
  _74245 u_74245_6 (
    ._1__DIR(1'b1), ._2__A1(register16_1_data_out[8]), ._3__A2(register16_1_data_out[9]),
    ._4__A3(register16_1_data_out[10]), ._5__A4(register16_1_data_out[11]),
    ._6__A5(register16_1_data_out[12]), ._7__A6(register16_1_data_out[13]),
    ._8__A7(register16_1_data_out[14]), ._9__A8(register16_1_data_out[15]), ._19__nG(and_4_out),
    ._18___B1(Memory_Out[8]), ._17__B2(Memory_Out[9]), ._16__B3(Memory_Out[10]), ._15__B4(Memory_Out[11]),
    ._14__B5(Memory_Out[12]), ._13__B6(Memory_Out[13]), ._12__B7(Memory_Out[14]), ._11__B8(Memory_Out[15]));  // open: _10__GND, _20__Vcc
  _74245 u_74245_7 (
    ._1__DIR(1'b1), ._2__A1(register16_1_data_out[0]), ._3__A2(register16_1_data_out[1]),
    ._4__A3(register16_1_data_out[2]), ._5__A4(register16_1_data_out[3]), ._6__A5(register16_1_data_out[4]),
    ._7__A6(register16_1_data_out[5]), ._8__A7(register16_1_data_out[6]), ._9__A8(register16_1_data_out[7]),
    ._19__nG(and_3_out), ._18___B1(A_Bus[0]), ._17__B2(A_Bus[1]), ._16__B3(A_Bus[2]), ._15__B4(A_Bus[3]),
    ._14__B5(A_Bus[4]), ._13__B6(A_Bus[5]), ._12__B7(A_Bus[6]), ._11__B8(A_Bus[7]));  // open: _10__GND, _20__Vcc
  _74245 u_74245_8 (
    ._1__DIR(1'b1), ._2__A1(register16_1_data_out[8]), ._3__A2(register16_1_data_out[9]),
    ._4__A3(register16_1_data_out[10]), ._5__A4(register16_1_data_out[11]),
    ._6__A5(register16_1_data_out[12]), ._7__A6(register16_1_data_out[13]),
    ._8__A7(register16_1_data_out[14]), ._9__A8(register16_1_data_out[15]), ._19__nG(and_3_out),
    ._18___B1(A_Bus[8]), ._17__B2(A_Bus[9]), ._16__B3(A_Bus[10]), ._15__B4(A_Bus[11]), ._14__B5(A_Bus[12]),
    ._13__B6(A_Bus[13]), ._12__B7(A_Bus[14]), ._11__B8(A_Bus[15]));  // open: _10__GND, _20__Vcc
  not not_2 (not_2_out, r_0____W_1);
  not not_3 (not_3_out, Bus_Select);
  and and_3 (and_3_out, not_3_out, not_2_out);
  and and_4 (and_4_out, Bus_Select, not_2_out);
endmodule

module Register16 (
  input  [15:0] Data_In,
  input  CLK,
  input  R___W,
  input  nEnable,
  output [15:0] Data_Out
);

  wire nand_1_out, not_1_out, not_2_out;

  not not_1 (not_1_out, R___W);
  not not_2 (not_2_out, nEnable);
  nand nand_1 (nand_1_out, not_1_out, not_2_out);
  _74374 u_74374_1 (
    .D0__2(Data_In[0]), .D1__3(Data_In[1]), .D2__4(Data_In[2]), .D3__5(Data_In[3]), .D4__6(Data_In[4]),
    .D5__7(Data_In[5]), .D6__8(Data_In[6]), .D7__9(Data_In[7]), .nOE__1(nand_1_out), .CLK__11(CLK),
    .Q0__19(Data_Out[0]), .Q1__18(Data_Out[1]), .Q2__17(Data_Out[2]), .Q3__16(Data_Out[3]),
    .Q4__15(Data_Out[4]), .Q5__14(Data_Out[5]), .Q6__13(Data_Out[6]), .Q7__12(Data_Out[7]));  // open: GND__10, Vcc__20
  _74374 u_74374_2 (
    .D0__2(Data_In[8]), .D1__3(Data_In[9]), .D2__4(Data_In[10]), .D3__5(Data_In[11]), .D4__6(Data_In[12]),
    .D5__7(Data_In[13]), .D6__8(Data_In[14]), .D7__9(Data_In[15]), .nOE__1(nand_1_out), .CLK__11(CLK),
    .Q0__19(Data_Out[8]), .Q1__18(Data_Out[9]), .Q2__17(Data_Out[10]), .Q3__16(Data_Out[11]),
    .Q4__15(Data_Out[12]), .Q5__14(Data_Out[13]), .Q6__13(Data_Out[14]), .Q7__12(Data_Out[15]));  // open: GND__10, Vcc__20
endmodule

module Register24 (
  input  r_0____W_1,
  input  Bus_Select,
  input  nOffset_Enable,
  input  nBase_Enable,
  input  [15:0] Address_In,
  input  [15:0] C_Bus,
  input  CLK,
  output [15:0] Offset_Out,
  output [15:0] A_Bus,
  output [7:0] Segment_Out
);

  wire and_1_out, and_2_out, and_3_out, and_4_out, and_5_out, and_6_out, nand_1_out, nor_1_out, not_1_out,
       not_2_out, not_3_out, not_4_out, not_5_out;
  wire [7:0] n74244_1__3__2y0, n74245_1__18___b1, n74245_4__18___b1, n74374_2_q0__19;
  wire [15:0] n74374_1_q0__19;

  and and_1 (and_1_out, nBase_Enable, r_0____W_1);
  and and_2 (and_2_out, nOffset_Enable, r_0____W_1);
  _74245 u_74245_1 (
    ._1__DIR(1'b1), ._2__A1(Address_In[0]), ._3__A2(Address_In[1]), ._4__A3(Address_In[2]),
    ._5__A4(Address_In[3]), ._6__A5(Address_In[4]), ._7__A6(Address_In[5]), ._8__A7(Address_In[6]),
    ._9__A8(Address_In[7]), ._19__nG(and_3_out), ._18___B1(n74245_1__18___b1[0]),
    ._17__B2(n74245_1__18___b1[1]), ._16__B3(n74245_1__18___b1[2]), ._15__B4(n74245_1__18___b1[3]),
    ._14__B5(n74245_1__18___b1[4]), ._13__B6(n74245_1__18___b1[5]), ._12__B7(n74245_1__18___b1[6]),
    ._11__B8(n74245_1__18___b1[7]));  // open: _10__GND, _20__Vcc
  _74244 u_74244_1 (
    ._1__E1(and_2_out), ._2__1A0(Address_In[11]), ._4__1A1(Address_In[10]), ._6__1A2(Address_In[9]),
    ._8__1A3(Address_In[8]), ._19__E2(and_1_out), ._17__2A0(Address_In[15]), ._15__2A1(Address_In[14]),
    ._13__2A2(Address_In[13]), ._11__2A3(Address_In[12]), ._18__1Y0(n74244_1__3__2y0[7]),
    ._16__1Y1(n74244_1__3__2y0[6]), ._14__1Y2(n74244_1__3__2y0[5]), ._12__1Y3(n74244_1__3__2y0[4]),
    ._3__2Y0(n74244_1__3__2y0[0]), ._5__2Y1(n74244_1__3__2y0[1]), ._7__2Y2(n74244_1__3__2y0[2]),
    ._9__2Y3(n74244_1__3__2y0[3]));  // open: _10__GND, _20__Vcc
  _74245 u_74245_2 (
    ._1__DIR(1'b1), ._2__A1(C_Bus[0]), ._3__A2(C_Bus[1]), ._4__A3(C_Bus[2]), ._5__A4(C_Bus[3]),
    ._6__A5(C_Bus[4]), ._7__A6(C_Bus[5]), ._8__A7(C_Bus[6]), ._9__A8(C_Bus[7]), ._19__nG(and_4_out),
    ._18___B1(n74244_1__3__2y0[0]), ._17__B2(n74244_1__3__2y0[1]), ._16__B3(n74244_1__3__2y0[2]),
    ._15__B4(n74244_1__3__2y0[3]), ._14__B5(n74244_1__3__2y0[4]), ._13__B6(n74244_1__3__2y0[5]),
    ._12__B7(n74244_1__3__2y0[6]), ._11__B8(n74244_1__3__2y0[7]));  // open: _10__GND, _20__Vcc
  _74245 u_74245_3 (
    ._1__DIR(1'b1), ._2__A1(C_Bus[8]), ._3__A2(C_Bus[9]), ._4__A3(C_Bus[10]), ._5__A4(C_Bus[11]),
    ._6__A5(C_Bus[12]), ._7__A6(C_Bus[13]), ._8__A7(C_Bus[14]), ._9__A8(C_Bus[15]), ._19__nG(and_4_out),
    ._18___B1(n74245_1__18___b1[0]), ._17__B2(n74245_1__18___b1[1]), ._16__B3(n74245_1__18___b1[2]),
    ._15__B4(n74245_1__18___b1[3]), ._14__B5(n74245_1__18___b1[4]), ._13__B6(n74245_1__18___b1[5]),
    ._12__B7(n74245_1__18___b1[6]), ._11__B8(n74245_1__18___b1[7]));  // open: _10__GND, _20__Vcc
  _74245 u_74245_4 (
    ._1__DIR(1'b1), ._2__A1(Address_In[0]), ._3__A2(Address_In[1]), ._4__A3(Address_In[2]),
    ._5__A4(Address_In[3]), ._6__A5(Address_In[4]), ._7__A6(Address_In[5]), ._8__A7(Address_In[6]),
    ._9__A8(Address_In[7]), ._19__nG(and_3_out), ._18___B1(n74245_4__18___b1[0]),
    ._17__B2(n74245_4__18___b1[1]), ._16__B3(n74245_4__18___b1[2]), ._15__B4(n74245_4__18___b1[3]),
    ._14__B5(n74245_4__18___b1[4]), ._13__B6(n74245_4__18___b1[5]), ._12__B7(n74245_4__18___b1[6]),
    ._11__B8(n74245_4__18___b1[7]));  // open: _10__GND, _20__Vcc
  _74245 u_74245_5 (
    ._1__DIR(1'b1), ._2__A1(C_Bus[0]), ._3__A2(C_Bus[1]), ._4__A3(C_Bus[2]), ._5__A4(C_Bus[3]),
    ._6__A5(C_Bus[4]), ._7__A6(C_Bus[5]), ._8__A7(C_Bus[6]), ._9__A8(C_Bus[7]), ._19__nG(and_4_out),
    ._18___B1(n74245_4__18___b1[0]), ._17__B2(n74245_4__18___b1[1]), ._16__B3(n74245_4__18___b1[2]),
    ._15__B4(n74245_4__18___b1[3]), ._14__B5(n74245_4__18___b1[4]), ._13__B6(n74245_4__18___b1[5]),
    ._12__B7(n74245_4__18___b1[6]), ._11__B8(n74245_4__18___b1[7]));  // open: _10__GND, _20__Vcc
  and and_3 (and_3_out, Bus_Select, r_0____W_1);
  not not_1 (not_1_out, Bus_Select);
  and and_4 (and_4_out, not_1_out, r_0____W_1);
  not not_2 (not_2_out, r_0____W_1);
  not not_3 (not_3_out, nOffset_Enable);
  nor nor_1 (nor_1_out, nOffset_Enable, nBase_Enable);
  _74374 u_74374_1 (
    .D0__2(n74244_1__3__2y0[0]), .D1__3(n74244_1__3__2y0[1]), .D2__4(n74244_1__3__2y0[2]),
    .D3__5(n74244_1__3__2y0[3]), .D4__6(n74244_1__3__2y0[4]), .D5__7(n74244_1__3__2y0[5]),
    .D6__8(n74244_1__3__2y0[6]), .D7__9(n74244_1__3__2y0[7]), .nOE__1(nand_1_out), .CLK__11(CLK),
    .Q0__19(n74374_1_q0__19[0]), .Q1__18(n74374_1_q0__19[1]), .Q2__17(n74374_1_q0__19[2]),
    .Q3__16(n74374_1_q0__19[3]), .Q4__15(n74374_1_q0__19[4]), .Q5__14(n74374_1_q0__19[5]),
    .Q6__13(n74374_1_q0__19[6]), .Q7__12(n74374_1_q0__19[7]));  // open: GND__10, Vcc__20
  nand nand_1 (nand_1_out, not_2_out, not_3_out);
  _74374 u_74374_2 (
    .D0__2(n74245_4__18___b1[0]), .D1__3(n74245_4__18___b1[1]), .D2__4(n74245_4__18___b1[2]),
    .D3__5(n74245_4__18___b1[3]), .D4__6(n74245_4__18___b1[4]), .D5__7(n74245_4__18___b1[5]),
    .D6__8(n74245_4__18___b1[6]), .D7__9(n74245_4__18___b1[7]), .nOE__1(nBase_Enable), .CLK__11(CLK),
    .Q0__19(n74374_2_q0__19[0]), .Q1__18(n74374_2_q0__19[1]), .Q2__17(n74374_2_q0__19[2]),
    .Q3__16(n74374_2_q0__19[3]), .Q4__15(n74374_2_q0__19[4]), .Q5__14(n74374_2_q0__19[5]),
    .Q6__13(n74374_2_q0__19[6]), .Q7__12(n74374_2_q0__19[7]));  // open: GND__10, Vcc__20
  _74374 u_74374_3 (
    .D0__2(n74245_1__18___b1[0]), .D1__3(n74245_1__18___b1[1]), .D2__4(n74245_1__18___b1[2]),
    .D3__5(n74245_1__18___b1[3]), .D4__6(n74245_1__18___b1[4]), .D5__7(n74245_1__18___b1[5]),
    .D6__8(n74245_1__18___b1[6]), .D7__9(n74245_1__18___b1[7]), .nOE__1(nand_1_out), .CLK__11(CLK),
    .Q0__19(n74374_1_q0__19[8]), .Q1__18(n74374_1_q0__19[9]), .Q2__17(n74374_1_q0__19[10]),
    .Q3__16(n74374_1_q0__19[11]), .Q4__15(n74374_1_q0__19[12]), .Q5__14(n74374_1_q0__19[13]),
    .Q6__13(n74374_1_q0__19[14]), .Q7__12(n74374_1_q0__19[15]));  // open: GND__10, Vcc__20
  _74245 u_74245_6 (
    ._1__DIR(1'b0), ._2__A1(1'b0), ._3__A2(1'b0), ._4__A3(1'b0), ._5__A4(1'b0), ._6__A5(1'b0), ._7__A6(1'b0),
    ._8__A7(1'b0), ._9__A8(1'b0), ._19__nG(nBase_Enable), ._18___B1(A_Bus[8]), ._17__B2(A_Bus[9]),
    ._16__B3(A_Bus[10]), ._15__B4(A_Bus[11]), ._14__B5(A_Bus[12]), ._13__B6(A_Bus[13]), ._12__B7(A_Bus[14]),
    ._11__B8(A_Bus[15]));  // open: _10__GND, _20__Vcc
  not not_4 (not_4_out, r_0____W_1);
  _74245 u_74245_7 (
    ._1__DIR(1'b1), ._2__A1(n74374_1_q0__19[0]), ._3__A2(n74374_1_q0__19[1]), ._4__A3(n74374_1_q0__19[2]),
    ._5__A4(n74374_1_q0__19[3]), ._6__A5(n74374_1_q0__19[4]), ._7__A6(n74374_1_q0__19[5]),
    ._8__A7(n74374_1_q0__19[6]), ._9__A8(n74374_1_q0__19[7]), ._19__nG(and_6_out), ._18___B1(Offset_Out[0]),
    ._17__B2(Offset_Out[1]), ._16__B3(Offset_Out[2]), ._15__B4(Offset_Out[3]), ._14__B5(Offset_Out[4]),
    ._13__B6(Offset_Out[5]), ._12__B7(Offset_Out[6]), ._11__B8(Offset_Out[7]));  // open: _10__GND, _20__Vcc
  _74245 u_74245_8 (
    ._1__DIR(1'b1), ._2__A1(n74374_1_q0__19[8]), ._3__A2(n74374_1_q0__19[9]), ._4__A3(n74374_1_q0__19[10]),
    ._5__A4(n74374_1_q0__19[11]), ._6__A5(n74374_1_q0__19[12]), ._7__A6(n74374_1_q0__19[13]),
    ._8__A7(n74374_1_q0__19[14]), ._9__A8(n74374_1_q0__19[15]), ._19__nG(and_6_out),
    ._18___B1(Offset_Out[8]), ._17__B2(Offset_Out[9]), ._16__B3(Offset_Out[10]), ._15__B4(Offset_Out[11]),
    ._14__B5(Offset_Out[12]), ._13__B6(Offset_Out[13]), ._12__B7(Offset_Out[14]), ._11__B8(Offset_Out[15]));  // open: _10__GND, _20__Vcc
  _74245 u_74245_9 (
    ._1__DIR(1'b1), ._2__A1(n74374_1_q0__19[0]), ._3__A2(n74374_1_q0__19[1]), ._4__A3(n74374_1_q0__19[2]),
    ._5__A4(n74374_1_q0__19[3]), ._6__A5(n74374_1_q0__19[4]), ._7__A6(n74374_1_q0__19[5]),
    ._8__A7(n74374_1_q0__19[6]), ._9__A8(n74374_1_q0__19[7]), ._19__nG(and_5_out), ._18___B1(A_Bus[0]),
    ._17__B2(A_Bus[1]), ._16__B3(A_Bus[2]), ._15__B4(A_Bus[3]), ._14__B5(A_Bus[4]), ._13__B6(A_Bus[5]),
    ._12__B7(A_Bus[6]), ._11__B8(A_Bus[7]));  // open: _10__GND, _20__Vcc
  _74245 u_74245_10 (
    ._1__DIR(1'b1), ._2__A1(n74374_1_q0__19[8]), ._3__A2(n74374_1_q0__19[9]), ._4__A3(n74374_1_q0__19[10]),
    ._5__A4(n74374_1_q0__19[11]), ._6__A5(n74374_1_q0__19[12]), ._7__A6(n74374_1_q0__19[13]),
    ._8__A7(n74374_1_q0__19[14]), ._9__A8(n74374_1_q0__19[15]), ._19__nG(and_5_out), ._18___B1(A_Bus[8]),
    ._17__B2(A_Bus[9]), ._16__B3(A_Bus[10]), ._15__B4(A_Bus[11]), ._14__B5(A_Bus[12]), ._13__B6(A_Bus[13]),
    ._12__B7(A_Bus[14]), ._11__B8(A_Bus[15]));  // open: _10__GND, _20__Vcc
  _74245 u_74245_11 (
    ._1__DIR(1'b1), ._2__A1(n74374_2_q0__19[0]), ._3__A2(n74374_2_q0__19[1]), ._4__A3(n74374_2_q0__19[2]),
    ._5__A4(n74374_2_q0__19[3]), ._6__A5(n74374_2_q0__19[4]), ._7__A6(n74374_2_q0__19[5]),
    ._8__A7(n74374_2_q0__19[6]), ._9__A8(n74374_2_q0__19[7]), ._19__nG(and_6_out), ._18___B1(Segment_Out[0]),
    ._17__B2(Segment_Out[1]), ._16__B3(Segment_Out[2]), ._15__B4(Segment_Out[3]), ._14__B5(Segment_Out[4]),
    ._13__B6(Segment_Out[5]), ._12__B7(Segment_Out[6]), ._11__B8(Segment_Out[7]));  // open: _10__GND, _20__Vcc
  _74245 u_74245_12 (
    ._1__DIR(1'b1), ._2__A1(n74374_2_q0__19[0]), ._3__A2(n74374_2_q0__19[1]), ._4__A3(n74374_2_q0__19[2]),
    ._5__A4(n74374_2_q0__19[3]), ._6__A5(n74374_2_q0__19[4]), ._7__A6(n74374_2_q0__19[5]),
    ._8__A7(n74374_2_q0__19[6]), ._9__A8(n74374_2_q0__19[7]), ._19__nG(and_5_out), ._18___B1(A_Bus[0]),
    ._17__B2(A_Bus[1]), ._16__B3(A_Bus[2]), ._15__B4(A_Bus[3]), ._14__B5(A_Bus[4]), ._13__B6(A_Bus[5]),
    ._12__B7(A_Bus[6]), ._11__B8(A_Bus[7]));  // open: _10__GND, _20__Vcc
  not not_5 (not_5_out, Bus_Select);
  and and_5 (and_5_out, not_5_out, not_4_out);
  and and_6 (and_6_out, Bus_Select, not_4_out);
  LED Write_Fault (.in(nor_1_out));
  // also tied to GND on the sheet: {Address_In[8], Address_In[9], Address_In[10], Address_In[11], Address_In[12], Address_In[13], Address_In[14], Address_In[15], C_Bus[8], C_Bus[9], C_Bus[10], C_Bus[11], C_Bus[12], C_Bus[13], C_Bus[14], C_Bus[15]}

  // Notes on the sheet:
  //   Segment
  //   Offset
endmodule
