// Logisim project 74LS283.circ as structural Verilog: 1 circuit, main circuit 74LS283
module _74LS283 (
  input  _7__C0,
  input  _5__A1,
  input  _6__B1,
  input  _3__A2,
  input  _2__B2,
  input  _14__A3,
  input  _15__B3,
  input  _12__A4,
  input  _11__B4,
  input  _8__GND,
  input  _16__Vcc,
  output _4__S1,
  output _1__S2,
  output _13__S3,
  output _10__S4,
  output _9__C4
);

  wire _2_out, _3_out, _5_out, _6_out, _7_out, _9_out, _10_out, _11_out, _12_out, _14_out, _15_out, _16_out,
       _17_out, _18_out, buffer_1_out, buffer_2_out, buffer_3_out, buffer_4_out, nand_1_out, nand_2_out,
       nand_3_out, nand_4_out, nor_1_out, nor_2_out, nor_3_out, nor_4_out, nor_5_out, nor_6_out, nor_7_out,
       not_1_out, not_2_out;

  not not_1 (not_1_out, _7__C0);
  nor nor_1 (nor_1_out, _5__A1, _6__B1);
  nand nand_1 (nand_1_out, _5__A1, _6__B1);
  nor nor_2 (nor_2_out, _3__A2, _2__B2);
  nand nand_2 (nand_2_out, _3__A2, _2__B2);
  nor nor_3 (nor_3_out, _14__A3, _15__B3);
  nand nand_3 (nand_3_out, _14__A3, _15__B3);
  nor nor_4 (nor_4_out, _12__A4, _11__B4);
  nand nand_4 (nand_4_out, _12__A4, _11__B4);
  not not_2 (not_2_out, not_1_out);
  and _2 (_2_out, ~nor_1_out, nand_1_out);  // AND_Gate
  and _3 (_3_out, not_1_out, nand_1_out);
  buf buffer_1 (buffer_1_out, nor_1_out);
  and _5 (_5_out, ~nor_2_out, nand_2_out);  // AND_Gate
  and _6 (_6_out, not_1_out, nand_1_out, nand_2_out);
  and _7 (_7_out, nand_2_out, nor_1_out);
  buf buffer_2 (buffer_2_out, nor_2_out);
  and _9 (_9_out, ~nor_3_out, nand_3_out);  // AND_Gate
  and _10 (_10_out, not_1_out, nand_1_out, nand_2_out, nand_3_out);
  and _11 (_11_out, nand_2_out, nand_3_out, nor_1_out);
  and _12 (_12_out, nand_3_out, nor_2_out);
  buf buffer_3 (buffer_3_out, nor_3_out);
  and _14 (_14_out, ~nor_4_out, nand_4_out);  // AND_Gate
  and _15 (_15_out, not_1_out, nand_1_out, nand_2_out, nand_3_out, nand_4_out);
  and _16 (_16_out, nand_2_out, nand_3_out, nand_4_out, nor_1_out);
  and _17 (_17_out, nand_3_out, nand_4_out, nor_2_out);
  and _18 (_18_out, nand_4_out, nor_3_out);
  buf buffer_4 (buffer_4_out, nor_4_out);
  nor nor_5 (nor_5_out, _3_out, buffer_1_out);
  nor nor_6 (nor_6_out, _6_out, _7_out, buffer_2_out);
  nor nor_7 (nor_7_out, _10_out, _11_out, _12_out, buffer_3_out);
  nor nor_8 (_9__C4, _15_out, _16_out, _17_out, _18_out, buffer_4_out);
  xor xor_1 (_4__S1, not_2_out, _2_out);
  xor xor_2 (_1__S2, nor_5_out, _5_out);
  xor xor_3 (_13__S3, nor_6_out, _9_out);
  xor xor_4 (_10__S4, nor_7_out, _14_out);
endmodule
