// Logisim project ALU Rev II.circ as structural Verilog: 2 circuits, main circuit ALU
module ALU (
  input  F0,
  input  Increment,
  input  F1,
  input  Invert_A,
  input  F2,
  input  [15:0] A_Bus,
  input  [15:0] B_Bus,
  input  Enable_A,
  input  Enable_B,
  output [15:0] C_Bus,
  output Carry,
  output Zero,
  output Negative,
  output Positive,
  output Overflow
);

  wire and_1_out, and_2_out, and_3_out, and_4_out, and_5_out, and_6_out, and_7_out, and_8_out,
       n4_bit_alu_1_p11, n4_bit_alu_2_p7, n4_bit_alu_2_p11, n4_bit_alu_4_p11, n74521_1__19__no__a_b,
       n74521_2__19__no__a_b, not_1_out, not_2_out, not_3_out, not_4_out, not_5_out, not_6_out, not_7_out,
       or_1_out, or_2_out, or_3_out, or_4_out, or_6_out;
  wire [2:0] undriven_3;
  wire [3:0] undriven_2;
  wire [7:0] buffer_1_out, buffer_2_out, n74245_1__18___b1, n74245_2__18___b1, n74245_3__18___b1,
       n74245_4__18___b1, undriven;

  _74245 u_74245_1 (
    ._1__DIR(1'b1), ._2__A1(undriven[7]), ._3__A2(undriven_2[0]), ._4__A3(undriven_2[1]),
    ._5__A4(undriven_2[2]), ._6__A5(undriven_2[3]), ._7__A6(undriven_3[0]), ._8__A7(undriven_3[1]),
    ._9__A8(undriven_3[2]), ._19__nG(or_1_out), ._18___B1(n74245_1__18___b1[0]),
    ._17__B2(n74245_1__18___b1[1]), ._16__B3(n74245_1__18___b1[2]), ._15__B4(n74245_1__18___b1[3]),
    ._14__B5(n74245_1__18___b1[4]), ._13__B6(n74245_1__18___b1[5]), ._12__B7(n74245_1__18___b1[6]),
    ._11__B8(n74245_1__18___b1[7]));  // open: _10__GND, _20__Vcc
  assign buffer_1_out = n74245_1__18___b1;  // Buffer buffer_1, 8 bits wide
  assign buffer_2_out = n74245_2__18___b1;  // Buffer buffer_2, 8 bits wide
  _74245 u_74245_2 (
    ._1__DIR(1'b1), ._2__A1(1'b0), ._3__A2(undriven[0]), ._4__A3(undriven[1]), ._5__A4(undriven[2]),
    ._6__A5(undriven[3]), ._7__A6(undriven[4]), ._8__A7(undriven[5]), ._9__A8(undriven[6]),
    ._19__nG(or_1_out), ._18___B1(n74245_2__18___b1[0]), ._17__B2(n74245_2__18___b1[1]),
    ._16__B3(n74245_2__18___b1[2]), ._15__B4(n74245_2__18___b1[3]), ._14__B5(n74245_2__18___b1[4]),
    ._13__B6(n74245_2__18___b1[5]), ._12__B7(n74245_2__18___b1[6]), ._11__B8(n74245_2__18___b1[7]));  // open: _10__GND, _20__Vcc
  // _4_Bit_ALU 4_bit_alu_1: pin names not known; wires that end beside it: Enable_A, A_Bus[0], A_Bus[1], A_Bus[2], A_Bus[3], Invert_A, Increment, F0, F1, F2, n4_bit_alu_1_p11, Enable_B, B_Bus[0], B_Bus[1], B_Bus[2], B_Bus[3]
  // _4_Bit_ALU 4_bit_alu_2: pin names not known; wires that end beside it: Enable_A, A_Bus[8], A_Bus[9], A_Bus[10], A_Bus[11], Invert_A, n4_bit_alu_2_p7, F0, F1, F2, n4_bit_alu_2_p11, Enable_B, B_Bus[8], B_Bus[9], B_Bus[10], B_Bus[11]
  _74245 u_74245_3 (
    ._1__DIR(1'b1), ._2__A1(undriven_2[1]), ._3__A2(undriven_2[2]), ._4__A3(undriven_2[3]),
    ._5__A4(undriven_3[0]), ._6__A5(undriven_3[1]), ._7__A6(undriven_3[2]), ._8__A7(Negative), ._9__A8(1'b0),
    ._19__nG(or_2_out), ._18___B1(n74245_3__18___b1[0]), ._17__B2(n74245_3__18___b1[1]),
    ._16__B3(n74245_3__18___b1[2]), ._15__B4(n74245_3__18___b1[3]), ._14__B5(n74245_3__18___b1[4]),
    ._13__B6(n74245_3__18___b1[5]), ._12__B7(n74245_3__18___b1[6]), ._11__B8(n74245_3__18___b1[7]));  // open: _10__GND, _20__Vcc
  assign buffer_1_out = n74245_3__18___b1;  // Buffer buffer_3, 8 bits wide
  assign buffer_2_out = n74245_4__18___b1;  // Buffer buffer_4, 8 bits wide
  // _4_Bit_ALU 4_bit_alu_3: pin names not known; wires that end beside it: Enable_A, A_Bus[4], A_Bus[5], A_Bus[6], A_Bus[7], Invert_A, n4_bit_alu_1_p11, F0, F1, F2, n4_bit_alu_2_p7, Enable_B, B_Bus[4], B_Bus[5], B_Bus[6], B_Bus[7]
  // _4_Bit_ALU 4_bit_alu_4: pin names not known; wires that end beside it: Enable_A, A_Bus[12], A_Bus[13], A_Bus[14], A_Bus[15], Invert_A, n4_bit_alu_2_p11, F0, F1, F2, n4_bit_alu_4_p11, Enable_B, B_Bus[12], B_Bus[13], B_Bus[14], B_Bus[15]
  and and_1 (and_1_out, undriven[0], F1);
  _74245 u_74245_4 (
    ._1__DIR(1'b1), ._2__A1(undriven[1]), ._3__A2(undriven[2]), ._4__A3(undriven[3]), ._5__A4(undriven[4]),
    ._6__A5(undriven[5]), ._7__A6(undriven[6]), ._8__A7(undriven[7]), ._9__A8(undriven_2[0]),
    ._19__nG(or_2_out), ._18___B1(n74245_4__18___b1[0]), ._17__B2(n74245_4__18___b1[1]),
    ._16__B3(n74245_4__18___b1[2]), ._15__B4(n74245_4__18___b1[3]), ._14__B5(n74245_4__18___b1[4]),
    ._13__B6(n74245_4__18___b1[5]), ._12__B7(n74245_4__18___b1[6]), ._11__B8(n74245_4__18___b1[7]));  // open: _10__GND, _20__Vcc
  or or_1 (or_1_out, not_1_out, not_2_out);
  or or_2 (or_2_out, not_2_out, not_3_out);
  not not_1 (not_1_out, F0);
  not not_2 (not_2_out, F2);
  _74245 u_74245_5 (
    ._1__DIR(not_6_out), ._2__A1(undriven_2[0]), ._3__A2(undriven_2[1]), ._4__A3(undriven_2[2]),
    ._5__A4(undriven_2[3]), ._6__A5(undriven_3[0]), ._7__A6(undriven_3[1]), ._8__A7(undriven_3[2]),
    ._9__A8(Negative), ._19__nG(1'b0), ._18___B1(C_Bus[0]), ._17__B2(C_Bus[1]), ._16__B3(C_Bus[2]),
    ._15__B4(C_Bus[3]), ._14__B5(C_Bus[4]), ._13__B6(C_Bus[5]), ._12__B7(C_Bus[6]), ._11__B8(C_Bus[7]));  // open: _10__GND, _20__Vcc
  not not_3 (not_3_out, F1);
  and and_2 (and_2_out, F1, Negative);
  or or_3 (or_3_out, and_1_out, and_2_out);
  _74521 u_74521_1 (
    ._2__A0(undriven[0]), ._3__B0(1'b0), ._4__A1(undriven[1]), ._5__B1(1'b0), ._6__A2(undriven[2]),
    ._7__B2(1'b0), ._8__A3(undriven[3]), ._9__B3(1'b0), ._11__A4(undriven_3[0]), ._12__B4(1'b0),
    ._13__A5(undriven_3[1]), ._14__B5(1'b0), ._15__A6(undriven_3[2]), ._16__B6(1'b0), ._17__A7(Negative),
    ._18__B7(1'b0), ._1__nI__A_B(1'b0), ._19__nO__A_B(n74521_1__19__no__a_b));  // open: _20__Vcc, _10__GND
  _74521 u_74521_2 (
    ._2__A0(undriven[4]), ._3__B0(1'b0), ._4__A1(undriven[5]), ._5__B1(1'b0), ._6__A2(undriven[6]),
    ._7__B2(1'b0), ._8__A3(undriven[7]), ._9__B3(1'b0), ._11__A4(undriven_2[0]), ._12__B4(1'b0),
    ._13__A5(undriven_2[1]), ._14__B5(1'b0), ._15__A6(undriven_2[2]), ._16__B6(1'b0),
    ._17__A7(undriven_2[3]), ._18__B7(1'b0), ._1__nI__A_B(1'b0), ._19__nO__A_B(n74521_2__19__no__a_b));  // open: _20__Vcc, _10__GND
  not not_4 (not_4_out, A_Bus[15]);
  and and_3 (and_3_out, not_4_out, not_5_out);
  not not_5 (not_5_out, B_Bus[15]);
  and and_4 (and_4_out, B_Bus[15], B_Bus[15]);
  and and_5 (and_5_out, F2, or_4_out);
  or or_4 (or_4_out, F1, F0);
  _74245 u_74245_6 (
    ._1__DIR(not_6_out), ._2__A1(undriven[0]), ._3__A2(undriven[1]), ._4__A3(undriven[2]),
    ._5__A4(undriven[3]), ._6__A5(undriven[4]), ._7__A6(undriven[5]), ._8__A7(undriven[6]),
    ._9__A8(undriven[7]), ._19__nG(1'b0), ._18___B1(C_Bus[8]), ._17__B2(C_Bus[9]), ._16__B3(C_Bus[10]),
    ._15__B4(C_Bus[11]), ._14__B5(C_Bus[12]), ._13__B6(C_Bus[13]), ._12__B7(C_Bus[14]), ._11__B8(C_Bus[15]));  // open: _10__GND, _20__Vcc
  not not_6 (not_6_out, and_5_out);
  not not_7 (not_7_out, Negative);
  _74245 u_74245_7 (
    ._1__DIR(and_5_out), ._2__A1(buffer_1_out[0]), ._3__A2(buffer_1_out[1]), ._4__A3(buffer_1_out[2]),
    ._5__A4(buffer_1_out[3]), ._6__A5(buffer_1_out[4]), ._7__A6(buffer_1_out[5]), ._8__A7(buffer_1_out[6]),
    ._9__A8(buffer_1_out[7]), ._19__nG(1'b0), ._18___B1(C_Bus[0]), ._17__B2(C_Bus[1]), ._16__B3(C_Bus[2]),
    ._15__B4(C_Bus[3]), ._14__B5(C_Bus[4]), ._13__B6(C_Bus[5]), ._12__B7(C_Bus[6]), ._11__B8(C_Bus[7]));  // open: _10__GND, _20__Vcc
  and and_6 (and_6_out, and_5_out, or_3_out);
  or or_5 (Carry, n4_bit_alu_4_p11, and_6_out);
  or or_6 (or_6_out, n74521_1__19__no__a_b, n74521_2__19__no__a_b);
  not not_8 (Zero, or_6_out);
  and and_7 (and_7_out, Negative, and_3_out);
  and and_8 (and_8_out, not_7_out, and_4_out);
  _74245 u_74245_8 (
    ._1__DIR(and_5_out), ._2__A1(buffer_2_out[0]), ._3__A2(buffer_2_out[1]), ._4__A3(buffer_2_out[2]),
    ._5__A4(buffer_2_out[3]), ._6__A5(buffer_2_out[4]), ._7__A6(buffer_2_out[5]), ._8__A7(buffer_2_out[6]),
    ._9__A8(buffer_2_out[7]), ._19__nG(1'b0), ._18___B1(C_Bus[8]), ._17__B2(C_Bus[9]), ._16__B3(C_Bus[10]),
    ._15__B4(C_Bus[11]), ._14__B5(C_Bus[12]), ._13__B6(C_Bus[13]), ._12__B7(C_Bus[14]), ._11__B8(C_Bus[15]));  // open: _10__GND, _20__Vcc
  nor nor_1 (Positive, Zero, Negative);
  or or_7 (Overflow, and_7_out, and_8_out);

  // Notes on the sheet:
  //   Shift Left
  //   Shift Right
  //   ALU Select
  //   F0 | F1 | F2 | ENA | ENB | INVA | INC || FUNC
  //   ---------------------------------------------
  //    0 |  1 |  0 |  1  |  0  |  0   |  0  || A
  //    0 |  1 |  0 |  0  |  1  |  0   |  0  || B
  //    0 |  1 |  0 |  1  |  0  |  1   |  0  || !A
  //    1 |  0 |  0 |  1  |  1  |  0   |  0  || !B
  //    1 |  1 |  0 |  1  |  1  |  0   |  0  || A + B
  //    1 |  1 |  0 |  1  |  1  |  0   |  1  || A + B + 1
  //    1 |  1 |  0 |  1  |  0  |  0   |  1  || A + 1
  //    1 |  1 |  0 |  0  |  1  |  0   |  1  || B + 1
  //    1 |  1 |  0 |  1  |  1  |  1   |  1  || B - A
  //    1 |  1 |  0 |  0  |  1  |  1   |  0  || B - 1
  //    1 |  1 |  0 |  1  |  0  |  1   |  1  || -A
  //    0 |  0 |  0 |  1  |  1  |  0   |  0  || A AND B
  //    0 |  1 |  0 |  1  |  1  |  0   |  0  || A OR B
  //    0 |  1 |  0 |  0  |  0  |  0   |  0  || 0
  //    1 |  1 |  0 |  0  |  0  |  0   |  1  || 1
  //    1 |  1 |  0 |  0  |  0  |  1   |  0  || -1
  //    0 |  0 |  1 |  1  |  1  |  0   |  0  || XOR
  //    0 |  1 |  1 |  1  |  0  |  0   |  0  || A SR 1
  //    1 |  0 |  1 |  1  |  0  |  0   |  0  || A SL 1
  //   Shift Select
endmodule

module Test (
  input  [7:0] in_1,
  input  in_2,
  output [7:0] out_3
);

  wire not_1_out;

  _74245 u_74245_1 (
    ._1__DIR(1'b1), ._2__A1(1'b0), ._3__A2(in_1[0]), ._4__A3(in_1[1]), ._5__A4(in_1[2]), ._6__A5(in_1[3]),
    ._7__A6(in_1[4]), ._8__A7(in_1[5]), ._9__A8(in_1[6]), ._19__nG(not_1_out), ._18___B1(out_3[0]),
    ._17__B2(out_3[1]), ._16__B3(out_3[2]), ._15__B4(out_3[3]), ._14__B5(out_3[4]), ._13__B6(out_3[5]),
    ._12__B7(out_3[6]), ._11__B8(out_3[7]));  // open: _10__GND, _20__Vcc
  _74245 u_74245_2 (
    ._1__DIR(1'b1), ._2__A1(in_1[1]), ._3__A2(in_1[2]), ._4__A3(in_1[3]), ._5__A4(in_1[4]), ._6__A5(in_1[5]),
    ._7__A6(in_1[6]), ._8__A7(in_1[7]), ._9__A8(1'b0), ._19__nG(in_2), ._18___B1(out_3[0]),
    ._17__B2(out_3[1]), ._16__B3(out_3[2]), ._15__B4(out_3[3]), ._14__B5(out_3[4]), ._13__B6(out_3[5]),
    ._12__B7(out_3[6]), ._11__B8(out_3[7]));  // open: _10__GND, _20__Vcc
  not not_1 (not_1_out, in_2);
endmodule
