// Logisim project ALU.circ as structural Verilog
module ALU (
  input  F0,
  input  F1,
  input  F2,
  input  F3,
  input  [15:0] A_Bus,
  input  [15:0] B_Bus,
  input  Enable_A,
  input  Enable_B,
  input  Increment,
  output [15:0] C_Bus,
  output Carry,
  output Zero,
  output Negative,
  output Positive,
  output Overflow
);

  wire alu_4_bit_1_carry_out, alu_4_bit_2_carry_out, alu_4_bit_3_carry_out, alu_4_bit_4_carry_out, and_1_out,
       and_2_out, and_3_out, and_4_out, and_5_out, and_6_out, n74521_1__19__no__a_b, n74521_2__19__no__a_b,
       not_1_out, or_1_out;
  wire [3:0] alu_4_bit_1_s1, alu_4_bit_3_s1;
  wire [6:0] alu_4_bit_2_s1;

  // Probe on A_Bus
  _74245 u_74245_1 (
    ._1__DIR(F3), ._2__A1(A_Bus[7]), ._3__A2(A_Bus[8]), ._4__A3(A_Bus[9]), ._5__A4(A_Bus[10]),
    ._6__A5(A_Bus[11]), ._7__A6(A_Bus[12]), ._8__A7(A_Bus[13]), ._9__A8(A_Bus[14]), ._19__nG(and_3_out),
    ._18___B1(C_Bus[8]), ._17__B2(C_Bus[9]), ._16__B3(C_Bus[10]), ._15__B4(C_Bus[11]), ._14__B5(C_Bus[12]),
    ._13__B6(C_Bus[13]), ._12__B7(C_Bus[14]), ._11__B8(C_Bus[15]));  // open: _10__GND, _20__Vcc
  // Probe on B_Bus
  _74245 u_74245_2 (
    ._1__DIR(F3), ._2__A1(1'b0), ._3__A2(A_Bus[0]), ._4__A3(A_Bus[1]), ._5__A4(A_Bus[2]), ._6__A5(A_Bus[3]),
    ._7__A6(A_Bus[4]), ._8__A7(A_Bus[5]), ._9__A8(A_Bus[6]), ._19__nG(and_3_out), ._18___B1(C_Bus[0]),
    ._17__B2(C_Bus[1]), ._16__B3(C_Bus[2]), ._15__B4(C_Bus[3]), ._14__B5(C_Bus[4]), ._13__B6(C_Bus[5]),
    ._12__B7(C_Bus[6]), ._11__B8(C_Bus[7]));  // open: _10__GND, _20__Vcc
  ALU_4_Bit alu_4_bit_1 (
    .F0(F0), .F1(F1), .F2(F2), .INC(Increment), .ENA(Enable_A), .A1(A_Bus[0]), .A2(A_Bus[1]), .A3(A_Bus[2]),
    .A4(A_Bus[3]), .ENB(Enable_B), .B1(B_Bus[0]), .B2(B_Bus[1]), .B3(B_Bus[2]), .B4(B_Bus[3]),
    .Carry_Out(alu_4_bit_1_carry_out), .S1(alu_4_bit_1_s1[0]), .S2(alu_4_bit_1_s1[1]),
    .S3(alu_4_bit_1_s1[2]), .S4(alu_4_bit_1_s1[3]));  // open: Overflow
  ALU_4_Bit alu_4_bit_2 (
    .F0(F0), .F1(F1), .F2(F2), .INC(alu_4_bit_3_carry_out), .ENA(Enable_A), .A1(A_Bus[8]), .A2(A_Bus[9]),
    .A3(A_Bus[10]), .A4(A_Bus[11]), .ENB(Enable_B), .B1(B_Bus[8]), .B2(B_Bus[9]), .B3(B_Bus[10]),
    .B4(B_Bus[11]), .Carry_Out(alu_4_bit_2_carry_out), .S1(alu_4_bit_2_s1[0]), .S2(alu_4_bit_2_s1[1]),
    .S3(alu_4_bit_2_s1[2]), .S4(alu_4_bit_2_s1[3]));  // open: Overflow
  and and_1 (and_1_out, F2, A_Bus[15]);
  _74245 u_74245_3 (
    ._1__DIR(F3), ._2__A1(A_Bus[9]), ._3__A2(A_Bus[10]), ._4__A3(A_Bus[11]), ._5__A4(A_Bus[12]),
    ._6__A5(A_Bus[13]), ._7__A6(A_Bus[14]), ._8__A7(A_Bus[15]), ._9__A8(and_1_out), ._19__nG(and_4_out),
    ._18___B1(C_Bus[8]), ._17__B2(C_Bus[9]), ._16__B3(C_Bus[10]), ._15__B4(C_Bus[11]), ._14__B5(C_Bus[12]),
    ._13__B6(C_Bus[13]), ._12__B7(C_Bus[14]), ._11__B8(C_Bus[15]));  // open: _10__GND, _20__Vcc
  ALU_4_Bit alu_4_bit_3 (
    .F0(F0), .F1(F1), .F2(F2), .INC(alu_4_bit_1_carry_out), .ENA(Enable_A), .A1(A_Bus[4]), .A2(A_Bus[5]),
    .A3(A_Bus[6]), .A4(A_Bus[7]), .ENB(Enable_B), .B1(B_Bus[4]), .B2(B_Bus[5]), .B3(B_Bus[6]), .B4(B_Bus[7]),
    .Carry_Out(alu_4_bit_3_carry_out), .S1(alu_4_bit_3_s1[0]), .S2(alu_4_bit_3_s1[1]),
    .S3(alu_4_bit_3_s1[2]), .S4(alu_4_bit_3_s1[3]));  // open: Overflow
  ALU_4_Bit alu_4_bit_4 (
    .F0(F0), .F1(F1), .F2(F2), .INC(alu_4_bit_2_carry_out), .ENA(Enable_A), .A1(A_Bus[12]), .A2(A_Bus[13]),
    .A3(A_Bus[14]), .A4(A_Bus[15]), .ENB(Enable_B), .B1(B_Bus[12]), .B2(B_Bus[13]), .B3(B_Bus[14]),
    .B4(B_Bus[15]), .Carry_Out(alu_4_bit_4_carry_out), .Overflow(Overflow), .S1(alu_4_bit_2_s1[4]),
    .S2(alu_4_bit_2_s1[5]), .S3(alu_4_bit_2_s1[6]), .S4(Negative));
  and and_2 (and_2_out, A_Bus[0], F0);
  _74245 u_74245_4 (
    ._1__DIR(F3), ._2__A1(A_Bus[1]), ._3__A2(A_Bus[2]), ._4__A3(A_Bus[3]), ._5__A4(A_Bus[4]),
    ._6__A5(A_Bus[5]), ._7__A6(A_Bus[6]), ._8__A7(A_Bus[7]), ._9__A8(A_Bus[8]), ._19__nG(and_4_out),
    ._18___B1(C_Bus[0]), ._17__B2(C_Bus[1]), ._16__B3(C_Bus[2]), ._15__B4(C_Bus[3]), ._14__B5(C_Bus[4]),
    ._13__B6(C_Bus[5]), ._12__B7(C_Bus[6]), ._11__B8(C_Bus[7]));  // open: _10__GND, _20__Vcc
  and and_3 (and_3_out, F0, F3);
  and and_4 (and_4_out, F3, F1);
  not not_1 (not_1_out, F3);
  and and_5 (and_5_out, F1, A_Bus[15]);
  _74245 u_74245_5 (
    ._1__DIR(not_1_out), ._2__A1(alu_4_bit_1_s1[0]), ._3__A2(alu_4_bit_1_s1[1]), ._4__A3(alu_4_bit_1_s1[2]),
    ._5__A4(alu_4_bit_1_s1[3]), ._6__A5(alu_4_bit_3_s1[0]), ._7__A6(alu_4_bit_3_s1[1]),
    ._8__A7(alu_4_bit_3_s1[2]), ._9__A8(alu_4_bit_3_s1[3]), ._19__nG(1'b0), ._18___B1(C_Bus[0]),
    ._17__B2(C_Bus[1]), ._16__B3(C_Bus[2]), ._15__B4(C_Bus[3]), ._14__B5(C_Bus[4]), ._13__B6(C_Bus[5]),
    ._12__B7(C_Bus[6]), ._11__B8(C_Bus[7]));  // open: _10__GND, _20__Vcc
  or or_1 (or_1_out, and_2_out, and_5_out);
  _74521 u_74521_1 (
    ._2__A0(alu_4_bit_1_s1[0]), ._3__B0(1'b0), ._4__A1(alu_4_bit_1_s1[1]), ._5__B1(1'b0),
    ._6__A2(alu_4_bit_1_s1[2]), ._7__B2(1'b0), ._8__A3(alu_4_bit_1_s1[3]), ._9__B3(1'b0),
    ._11__A4(alu_4_bit_2_s1[4]), ._12__B4(1'b0), ._13__A5(alu_4_bit_2_s1[5]), ._14__B5(1'b0),
    ._15__A6(alu_4_bit_2_s1[6]), ._16__B6(1'b0), ._17__A7(Negative), ._18__B7(1'b0), ._1__nI__A_B(1'b0),
    ._19__nO__A_B(n74521_1__19__no__a_b));  // open: _20__Vcc, _10__GND
  _74521 u_74521_2 (
    ._2__A0(alu_4_bit_3_s1[0]), ._3__B0(1'b0), ._4__A1(alu_4_bit_3_s1[1]), ._5__B1(1'b0),
    ._6__A2(alu_4_bit_3_s1[2]), ._7__B2(1'b0), ._8__A3(alu_4_bit_3_s1[3]), ._9__B3(1'b0),
    ._11__A4(alu_4_bit_2_s1[0]), ._12__B4(1'b0), ._13__A5(alu_4_bit_2_s1[1]), ._14__B5(1'b0),
    ._15__A6(alu_4_bit_2_s1[2]), ._16__B6(1'b0), ._17__A7(alu_4_bit_2_s1[3]), ._18__B7(1'b0),
    ._1__nI__A_B(1'b0), ._19__nO__A_B(n74521_2__19__no__a_b));  // open: _20__Vcc, _10__GND
  _74245 u_74245_6 (
    ._1__DIR(not_1_out), ._2__A1(alu_4_bit_2_s1[0]), ._3__A2(alu_4_bit_2_s1[1]), ._4__A3(alu_4_bit_2_s1[2]),
    ._5__A4(alu_4_bit_2_s1[3]), ._6__A5(alu_4_bit_2_s1[4]), ._7__A6(alu_4_bit_2_s1[5]),
    ._8__A7(alu_4_bit_2_s1[6]), ._9__A8(Negative), ._19__nG(1'b0), ._18___B1(C_Bus[8]), ._17__B2(C_Bus[9]),
    ._16__B3(C_Bus[10]), ._15__B4(C_Bus[11]), ._14__B5(C_Bus[12]), ._13__B6(C_Bus[13]), ._12__B7(C_Bus[14]),
    ._11__B8(C_Bus[15]));  // open: _10__GND, _20__Vcc
  and and_6 (and_6_out, or_1_out, F3);
  or or_2 (Carry, alu_4_bit_4_carry_out, and_6_out);
  nor nor_1 (Zero, n74521_1__19__no__a_b, n74521_2__19__no__a_b);
  nor nor_2 (Positive, Zero, Negative);
  ALU_Functions alu_functions_1 ();

  // Notes on the sheet:
  //   Genesis I ALU
  //   Shift Left
  //   F3 - Shift
  //   Shift Right
  //   Test Zero
  //   ALU || (shift)
endmodule

module ALU_4_Bit (
  input  F0,
  input  F1,
  input  F2,
  input  INC,
  input  ENA,
  input  A1,
  input  A2,
  input  A3,
  input  A4,
  input  ENB,
  input  B1,
  input  B2,
  input  B3,
  input  B4,
  output Carry_Out,
  output Overflow,
  output S1,
  output S2,
  output S3,
  output S4
);

  wire n7408_1__3__1y, n7408_1__6__2y, n7408_1__8__3y, n7408_1__11__4y, n7408_2__3__1y, n7408_2__6__2y,
       n7408_2__8__3y, n7408_2__11__4y;

  _7408 u_7408_1 (
    ._1__1A(A1), ._2__1B(ENA), ._3__1Y(n7408_1__3__1y), ._4__2A(A2), ._5__2B(ENA), ._6__2Y(n7408_1__6__2y),
    ._13__4B(ENA), ._12__4A(A4), ._11__4Y(n7408_1__11__4y), ._10__3B(ENA), ._9__3A(A3),
    ._8__3Y(n7408_1__8__3y));  // open: _7__GND, _14__Vcc
  _7408 u_7408_2 (
    ._1__1A(B1), ._2__1B(ENB), ._3__1Y(n7408_2__3__1y), ._4__2A(B2), ._5__2B(ENB), ._6__2Y(n7408_2__6__2y),
    ._13__4B(ENB), ._12__4A(B4), ._11__4Y(n7408_2__11__4y), ._10__3B(ENB), ._9__3A(B3),
    ._8__3Y(n7408_2__8__3y));  // open: _7__GND, _14__Vcc
  _74382 u_74382_1 (
    .Cin(INC), .A0(n7408_1__3__1y), .B0(n7408_2__3__1y), .A1(n7408_1__6__2y), .B1(n7408_2__6__2y),
    .A2(n7408_1__8__3y), .B2(n7408_2__8__3y), .A3(n7408_1__11__4y), .B3(n7408_2__11__4y), .F0(F0), .F1(F1),
    .F2(F2), .Cout(Carry_Out), .OVR(Overflow), .C2(S3), .C3(S4), .C0(S1), .C1(S2));  // open: Vcc, GND
  ALU_Functions alu_functions_1 ();
endmodule

module Test (
  input  [7:0] in_1,
  input  in_2,
  output [7:0] out_3
);

  wire not_1_out;

  _74245 u_74245_1 (
    ._1__DIR(1'b1), ._2__A1(1'b0), ._3__A2(in_1[0]), ._4__A3(in_1[1]), ._5__A4(in_1[2]), ._6__A5(in_1[3]),
    ._7__A6(in_1[4]), ._8__A7(in_1[5]), ._9__A8(in_1[6]), ._19__nG(not_1_out), ._18___B1(out_3[0]),
    ._17__B2(out_3[1]), ._16__B3(out_3[2]), ._15__B4(out_3[3]), ._14__B5(out_3[4]), ._13__B6(out_3[5]),
    ._12__B7(out_3[6]), ._11__B8(out_3[7]));  // open: _10__GND, _20__Vcc
  _74245 u_74245_2 (
    ._1__DIR(1'b1), ._2__A1(in_1[1]), ._3__A2(in_1[2]), ._4__A3(in_1[3]), ._5__A4(in_1[4]), ._6__A5(in_1[5]),
    ._7__A6(in_1[6]), ._8__A7(in_1[7]), ._9__A8(1'b0), ._19__nG(in_2), ._18___B1(out_3[0]),
    ._17__B2(out_3[1]), ._16__B3(out_3[2]), ._15__B4(out_3[3]), ._14__B5(out_3[4]), ._13__B6(out_3[5]),
    ._12__B7(out_3[6]), ._11__B8(out_3[7]));  // open: _10__GND, _20__Vcc
  not not_1 (not_1_out, in_2);
endmodule
