// Logisim project ALU4.circ as structural Verilog: 1 circuit, main circuit main
module main (
  input  X0,
  input  ZX,
  input  NX,
  input  Y0,
  input  ZY,
  input  NY,
  input  AA,
  input  INV,
  input  X1,
  input  Y1,
  input  X2,
  input  in_12,
  input  Y2,
  input  X3,
  input  Y3,
  output NG,
  output O0,
  output O1,
  output O2,
  output O3,
  output Carry,
  output ZR
);

  wire and_1_out, and_2_out, and_3_out, and_4_out, and_5_out, and_6_out, and_7_out, and_8_out, and_9_out,
       and_10_out, and_11_out, and_12_out, multiplexer_1_out, multiplexer_2_out, multiplexer_3_out,
       multiplexer_4_out, n74ls283_1__1__s2, n74ls283_1__4__s1, n74ls283_1__10__s4, n74ls283_1__13__s3,
       not_1_out, not_2_out, not_3_out, not_4_out, not_5_out, not_6_out, not_7_out, not_8_out, xor_1_out,
       xor_2_out, xor_3_out, xor_4_out, xor_5_out, xor_6_out, xor_7_out, xor_8_out;

  not not_1 (not_1_out, ZX);
  not not_2 (not_2_out, ZY);
  not not_3 (not_3_out, ZX);
  not not_4 (not_4_out, ZY);
  not not_5 (not_5_out, ZX);
  not not_6 (not_6_out, ZY);
  not not_7 (not_7_out, ZX);
  not not_8 (not_8_out, ZY);
  and and_1 (and_1_out, X0, not_1_out);
  and and_2 (and_2_out, Y0, not_2_out);
  and and_3 (and_3_out, X1, not_3_out);
  and and_4 (and_4_out, Y1, not_4_out);
  and and_5 (and_5_out, X2, not_5_out);
  and and_6 (and_6_out, Y2, not_6_out);
  and and_7 (and_7_out, X3, not_7_out);
  and and_8 (and_8_out, Y3, not_8_out);
  xor xor_1 (xor_1_out, and_1_out, NX);
  xor xor_2 (xor_2_out, and_2_out, NY);
  xor xor_3 (xor_3_out, and_3_out, NX);
  xor xor_4 (xor_4_out, and_4_out, NY);
  xor xor_5 (xor_5_out, and_5_out, NX);
  xor xor_6 (xor_6_out, and_6_out, NY);
  xor xor_7 (xor_7_out, and_7_out, NX);
  xor xor_8 (xor_8_out, and_8_out, NY);
  and and_9 (and_9_out, xor_1_out, xor_2_out);
  and and_10 (and_10_out, xor_3_out, xor_4_out);
  and and_11 (and_11_out, xor_5_out, xor_6_out);
  and and_12 (and_12_out, xor_7_out, xor_8_out);
  _74LS283 u_74ls283_1 (
    ._7__C0(in_12), ._5__A1(xor_1_out), ._6__B1(xor_2_out), ._3__A2(xor_3_out), ._2__B2(xor_4_out),
    ._14__A3(xor_5_out), ._15__B3(xor_6_out), ._12__A4(xor_7_out), ._11__B4(xor_8_out),
    ._4__S1(n74ls283_1__4__s1), ._1__S2(n74ls283_1__1__s2), ._13__S3(n74ls283_1__13__s3),
    ._10__S4(n74ls283_1__10__s4), ._9__C4(Carry));  // open: _8__GND, _16__Vcc
  Multiplexer multiplexer_1 (.in0(and_9_out), .in1(n74ls283_1__4__s1), .out(multiplexer_1_out), .sel(AA));  // open: en
  Multiplexer multiplexer_2 (.in0(and_10_out), .in1(n74ls283_1__1__s2), .out(multiplexer_2_out), .sel(AA));  // open: en
  Multiplexer multiplexer_3 (
    .in0(and_11_out), .in1(n74ls283_1__13__s3), .out(multiplexer_3_out), .sel(AA));  // open: en
  Multiplexer multiplexer_4 (
    .in0(and_12_out), .in1(n74ls283_1__10__s4), .out(multiplexer_4_out), .sel(AA));  // open: en
  xor xor_9 (NG, multiplexer_1_out, INV);
  xor xor_10 (O1, multiplexer_2_out, INV);
  xor xor_11 (O2, multiplexer_3_out, INV);
  xor xor_12 (O3, multiplexer_4_out, INV);
  nor nor_1 (ZR, NG, O1, O2, O3);

  assign O0 = NG;

  // Notes on the sheet:
  //   in_12: pull=up
endmodule
