// Logisim project ALU8.circ as structural Verilog: 1 circuit, main circuit main
module main (
  input  X,
  input  zx,
  input  nx,
  input  y,
  input  zy,
  input  ny,
  input  in_7,
  input  nout,
  input  [7:0] in_9,
  input  in_10,
  input  in_11,
  input  [7:0] in_12,
  input  in_13,
  input  in_14,
  input  in_15,
  input  in_16,
  output out_17,
  output [7:0] out_18
);

  wire and_3_out, and_4_out, and_5_out, multiplexer_1_out, not_1_out, not_2_out, or_1_out, xor_1_out,
       xor_2_out;
  wire [7:0] adder_1_out, and_1_out, and_2_out, and_6_out, bit_extender_1_out, bit_extender_2_out,
       bit_extender_3_out, bit_extender_4_out, bit_extender_5_out, multiplexer_2_out, xor_3_out, xor_4_out;

  assign bit_extender_1_out = {{7{in_10}}, in_10};  // Bit_Extender bit_extender_1
  assign bit_extender_2_out = {{7{in_11}}, in_11};  // Bit_Extender bit_extender_2
  assign bit_extender_3_out = {{7{in_13}}, in_13};  // Bit_Extender bit_extender_3
  assign bit_extender_4_out = {{7{in_14}}, in_14};  // Bit_Extender bit_extender_4
  assign bit_extender_5_out = {{7{in_16}}, in_16};  // Bit_Extender bit_extender_5
  not not_1 (not_1_out, zx);
  not not_2 (not_2_out, zy);
  assign and_1_out = in_9 & ~bit_extender_1_out;  // AND_Gate and_1, 8 bits wide
  assign and_2_out = in_12 & ~bit_extender_3_out;  // AND_Gate and_2, 8 bits wide
  and and_3 (and_3_out, X, not_1_out);
  and and_4 (and_4_out, y, not_2_out);
  // Probe on and_1_out
  // Probe on bit_extender_2_out
  // Probe on and_2_out
  // Probe on bit_extender_4_out
  xor xor_1 (xor_1_out, and_3_out, nx);
  xor xor_2 (xor_2_out, and_4_out, ny);
  assign xor_3_out = and_1_out ^ bit_extender_2_out;  // XOR_Gate xor_3, 8 bits wide
  assign xor_4_out = and_2_out ^ bit_extender_4_out;  // XOR_Gate xor_4, 8 bits wide
  // Probe on xor_1_out
  // Probe on xor_2_out
  // Probe on xor_3_out
  // Probe on xor_4_out
  or or_1 (or_1_out, xor_1_out, xor_2_out);
  and and_5 (and_5_out, xor_1_out, xor_2_out);
  assign and_6_out = xor_3_out & xor_4_out;  // AND_Gate and_6, 8 bits wide
  Adder adder_1 (.a(xor_3_out), .b(xor_4_out), .out(adder_1_out));  // open: cin, cout
  Multiplexer #(.enable("false")) multiplexer_1 (.in0(and_5_out), .in1(or_1_out), .out(multiplexer_1_out), .sel(in_7));
  // Probe on or_1_out
  // Probe on and_5_out
  // Probe on and_6_out
  // Probe on adder_1_out
  // Probe on multiplexer_1_out
  Multiplexer #(.width(8)) multiplexer_2 (
    .in0(and_6_out), .in1(adder_1_out), .out(multiplexer_2_out), .sel(in_15));  // open: en
  xor xor_5 (out_17, multiplexer_1_out, nout);
  // Probe on multiplexer_2_out
  assign out_18 = multiplexer_2_out ^ bit_extender_5_out;  // XOR_Gate xor_6, 8 bits wide
endmodule
