// Logisim project ALU_4Bit Rev II.circ as structural Verilog: 1 circuit, main circuit 4-Bit ALU
module _4_Bit_ALU (
  input  F0,
  input  F1,
  input  F2,
  input  INC,
  input  ENA,
  input  INVA,
  input  A1,
  input  A2,
  input  A3,
  input  A4,
  input  ENB,
  input  B1,
  input  B2,
  input  B3,
  input  B4,
  output S1,
  output S2,
  output S3,
  output S4,
  output Carry_Out
);

  wire n7404_1__2__1y, n7404_1__4__2y, n7404_1__6__3y, n7404_1__12__6y, n7408_1__3__1y, n7408_1__6__2y,
       n7408_1__8__3y, n7408_1__11__4y, n7408_2__3__1y, n7408_2__6__2y, n7408_2__8__3y, n7408_2__11__4y,
       n7408_3__3__1y, n7408_3__6__2y, n7408_3__8__3y, n7408_3__11__4y, n7432_1__3__1y, n7432_1__6__2y,
       n7432_1__8__3y, n7432_1__11__4y, n7486_1__3__1y, n7486_1__6__2y, n7486_1__8__3y, n7486_1__11__4y,
       n7486_2__3__1y, n7486_2__6__2y, n7486_2__8__3y, n7486_2__11__4y, n74253_1__7__1y, n74253_1__9__2y,
       n74253_2__7__1y, n74253_2__9__2y, n74283_1__1__s2, n74283_1__4__s1, n74283_1__10__s4, n74283_1__13__s3;

  _7408 u_7408_1 (
    ._1__1A(A1), ._2__1B(ENA), ._3__1Y(n7408_1__3__1y), ._4__2A(A2), ._5__2B(ENA), ._6__2Y(n7408_1__6__2y),
    ._13__4B(ENA), ._12__4A(A4), ._11__4Y(n7408_1__11__4y), ._10__3B(ENA), ._9__3A(A3),
    ._8__3Y(n7408_1__8__3y));  // open: _7__GND, _14__Vcc
  _7408 u_7408_2 (
    ._1__1A(B1), ._2__1B(ENB), ._3__1Y(n7408_2__3__1y), ._4__2A(B2), ._5__2B(ENB), ._6__2Y(n7408_2__6__2y),
    ._13__4B(ENB), ._12__4A(B4), ._11__4Y(n7408_2__11__4y), ._10__3B(ENB), ._9__3A(B3),
    ._8__3Y(n7408_2__8__3y));  // open: _7__GND, _14__Vcc
  _7486 u_7486_1 (
    ._1__1A(n7408_1__3__1y), ._2__1B(INVA), ._3__1Y(n7486_1__3__1y), ._4__2A(n7408_1__6__2y), ._5__2B(INVA),
    ._6__2Y(n7486_1__6__2y), ._13__4B(INVA), ._12__4A(n7408_1__11__4y), ._11__4Y(n7486_1__11__4y),
    ._10__3B(INVA), ._9__3A(n7408_1__8__3y), ._8__3Y(n7486_1__8__3y));  // open: _7__GND, _14__Vcc
  _7404 u_7404_1 (
    ._1__1A(n7408_2__3__1y), ._2__1Y(n7404_1__2__1y), ._3__2A(n7408_2__6__2y), ._4__2Y(n7404_1__4__2y),
    ._5__3A(n7408_2__8__3y), ._6__3Y(n7404_1__6__3y), ._13__6A(n7408_2__11__4y), ._12__6Y(n7404_1__12__6y));  // open: _7__GND, _14__Vcc, _11__5A, _10__5Y, _9__4A, _8__4Y
  _7486 u_7486_2 (
    ._1__1A(n7486_1__3__1y), ._2__1B(n7408_2__3__1y), ._3__1Y(n7486_2__3__1y), ._4__2A(n7486_1__6__2y),
    ._5__2B(n7408_2__6__2y), ._6__2Y(n7486_2__6__2y), ._13__4B(n7408_2__11__4y), ._12__4A(n7486_1__11__4y),
    ._11__4Y(n7486_2__11__4y), ._10__3B(n7408_2__8__3y), ._9__3A(n7486_1__8__3y), ._8__3Y(n7486_2__8__3y));  // open: _7__GND, _14__Vcc
  _7408 u_7408_3 (
    ._1__1A(n7486_1__3__1y), ._2__1B(n7408_2__3__1y), ._3__1Y(n7408_3__3__1y), ._4__2A(n7486_1__6__2y),
    ._5__2B(n7408_2__6__2y), ._6__2Y(n7408_3__6__2y), ._13__4B(n7408_2__11__4y), ._12__4A(n7486_1__11__4y),
    ._11__4Y(n7408_3__11__4y), ._10__3B(n7408_2__8__3y), ._9__3A(n7486_1__8__3y), ._8__3Y(n7408_3__8__3y));  // open: _7__GND, _14__Vcc
  _7432 u_7432_1 (
    ._1__1A(n7486_1__3__1y), ._2__1B(n7408_2__3__1y), ._3__1Y(n7432_1__3__1y), ._4__2A(n7486_1__6__2y),
    ._5__2B(n7408_2__6__2y), ._6__2Y(n7432_1__6__2y), ._13__4B(n7408_2__11__4y), ._12__4A(n7486_1__11__4y),
    ._11__4Y(n7432_1__11__4y), ._10__3B(n7408_2__8__3y), ._9__3A(n7486_1__8__3y), ._8__3Y(n7432_1__8__3y));  // open: _7__GND, _14__Vcc
  _74283 u_74283_1 (
    ._7__C0(INC), ._5__A1(n7486_1__3__1y), ._6__B1(n7408_2__3__1y), ._3__A2(n7486_1__6__2y),
    ._2__B2(n7408_2__6__2y), ._14__A3(n7486_1__8__3y), ._15__B3(n7408_2__8__3y), ._12__A4(n7486_1__11__4y),
    ._11__B4(n7408_2__11__4y), ._4__S1(n74283_1__4__s1), ._1__S2(n74283_1__1__s2),
    ._13__S3(n74283_1__13__s3), ._10__S4(n74283_1__10__s4), ._9__C4(Carry_Out));  // open: _8__GND, _16__Vcc
  _74253 u_74253_1 (
    ._1__1G(1'b0), ._2__Sb(F1), ._3__1C3(n74283_1__4__s1), ._4__1C2(n7432_1__3__1y),
    ._5__1C1(n7404_1__2__1y), ._6__1C0(n7408_3__3__1y), ._7__1Y(n74253_1__7__1y), ._15__2G(1'b0),
    ._14__Sa(F0), ._13__2C3(n74283_1__1__s2), ._12__2C2(n7432_1__6__2y), ._11__2C1(n7404_1__4__2y),
    ._10__2C0(n7408_3__6__2y), ._9__2Y(n74253_1__9__2y));  // open: _8__GND, _16__Vcc
  _74253 u_74253_2 (
    ._1__1G(1'b0), ._2__Sb(F1), ._3__1C3(n74283_1__13__s3), ._4__1C2(n7432_1__8__3y),
    ._5__1C1(n7404_1__6__3y), ._6__1C0(n7408_3__11__4y), ._7__1Y(n74253_2__7__1y), ._15__2G(1'b0),
    ._14__Sa(F0), ._13__2C3(n74283_1__10__s4), ._12__2C2(n7432_1__11__4y), ._11__2C1(n7404_1__12__6y),
    ._10__2C0(n7408_3__8__3y), ._9__2Y(n74253_2__9__2y));  // open: _8__GND, _16__Vcc
  _74157 u_74157_1 (
    ._1__S(F2), ._2__A1(n74253_1__7__1y), ._3__B1(n7486_2__3__1y), ._4__Y1(S1), ._5__A2(n74253_1__9__2y),
    ._6__B2(n7486_2__6__2y), ._7__Y2(S2), ._15__G(1'b0), ._14__A4(n74253_2__9__2y),
    ._13__B4(n7486_2__11__4y), ._12__Y4(S4), ._11__A3(n74253_2__7__1y), ._10__B3(n7486_2__8__3y), ._9__Y3(S3));  // open: _8__GND, _16__Vcc

  // Notes on the sheet:
  //   F0 | F1 | F2 | ENA | ENB | INVA | INC || FUNC
  //   ---------------------------------------------
  //    0 |  1 |  0 |  1  |  0  |  0   |  0  || A
  //    0 |  1 |  0 |  0  |  1  |  0   |  0  || B
  //    0 |  1 |  0 |  1  |  0  |  1   |  0  || !A
  //    1 |  0 |  0 |  1  |  1  |  0   |  0  || !B
  //    1 |  1 |  0 |  1  |  1  |  0   |  0  || A + B
  //    1 |  1 |  0 |  1  |  1  |  0   |  1  || A + B + 1
  //    1 |  1 |  0 |  1  |  0  |  0   |  1  || A + 1
  //    1 |  1 |  0 |  0  |  1  |  0   |  1  || B + 1
  //    1 |  1 |  0 |  1  |  1  |  1   |  1  || B - A
  //    1 |  1 |  0 |  0  |  1  |  1   |  0  || B - 1
  //    1 |  1 |  0 |  1  |  0  |  1   |  1  || -A
  //    0 |  0 |  0 |  1  |  1  |  0   |  0  || A AND B
  //    0 |  1 |  0 |  1  |  1  |  0   |  0  || A OR B
  //    0 |  1 |  0 |  0  |  0  |  0   |  0  || 0
  //    1 |  1 |  0 |  0  |  0  |  0   |  1  || 1
  //    1 |  1 |  0 |  0  |  0  |  1   |  0  || -1
  //    0 |  0 |  1 |  1  |  1  |  0   |  0  || XOR
  //    0 |  1 |  1 |  1  |  0  |  0   |  0  || A SR 1
  //    1 |  0 |  1 |  1  |  0  |  0   |  0  || A SL 1
  //   1 - 7404 - 6-Way Hex Inverter
  //   3 - 7408 - Quad AND
  //   1 - 7432 - Quad OR
  //   1 - 7486 - Quad XOR
  //   2 - 74253 - Dual 4-1 Selector
  //   1 - 74283 - 4 bit adder
endmodule
