// Logisim project ALU_4Bit_discrete.circ as structural Verilog: 1 circuit, main circuit main
module main (
  input  A1,
  input  B1,
  input  Carry_In,
  input  A2,
  input  B2,
  input  A3,
  input  B3,
  input  A4,
  input  B4,
  input  ENA,
  input  ENB,
  input  INVA,
  input  F0,
  input  F1,
  output S1,
  output S2,
  output S3,
  output S4,
  output Carry
);

  wire and_1_out, and_2_out, and_3_out, and_4_out, and_5_out, and_6_out, and_7_out, and_8_out, and_9_out,
       and_10_out, and_11_out, and_12_out, and_13_out, and_14_out, and_15_out, and_16_out, and_17_out,
       and_18_out, and_19_out, and_20_out, and_21_out, and_22_out, and_23_out, and_24_out, and_25_out,
       and_26_out, and_27_out, and_28_out, and_29_out, and_30_out, and_31_out, and_32_out, and_33_out,
       and_34_out, and_35_out, and_36_out, and_37_out, and_38_out, and_39_out, and_40_out, not_1_out,
       not_2_out, not_3_out, not_4_out, or_1_out, or_2_out, or_3_out, or_4_out, or_5_out, or_6_out, or_7_out,
       xor_1_out, xor_2_out, xor_3_out, xor_4_out, xor_5_out, xor_6_out, xor_7_out, xor_8_out, xor_9_out,
       xor_10_out, xor_11_out, xor_12_out;

  and and_1 (and_1_out, A1, ENA);
  and and_2 (and_2_out, B1, ENB);
  and and_3 (and_3_out, A2, ENA);
  and and_4 (and_4_out, B2, ENB);
  and and_5 (and_5_out, A3, ENA);
  and and_6 (and_6_out, B3, ENB);
  and and_7 (and_7_out, A4, ENA);
  and and_8 (and_8_out, B4, ENB);
  xor xor_1 (xor_1_out, and_1_out, INVA);
  xor xor_2 (xor_2_out, and_3_out, INVA);
  xor xor_3 (xor_3_out, and_5_out, INVA);
  xor xor_4 (xor_4_out, and_7_out, INVA);
  and and_9 (and_9_out, ~F0, ~F1);  // AND_Gate
  and and_10 (and_10_out, ~F0, F1);  // AND_Gate
  and and_11 (and_11_out, F0, ~F1);  // AND_Gate
  and and_12 (and_12_out, F0, F1);
  and and_13 (and_13_out, xor_1_out, and_2_out);
  or or_1 (or_1_out, xor_1_out, and_2_out);
  not not_1 (not_1_out, and_2_out);
  and and_14 (and_14_out, xor_2_out, and_4_out);
  or or_2 (or_2_out, xor_2_out, and_4_out);
  not not_2 (not_2_out, and_4_out);
  and and_15 (and_15_out, xor_3_out, and_6_out);
  or or_3 (or_3_out, xor_3_out, and_6_out);
  not not_3 (not_3_out, and_6_out);
  and and_16 (and_16_out, xor_4_out, and_8_out);
  or or_4 (or_4_out, xor_4_out, and_8_out);
  not not_4 (not_4_out, and_8_out);
  and and_17 (and_17_out, and_13_out, and_9_out);
  and and_18 (and_18_out, or_1_out, and_10_out);
  and and_19 (and_19_out, not_1_out, and_11_out);
  and and_20 (and_20_out, and_12_out, xor_1_out, and_2_out);
  and and_21 (and_21_out, and_14_out, and_9_out);
  and and_22 (and_22_out, or_2_out, and_10_out);
  and and_23 (and_23_out, not_2_out, and_11_out);
  and and_24 (and_24_out, and_12_out, xor_2_out, and_4_out);
  and and_25 (and_25_out, and_15_out, and_9_out);
  and and_26 (and_26_out, or_3_out, and_10_out);
  and and_27 (and_27_out, not_3_out, and_11_out);
  and and_28 (and_28_out, and_12_out, xor_3_out, and_6_out);
  and and_29 (and_29_out, and_16_out, and_9_out);
  and and_30 (and_30_out, or_4_out, and_10_out);
  and and_31 (and_31_out, not_4_out, and_11_out);
  and and_32 (and_32_out, and_12_out, xor_4_out, and_8_out);
  xor xor_5 (xor_5_out, and_2_out, xor_1_out);
  and and_33 (and_33_out, and_12_out, xor_5_out, Carry_In);
  or or_5 (or_5_out, and_20_out, and_33_out);
  xor xor_6 (xor_6_out, and_4_out, xor_2_out);
  and and_34 (and_34_out, and_12_out, xor_6_out, or_5_out);
  or or_6 (or_6_out, and_24_out, and_34_out);
  xor xor_7 (xor_7_out, and_6_out, xor_3_out);
  and and_35 (and_35_out, and_12_out, xor_7_out, or_6_out);
  or or_7 (or_7_out, and_28_out, and_35_out);
  xor xor_8 (xor_8_out, and_8_out, xor_4_out);
  and and_36 (and_36_out, and_12_out, xor_8_out, or_7_out);
  or or_8 (Carry, and_32_out, and_36_out);
  xor xor_9 (xor_9_out, Carry_In, xor_5_out);
  xor xor_10 (xor_10_out, or_5_out, xor_6_out);
  xor xor_11 (xor_11_out, or_6_out, xor_7_out);
  xor xor_12 (xor_12_out, or_7_out, xor_8_out);
  and and_37 (and_37_out, xor_9_out, and_12_out);
  and and_38 (and_38_out, xor_10_out, and_12_out);
  and and_39 (and_39_out, xor_11_out, and_12_out);
  and and_40 (and_40_out, xor_12_out, and_12_out);
  or or_9 (S1, and_17_out, and_18_out, and_19_out, and_37_out);
  or or_10 (S2, and_21_out, and_22_out, and_23_out, and_38_out);
  or or_11 (S3, and_25_out, and_26_out, and_27_out, and_39_out);
  or or_12 (S4, and_29_out, and_30_out, and_31_out, and_40_out);
endmodule
