// Logisim project ScratchPad.circ as structural Verilog: 1 circuit, main circuit main
module main (
  input  [7:0] in_1,
  input  w_0____R_1
);

  wire clock_1_out, not_1_out;
  wire [7:0] MAR_q, MBR_q, n74245_4__18___b1, ram_1_data;

  Register MAR (.D(in_1), .Q(MAR_q), .clk(clock_1_out));  // open: en, clr
  // _74245 74245_1: pin names not known
  // _74245 74245_2: pin names not known
  RAM ram_1 (.addr(MAR_q), .data(ram_1_data), .clk(clock_1_out), .ld(w_0____R_1));  // open: sel, clr
  Clock clock_1 (.out(clock_1_out));
  _74245 u_74245_3 (
    ._1__DIR(1'b1), ._2__A1(MBR_q[7]), ._3__A2(MBR_q[6]), ._4__A3(MBR_q[5]), ._5__A4(MBR_q[4]),
    ._6__A5(MBR_q[3]), ._7__A6(MBR_q[2]), ._8__A7(MBR_q[1]), ._9__A8(MBR_q[0]), ._19__nG(w_0____R_1),
    ._18___B1(ram_1_data[7]), ._17__B2(ram_1_data[6]), ._16__B3(ram_1_data[5]), ._15__B4(ram_1_data[4]),
    ._14__B5(ram_1_data[3]), ._13__B6(ram_1_data[2]), ._12__B7(ram_1_data[1]), ._11__B8(ram_1_data[0]));  // open: _10__GND, _20__Vcc
  not not_1 (not_1_out, w_0____R_1);
  _74245 u_74245_4 (
    ._1__DIR(1'b1), ._2__A1(ram_1_data[0]), ._3__A2(ram_1_data[1]), ._4__A3(ram_1_data[2]),
    ._5__A4(ram_1_data[3]), ._6__A5(ram_1_data[4]), ._7__A6(ram_1_data[5]), ._8__A7(ram_1_data[6]),
    ._9__A8(ram_1_data[7]), ._19__nG(not_1_out), ._18___B1(n74245_4__18___b1[0]),
    ._17__B2(n74245_4__18___b1[1]), ._16__B3(n74245_4__18___b1[2]), ._15__B4(n74245_4__18___b1[3]),
    ._14__B5(n74245_4__18___b1[4]), ._13__B6(n74245_4__18___b1[5]), ._12__B7(n74245_4__18___b1[6]),
    ._11__B8(n74245_4__18___b1[7]));  // open: _10__GND, _20__Vcc
  Register MBR (.D(n74245_4__18___b1), .Q(MBR_q), .clk(clock_1_out));  // open: en, clr
endmodule
